// Logisim project 16 bit computer.circ as structural Verilog
module CPU (
  output [7:0] out_1,
  output [7:0] out_2,
  output [7:0] out_3,
  output [7:0] out_4,
  output [7:0] out_5,
  output [7:0] out_6,
  output [7:0] out_7,
  output [7:0] out_8,
  output [7:0] out_9,
  output [7:0] out_10
);

  wire clock_1_out, jmp_a_out, mov_ah_value8_out, mov_al_value8_out, mov_ax_value16_out, mov_bh_value8_out,
       mov_bl_value8_out, mov_bx_value16_out, mov_ch_value8_out, mov_cl_value8_out, mov_cx_value16_out,
       mov_dh_value8_out, mov_dl_value8_out, mov_dx_value16_out, mov_sp_value16_out, mov_sph_value8_out,
       mov_spl_value8_out;
  wire [7:0] ram_1_data;
  wire [15:0] ip_register_small_1_ip;

  ip_Register_small ip_register_small_1 (
    .mov_ip_value16(jmp_a_out), .Data_In({out_1, out_2}), .CLK(clock_1_out), .ip(ip_register_small_1_ip));
  Clock clock_1 (.out(clock_1_out));
  RAM #(.addrWidth(16)) ram_1 (
    .addr(ip_register_small_1_ip), .data(ram_1_data), .clk(clock_1_out));  // open: sel, ld, clr
  and mov_ax_value16 (mov_ax_value16_out, ram_1_data[0], ~ram_1_data[1], ~ram_1_data[2], ~ram_1_data[3], ~ram_1_data[4], ~ram_1_data[5], ~ram_1_data[6], ~ram_1_data[7]);  // AND_Gate
  and mov_bx_value16 (mov_bx_value16_out, ~ram_1_data[0], ram_1_data[1], ~ram_1_data[2], ~ram_1_data[3], ~ram_1_data[4], ~ram_1_data[5], ~ram_1_data[6], ~ram_1_data[7]);  // AND_Gate
  and mov_cx_value16 (mov_cx_value16_out, ram_1_data[0], ram_1_data[1], ~ram_1_data[2], ~ram_1_data[3], ~ram_1_data[4], ~ram_1_data[5], ~ram_1_data[6], ~ram_1_data[7]);  // AND_Gate
  and mov_dx_value16 (mov_dx_value16_out, ~ram_1_data[0], ~ram_1_data[1], ram_1_data[2], ~ram_1_data[3], ~ram_1_data[4], ~ram_1_data[5], ~ram_1_data[6], ~ram_1_data[7]);  // AND_Gate
  and mov_sp_value16 (mov_sp_value16_out, ram_1_data[0], ~ram_1_data[1], ram_1_data[2], ~ram_1_data[3], ~ram_1_data[4], ~ram_1_data[5], ~ram_1_data[6], ~ram_1_data[7]);  // AND_Gate
  and mov_al_value8 (mov_al_value8_out, ~ram_1_data[0], ram_1_data[1], ram_1_data[2], ~ram_1_data[3], ~ram_1_data[4], ~ram_1_data[5], ~ram_1_data[6], ~ram_1_data[7]);  // AND_Gate
  and mov_ah_value8 (mov_ah_value8_out, ram_1_data[0], ram_1_data[1], ram_1_data[2], ~ram_1_data[3], ~ram_1_data[4], ~ram_1_data[5], ~ram_1_data[6], ~ram_1_data[7]);  // AND_Gate
  and mov_bl_value8 (mov_bl_value8_out, ~ram_1_data[0], ~ram_1_data[1], ~ram_1_data[2], ram_1_data[3], ~ram_1_data[4], ~ram_1_data[5], ~ram_1_data[6], ~ram_1_data[7]);  // AND_Gate
  and mov_bh_value8 (mov_bh_value8_out, ram_1_data[0], ~ram_1_data[1], ~ram_1_data[2], ram_1_data[3], ~ram_1_data[4], ~ram_1_data[5], ~ram_1_data[6], ~ram_1_data[7]);  // AND_Gate
  and mov_cl_value8 (mov_cl_value8_out, ~ram_1_data[0], ram_1_data[1], ~ram_1_data[2], ram_1_data[3], ~ram_1_data[4], ~ram_1_data[5], ~ram_1_data[6], ~ram_1_data[7]);  // AND_Gate
  and mov_ch_value8 (mov_ch_value8_out, ram_1_data[0], ram_1_data[1], ~ram_1_data[2], ram_1_data[3], ~ram_1_data[4], ~ram_1_data[5], ~ram_1_data[6], ~ram_1_data[7]);  // AND_Gate
  and mov_dl_value8 (mov_dl_value8_out, ~ram_1_data[0], ~ram_1_data[1], ram_1_data[2], ram_1_data[3], ~ram_1_data[4], ~ram_1_data[5], ~ram_1_data[6], ~ram_1_data[7]);  // AND_Gate
  and mov_dh_value8 (mov_dh_value8_out, ram_1_data[0], ~ram_1_data[1], ram_1_data[2], ram_1_data[3], ~ram_1_data[4], ~ram_1_data[5], ~ram_1_data[6], ~ram_1_data[7]);  // AND_Gate
  and mov_spl_value8 (mov_spl_value8_out, ~ram_1_data[0], ram_1_data[1], ram_1_data[2], ram_1_data[3], ~ram_1_data[4], ~ram_1_data[5], ~ram_1_data[6], ~ram_1_data[7]);  // AND_Gate
  and mov_sph_value8 (mov_sph_value8_out, ram_1_data[0], ram_1_data[1], ram_1_data[2], ram_1_data[3], ~ram_1_data[4], ~ram_1_data[5], ~ram_1_data[6], ~ram_1_data[7]);  // AND_Gate
  and jmp_a (jmp_a_out, ~ram_1_data[0], ~ram_1_data[1], ~ram_1_data[2], ~ram_1_data[3], ram_1_data[4], ~ram_1_data[5], ~ram_1_data[6], ~ram_1_data[7]);  // AND_Gate
  _16_Bit_Register ax (
    .mov_ax_value16(mov_ax_value16_out), .mov_ah_value8(mov_ah_value8_out),
    .mov_al_value8(mov_al_value8_out), .Data(ram_1_data), .CLK(clock_1_out), .ah(out_1), .al(out_2));
  _16_Bit_Register bx (
    .mov_ax_value16(mov_bx_value16_out), .mov_ah_value8(mov_bh_value8_out),
    .mov_al_value8(mov_bl_value8_out), .Data(ram_1_data), .CLK(clock_1_out), .ah(out_3), .al(out_4));
  _16_Bit_Register cx (
    .mov_ax_value16(mov_cx_value16_out), .mov_ah_value8(mov_ch_value8_out),
    .mov_al_value8(mov_cl_value8_out), .Data(ram_1_data), .CLK(clock_1_out), .ah(out_5), .al(out_6));
  _16_Bit_Register dx (
    .mov_ax_value16(mov_dx_value16_out), .mov_ah_value8(mov_dh_value8_out),
    .mov_al_value8(mov_dl_value8_out), .Data(ram_1_data), .CLK(clock_1_out), .ah(out_7), .al(out_8));
  _16_Bit_Register sp (
    .mov_ax_value16(mov_sp_value16_out), .mov_ah_value8(mov_sph_value8_out),
    .mov_al_value8(mov_spl_value8_out), .Data(ram_1_data), .CLK(clock_1_out), .ah(out_9), .al(out_10));
endmodule

module Register_small (
  input  mov_ah_value8,
  input  mov_al_value8,
  input  [7:0] Data_In,
  input  CLK,
  output [7:0] ah,
  output [7:0] al
);

  wire [7:0] transistor_1_out, transistor_2_out;

  Transistor #(.\type ("n"), .width(8)) transistor_1 (.in(Data_In), .out(transistor_1_out), .gate(mov_ah_value8));
  Transistor #(.\type ("n"), .width(8)) transistor_2 (.in(Data_In), .out(transistor_2_out), .gate(mov_al_value8));
  Register_part u_ah (.D(transistor_1_out), .en(mov_ah_value8), .Q(ah), .clk(CLK));  // open: clr
  Register_part u_al (.D(transistor_2_out), .en(mov_al_value8), .Q(al), .clk(CLK));  // open: clr
endmodule

module _2_cycle (
  input  Active,
  input  CLK,
  output Trigger
);

  wire and_1_out, d_ff_1_qn, or_1_out, t_ff_1_q;

  D_Flip_Flop d_ff_1 (
    .clk(CLK), .D(and_1_out), .Q(Trigger), .Qn(d_ff_1_qn), .en(or_1_out), .reset(t_ff_1_q));  // open: preset
  and and_1 (and_1_out, ~Trigger, Active);  // AND_Gate
  or or_1 (or_1_out, and_1_out, t_ff_1_q);
  T_Flip_Flop t_ff_1 (.clk(CLK), .T(Trigger), .Q(t_ff_1_q), .reset(d_ff_1_qn), .en(CLK));  // open: Qn, preset
endmodule

module _3_cycle (
  input  Active,
  input  CLK,
  output _1,
  output _2,
  output _3
);

  wire and_1_out, and_2_out, and_3_out, or_1_out;

  and and_1 (and_1_out, ~or_1_out, Active);  // AND_Gate
  D_Flip_Flop d_ff_1 (.clk(CLK), .D(and_2_out), .Q(_1));  // open: Qn, preset, en, reset
  and and_2 (and_2_out, ~_1, and_1_out);  // AND_Gate
  T_Flip_Flop t_ff_1 (.clk(CLK), .T(_1), .Q(_2), .reset(and_3_out), .en(CLK));  // open: Qn, preset
  and and_3 (and_3_out, _2, _3);
  or or_1 (or_1_out, _1, _2);
  D_Flip_Flop d_ff_2 (.clk(CLK), .D(_2), .Q(_3));  // open: Qn, preset, en, reset
endmodule

module _16_Bit_Register (
  input  mov_ax_value16,
  input  mov_ah_value8,
  input  mov_al_value8,
  input  [7:0] Data,
  input  CLK,
  output [7:0] ah,
  output [7:0] al
);

  wire n2_cycle_1_trigger, n2_cycle_2_trigger, n3_cycle_1__1, or_1_out, or_2_out, or_3_out;
  wire [7:0] transistor_1_out;

  or or_1 (or_1_out, mov_ax_value16, mov_ah_value8);
  or or_2 (or_2_out, n3_cycle_1__1, mov_al_value8);
  _3_cycle u_3_cycle_1 (.Active(mov_ax_value16), .CLK(CLK), ._1(n3_cycle_1__1));  // open: _2, _3
  _2_cycle u_2_cycle_1 (.Active(or_1_out), .CLK(CLK), .Trigger(n2_cycle_1_trigger));
  _2_cycle u_2_cycle_2 (.Active(or_2_out), .CLK(CLK), .Trigger(n2_cycle_2_trigger));
  or or_3 (or_3_out, n2_cycle_1_trigger, n2_cycle_2_trigger);
  Transistor #(.\type ("n"), .width(8)) transistor_1 (.in(Data), .out(transistor_1_out), .gate(or_3_out));
  Register_small ax (
    .mov_ah_value8(n2_cycle_1_trigger), .mov_al_value8(n2_cycle_2_trigger), .Data_In(transistor_1_out),
    .CLK(CLK), .ah(ah), .al(al));
endmodule

module ip_Register (
  input  mov_ip_value16,
  input  mov_iph_value8,
  input  mov_ipl_value8,
  input  [7:0] Data,
  input  CLK,
  output out_6,
  output [7:0] ah,
  output [7:0] al
);

  wire n2_cycle_1_trigger, n2_cycle_2_trigger, n3_cycle_1__1, or_1_out, or_2_out, or_3_out;
  wire [7:0] transistor_1_out;

  or or_1 (or_1_out, mov_ip_value16, mov_iph_value8);
  or or_2 (or_2_out, n3_cycle_1__1, mov_ipl_value8);
  _3_cycle u_3_cycle_1 (.Active(mov_ip_value16), .CLK(CLK), ._1(n3_cycle_1__1));  // open: _2, _3
  _2_cycle u_2_cycle_1 (.Active(or_1_out), .CLK(CLK), .Trigger(n2_cycle_1_trigger));
  _2_cycle u_2_cycle_2 (.Active(or_2_out), .CLK(CLK), .Trigger(n2_cycle_2_trigger));
  or or_3 (or_3_out, n2_cycle_1_trigger, n2_cycle_2_trigger);
  Transistor #(.\type ("n"), .width(8)) transistor_1 (.in(Data), .out(transistor_1_out), .gate(or_3_out));
  or or_4 (out_6, n2_cycle_2_trigger, n2_cycle_1_trigger);
  Register_small ax (
    .mov_ah_value8(n2_cycle_1_trigger), .mov_al_value8(n2_cycle_2_trigger), .Data_In(transistor_1_out),
    .CLK(CLK), .ah(ah), .al(al));
endmodule

module ip_Register_small (
  input  mov_ip_value16,
  input  [15:0] Data_In,
  input  CLK,
  output [15:0] ip
);

  wire not_1_out;

  not not_1 (not_1_out, mov_ip_value16);
  Counter #(.width(16), .max('hffff), .trigger("falling")) counter_1 (
    .load(mov_ip_value16), .D(Data_In), .count(not_1_out), .Q(ip), .clk(CLK));  // open: carry, clr
endmodule

module Register_Block (
);

  Register_small ax ();  // open: mov_ah_value8, mov_al_value8, Data_In, CLK, ah, al
  Register_small bx ();  // open: mov_ah_value8, mov_al_value8, Data_In, CLK, ah, al
  Register_small cx ();  // open: mov_ah_value8, mov_al_value8, Data_In, CLK, ah, al
  Register_small dx ();  // open: mov_ah_value8, mov_al_value8, Data_In, CLK, ah, al
  Register_small sp ();  // open: mov_ah_value8, mov_al_value8, Data_In, CLK, ah, al
endmodule

module Register (
  input  mov_reg_value16,
  input  mov_highbyte_value8,
  input  mov_lowbyte_value8,
  input  [7:0] value8_in,
  input  [15:0] value16_in,
  input  CLK,
  output [15:0] value16,
  output [7:0] High_Byte,
  output [7:0] Low_Byte
);

  wire or_1_out, or_2_out;
  wire [7:0] or_3_out, or_4_out, transistor_2_out;
  wire [15:0] transistor_1_out;

  Transistor #(.\type ("n"), .width(16)) transistor_1 (.in(value16_in), .out(transistor_1_out), .gate(mov_reg_value16));
  Transistor #(.width(8)) transistor_2 (.in(value8_in), .out(transistor_2_out), .gate(mov_reg_value16));
  or or_1 (or_1_out, mov_reg_value16, mov_lowbyte_value8);
  or or_2 (or_2_out, mov_reg_value16, mov_highbyte_value8);
  assign or_3_out = transistor_2_out | transistor_1_out[7:0];  // OR_Gate or_3, 8 bits wide
  assign or_4_out = transistor_2_out | transistor_1_out[15:8];  // OR_Gate or_4, 8 bits wide
  Register_part u_low_byte (.D(or_3_out), .en(or_1_out), .Q(Low_Byte), .clk(CLK));  // open: clr
  Register_part u_high_byte (.D(or_4_out), .en(or_2_out), .Q(High_Byte), .clk(CLK));  // open: clr

  assign value16 = {High_Byte, Low_Byte};
endmodule

module RegisterPlusAnd (
  input  CLK,
  input  d0,
  input  in_3,
  input  in_4,
  input  in_5,
  input  in_6,
  input  in_7,
  input  in_8,
  input  d7,
  output [7:0] out_10,
  output [7:0] out_11,
  output [7:0] out_12,
  output [7:0] out_13,
  output [7:0] out_14,
  output [7:0] out_15,
  output [7:0] out_16,
  output [7:0] out_17,
  output [7:0] out_18,
  output [7:0] out_19
);

  _16_Bit_Register ax (
    .Data({d7, in_8, in_7, in_6, in_5, in_4, in_3, d0}), .CLK(CLK), .ah(out_10), .al(out_11));  // open: mov_ax_value16, mov_ah_value8, mov_al_value8
  _16_Bit_Register bx (
    .Data({d7, in_8, in_7, in_6, in_5, in_4, in_3, d0}), .CLK(CLK), .ah(out_12), .al(out_13));  // open: mov_ax_value16, mov_ah_value8, mov_al_value8
  _16_Bit_Register cx (
    .Data({d7, in_8, in_7, in_6, in_5, in_4, in_3, d0}), .CLK(CLK), .ah(out_14), .al(out_15));  // open: mov_ax_value16, mov_ah_value8, mov_al_value8
  _16_Bit_Register dx (
    .Data({d7, in_8, in_7, in_6, in_5, in_4, in_3, d0}), .CLK(CLK), .ah(out_16), .al(out_17));  // open: mov_ax_value16, mov_ah_value8, mov_al_value8
  _16_Bit_Register sp (
    .Data({d7, in_8, in_7, in_6, in_5, in_4, in_3, d0}), .CLK(CLK), .ah(out_18), .al(out_19));  // open: mov_ax_value16, mov_ah_value8, mov_al_value8
endmodule

module _16_bit_Reg (
  input  CLK,
  input  mov_reg_value16,
  input  mov_regh_value8,
  input  mov_regl_value8,
  input  [7:0] Data,
  output reg_write,
  output [7:0] regh,
  output [7:0] regl
);

  wire d_ff_1_q, d_ff_2_q, d_ff_3_q, d_ff_4_q, or_1_out, or_3_out;

  D_Flip_Flop d_ff_1 (.clk(CLK), .D(mov_regh_value8), .Q(d_ff_1_q));  // open: Qn, preset, en, reset
  D_Flip_Flop d_ff_2 (.clk(CLK), .D(mov_regl_value8), .Q(d_ff_2_q));  // open: Qn, preset, en, reset
  D_Flip_Flop d_ff_3 (.clk(CLK), .D(mov_reg_value16), .Q(d_ff_3_q));  // open: Qn, preset, en, reset
  or or_1 (or_1_out, d_ff_3_q, d_ff_2_q);
  D_Flip_Flop d_ff_4 (.clk(CLK), .D(d_ff_3_q), .Q(d_ff_4_q));  // open: Qn, preset, en, reset
  or or_2 (reg_write, or_1_out, or_3_out);
  or or_3 (or_3_out, d_ff_4_q, d_ff_1_q);
  Register_part u_regh (.D(Data), .en(or_3_out), .Q(regh), .clk(CLK));  // open: clr
  Register_part u_regl (.D(Data), .en(or_1_out), .Q(regl), .clk(CLK));  // open: clr
endmodule

module CPU_2 (
  input  write,
  input  [7:0] in_2,
  input  in_3,
  input  in_4,
  input  [15:0] in_5,
  input  in_6,
  input  enable,
  input  in_8,
  input  in_9,
  input  [7:0] in_10,
  input  [7:0] in_11,
  output [7:0] out_12,
  output [7:0] out_13,
  output [7:0] out_14,
  output [7:0] out_15,
  output [7:0] out_16,
  output [7:0] out_17,
  output [7:0] out_18,
  output [7:0] out_19,
  output [7:0] out_20,
  output [7:0] out_21,
  output [7:0] out_22
);

  wire clock_1_out, counter_2_carry, counter_3_carry, counter_4_carry, d_ff_1_q, decoder_1_mov_ax_value16,
       decoder_1_mov_bx_value16, or_2_out, undriven, undriven_2, undriven_3, undriven_4, undriven_5,
       undriven_6;
  wire [7:0] counter_2_q, counter_3_q, counter_4_q, decoder_1_data_out, or_1_out;
  wire [15:0] counter_1_q;

  Clock clock_1 (.out(clock_1_out));
  Counter #(.width(16), .max('hffff)) counter_1 (
    .load(in_3), .D(in_5), .count(in_6), .Q(counter_1_q), .clk(clock_1_out));  // open: carry, clr
  assign or_1_out = in_11 | in_11;  // OR_Gate or_1, 8 bits wide
  RAM #(.addrWidth(16), .bus("separate")) ram_1 (
    .addr(counter_1_q), .din(or_1_out), .data(in_2), .str(in_8), .sel(enable), .clk(clock_1_out), .ld(in_9));  // open: clr
  Decoder decoder_1 (
    .CLK(clock_1_out), .data_in(in_10), .data_out(decoder_1_data_out),
    .mov_ax_value16(decoder_1_mov_ax_value16), .mov_bx_value16(decoder_1_mov_bx_value16));  // open: mov_cx_value16, mov_dx_value16, mov_dx_value16_2
  Counter counter_2 (
    .load(undriven), .D(in_2), .count(undriven_2), .Q(counter_2_q), .carry(counter_2_carry), .clk(write));  // open: clr
  Counter counter_3 (
    .load(undriven_3), .D(in_2), .count(undriven_4), .Q(counter_3_q), .carry(counter_3_carry), .clk(write));  // open: clr
  Counter counter_4 (
    .load(undriven_5), .D(in_2), .count(undriven_6), .Q(counter_4_q), .carry(counter_4_carry), .clk(write));  // open: clr
  or or_2 (or_2_out, in_4, in_4);
  _16_bit_Reg ax (
    .CLK(clock_1_out), .mov_reg_value16(decoder_1_mov_ax_value16), .Data(decoder_1_data_out), .regh(out_13),
    .regl(out_14));  // open: mov_regh_value8, mov_regl_value8, reg_write
  _16_bit_Reg bx (
    .CLK(clock_1_out), .mov_reg_value16(decoder_1_mov_bx_value16), .Data(decoder_1_data_out), .regh(out_15),
    .regl(out_16));  // open: mov_regh_value8, mov_regl_value8, reg_write
  _16_bit_Reg cx (
    .regh(out_17), .regl(out_18));  // open: CLK, mov_reg_value16, mov_regh_value8, mov_regl_value8, Data, reg_write
  _16_bit_Reg dx (
    .regh(out_19), .regl(out_20));  // open: CLK, mov_reg_value16, mov_regh_value8, mov_regl_value8, Data, reg_write
  _16_bit_Reg sp (
    .regh(out_21), .regl(out_22));  // open: CLK, mov_reg_value16, mov_regh_value8, mov_regl_value8, Data, reg_write
  D_Flip_Flop d_ff_1 (.clk(clock_1_out), .D(or_2_out), .Q(d_ff_1_q));  // open: Qn, preset, en, reset
  RAM #(.addrWidth(24), .bus("separate")) ram_2 (
    .addr({counter_4_q, counter_3_q, counter_2_q}), .sel(d_ff_1_q), .clk(clock_1_out));  // open: din, data, str, ld, clr

  assign out_12 = in_2;

  // Notes on the sheet:
  //   Program execute/program read write memory
  //   24 bit memory for graphics
endmodule

module RAM_Interface (
  input  CLK,
  input  load,
  input  store,
  input  [7:0] data_in,
  output [7:0] data_out
);

  Counter #(.width(16), .max('hffff)) counter_1 ();  // open: load, D, count, Q, carry, clk, clr
  RAM #(.addrWidth(16), .bus("separate")) ram_1 (.clk(CLK));  // open: addr, din, data, str, sel, ld, clr
endmodule

module Decoder (
  input  CLK,
  input  [7:0] data_in,
  output [7:0] data_out,
  output mov_ax_value16,
  output mov_bx_value16,
  output mov_cx_value16,
  output mov_dx_value16,
  output mov_dx_value16_2
);

  wire and_1_out, exec_q, mov_ax_value16_out, mov_bx_value16_out, mov_cx_value16_out, mov_dx_value16_out,
       mov_sp_value16_out, n3_cycle_1__1, n3_cycle_1__2, n3_cycle_1__3, or_1_out, or_2_out;

  and u_mov_ax_value16 (mov_ax_value16_out, data_in[0], ~data_in[1], ~data_in[2], ~data_in[3], ~data_in[4], ~data_in[5], ~data_in[6], ~data_in[7]);  // AND_Gate
  and u_mov_bx_value16 (mov_bx_value16_out, ~data_in[0], data_in[1], ~data_in[2], ~data_in[3], ~data_in[4], ~data_in[5], ~data_in[6], ~data_in[7]);  // AND_Gate
  and u_mov_cx_value16 (mov_cx_value16_out, data_in[0], data_in[1], ~data_in[2], ~data_in[3], ~data_in[4], ~data_in[5], ~data_in[6], ~data_in[7]);  // AND_Gate
  and u_mov_dx_value16 (mov_dx_value16_out, ~data_in[0], ~data_in[1], data_in[2], ~data_in[3], ~data_in[4], ~data_in[5], ~data_in[6], ~data_in[7]);  // AND_Gate
  and mov_sp_value16 (mov_sp_value16_out, data_in[0], ~data_in[1], data_in[2], ~data_in[3], ~data_in[4], ~data_in[5], ~data_in[6], ~data_in[7]);  // AND_Gate
  D_Flip_Flop #(.trigger("high")) exec (.clk(CLK), .D(or_2_out), .Q(exec_q));  // open: Qn, preset, en, reset
  and and_1 (and_1_out, or_1_out, ~n3_cycle_1__1, ~n3_cycle_1__2, ~1'b0);  // AND_Gate
  or or_1 (or_1_out, mov_ax_value16_out, mov_bx_value16_out, mov_cx_value16_out, mov_dx_value16_out, mov_sp_value16_out);
  _3_cycle u_3_cycle_1 (.Active(and_1_out), .CLK(CLK), ._1(n3_cycle_1__1), ._2(n3_cycle_1__2), ._3(n3_cycle_1__3));
  or or_2 (or_2_out, n3_cycle_1__1, n3_cycle_1__2);
  and and_2 (mov_ax_value16, ~exec_q, mov_ax_value16_out);  // AND_Gate
  and and_3 (mov_bx_value16, ~exec_q, mov_bx_value16_out);  // AND_Gate
  and and_4 (mov_cx_value16, ~exec_q, mov_cx_value16_out);  // AND_Gate
  and and_5 (mov_dx_value16, ~exec_q, mov_dx_value16_out);  // AND_Gate
  and and_6 (mov_dx_value16_2, ~exec_q, mov_sp_value16_out);  // AND_Gate

  assign data_out = data_in;
endmodule

module CPU_BUS (
);

  wire bus_command_unit_v3_1_ax_enable_instruction, bus_command_unit_v3_1_bx_enable_instruction,
       bus_command_unit_v3_1_comparison_enable, bus_command_unit_v3_1_comparison_instruction,
       bus_command_unit_v3_1_cx_enable_instruction, bus_command_unit_v3_1_dx_enable_instruction,
       bus_command_unit_v3_1_math_unit_enable, bus_command_unit_v3_1_ram0_instruction_enable, CLK_out;
  wire [1:0] bus_comparator_1_comparison_line;
  wire [2:0] bus_command_unit_v3_1_ax_instruction, bus_command_unit_v3_1_bx_instruction,
       bus_command_unit_v3_1_cx_instruction, bus_command_unit_v3_1_dx_instruction;
  wire [3:0] bus_command_unit_v3_1_math_unit_instruction;
  wire [7:0] bus_command_unit_v3_1_ram0_instruction;
  wire [15:0] ax_dataout;

  BUS_Register ax (
    .DataOut(ax_dataout), .DataIn(ax_dataout),
    .Instruction_Enable(bus_command_unit_v3_1_ax_enable_instruction), .CLK(CLK_out),
    .Instruction_Line(bus_command_unit_v3_1_ax_instruction));
  BUS_Register bx (
    .DataOut(ax_dataout), .DataIn(ax_dataout),
    .Instruction_Enable(bus_command_unit_v3_1_bx_enable_instruction), .CLK(CLK_out),
    .Instruction_Line(bus_command_unit_v3_1_bx_instruction));
  BUS_Register cx (
    .DataOut(ax_dataout), .DataIn(ax_dataout),
    .Instruction_Enable(bus_command_unit_v3_1_cx_enable_instruction), .CLK(CLK_out),
    .Instruction_Line(bus_command_unit_v3_1_cx_instruction));
  BUS_Register dx (
    .DataOut(ax_dataout), .DataIn(ax_dataout),
    .Instruction_Enable(bus_command_unit_v3_1_dx_enable_instruction), .CLK(CLK_out),
    .Instruction_Line(bus_command_unit_v3_1_dx_instruction));
  Clock CLK (.out(CLK_out));
  BUS_Command_Unit_V3 bus_command_unit_v3_1 (
    .CLK(CLK_out), .ax_enable_instruction(bus_command_unit_v3_1_ax_enable_instruction),
    .ax_instruction(bus_command_unit_v3_1_ax_instruction),
    .bx_enable_instruction(bus_command_unit_v3_1_bx_enable_instruction),
    .bx_instruction(bus_command_unit_v3_1_bx_instruction),
    .cx_enable_instruction(bus_command_unit_v3_1_cx_enable_instruction),
    .cx_instruction(bus_command_unit_v3_1_cx_instruction),
    .dx_enable_instruction(bus_command_unit_v3_1_dx_enable_instruction),
    .dx_instruction(bus_command_unit_v3_1_dx_instruction), .Data_In(ax_dataout),
    .RAM0_Instruction_Enable(bus_command_unit_v3_1_ram0_instruction_enable),
    .RAM0_Instruction(bus_command_unit_v3_1_ram0_instruction),
    .Math_Unit_Enable(bus_command_unit_v3_1_math_unit_enable),
    .Math_Unit_Instruction(bus_command_unit_v3_1_math_unit_instruction),
    .Comparison_Line(bus_comparator_1_comparison_line),
    .Comparison_Enable(bus_command_unit_v3_1_comparison_enable),
    .Comparison_Instruction(bus_command_unit_v3_1_comparison_instruction));
  BUS_RAM bus_ram_1 (
    .Bus_Out(ax_dataout), .Bus_In(ax_dataout), .CLK(CLK_out),
    .RAM_Instruction(bus_command_unit_v3_1_ram0_instruction),
    .RAM_Instruction_Enable(bus_command_unit_v3_1_ram0_instruction_enable));
  BUS_Math_Unit bus_math_unit_1 (
    .BUS_IN(ax_dataout), .BUS_OUT(ax_dataout), .Instruction(bus_command_unit_v3_1_math_unit_instruction),
    .Enable(bus_command_unit_v3_1_math_unit_enable), .CLK(CLK_out));
  BUS_Comparator bus_comparator_1 (
    .Data_In(ax_dataout), .CLK(CLK_out), .Enable(bus_command_unit_v3_1_comparison_enable),
    .Instruction(bus_command_unit_v3_1_comparison_instruction),
    .Comparison_Line(bus_comparator_1_comparison_line));
endmodule

module BUS_Register (
  input  [15:0] DataIn,
  input  Instruction_Enable,
  input  CLK,
  input  [2:0] Instruction_Line,
  output [15:0] DataOut
);

  wire and_1_out, and_2_out, and_3_out, and_4_out, and_5_out, and_6_out, and_7_out, and_8_out, and_9_out,
       counter_1_carry, decoder_1_out0, decoder_1_out1, decoder_1_out2, decoder_1_out3, decoder_1_out4,
       decoder_1_out5, decoder_1_out6, not_1_out, not_2_out, or_1_out, or_2_out, or_3_out, or_4_out;
  wire [7:0] counter_1_q, counter_2_q, multiplexer_1_out;
  wire [15:0] controlled_buffer_1_out;

  Decoder_part #(.select(3), .enable("false")) decoder_1 (
    .out0(decoder_1_out0), .out1(decoder_1_out1), .out2(decoder_1_out2), .out3(decoder_1_out3),
    .out4(decoder_1_out4), .out5(decoder_1_out5), .out6(decoder_1_out6), .sel(Instruction_Line));  // open: out7
  and and_1 (and_1_out, decoder_1_out0, Instruction_Enable);
  and and_2 (and_2_out, decoder_1_out1, Instruction_Enable);
  and and_3 (and_3_out, decoder_1_out2, Instruction_Enable);
  and and_4 (and_4_out, decoder_1_out3, Instruction_Enable);
  and and_5 (and_5_out, decoder_1_out4, Instruction_Enable);
  and and_6 (and_6_out, decoder_1_out5, Instruction_Enable);
  and and_7 (and_7_out, decoder_1_out6, Instruction_Enable);
  assign controlled_buffer_1_out = not_1_out ? DataIn : 16'bz;  // Controlled_Buffer controlled_buffer_1
  not not_1 (not_1_out, and_7_out);
  or or_1 (or_1_out, and_4_out, and_1_out, and_3_out);
  or or_2 (or_2_out, and_8_out, and_1_out, and_2_out);
  not not_2 (not_2_out, and_2_out);
  or or_3 (or_3_out, and_4_out, and_5_out);
  Multiplexer #(.width(8)) multiplexer_1 (
    .in0(controlled_buffer_1_out[7:0]), .in1(controlled_buffer_1_out[15:8]), .out(multiplexer_1_out),
    .sel(not_2_out), .en(1'b1));
  Counter counter_1 (
    .load(or_1_out), .D(controlled_buffer_1_out[7:0]), .count(or_3_out), .Q(counter_1_q),
    .carry(counter_1_carry), .clk(CLK), .clr(and_6_out));
  Counter counter_2 (
    .load(or_2_out), .D(multiplexer_1_out), .count(or_4_out), .Q(counter_2_q), .clk(CLK), .clr(and_6_out));  // open: carry
  and and_8 (and_8_out, counter_1_carry, and_4_out);
  and and_9 (and_9_out, counter_1_carry, ~or_2_out, ~and_7_out, Instruction_Enable);  // AND_Gate
  or or_4 (or_4_out, and_9_out, and_8_out);
  assign DataOut = and_7_out ? {counter_2_q, counter_1_q} : 16'bz;  // Controlled_Buffer controlled_buffer_2

  // Notes on the sheet:
  //   mov reg,value16
  //   mov regH,value8
  //   mov regL,value8
  //   dec reg
  //   inc reg
  //   set 0
  //   Read/Write
endmodule

module BUS_Command_Unit (
  input  CLK,
  input  [15:0] Data_In,
  output ax_enable_instruction,
  output [2:0] ax_instruction,
  output bx_enable_instruction,
  output [2:0] bx_instruction,
  output [15:0] Control_Line_Out,
  output cx_enable_instruction,
  output [2:0] cx_instruction,
  output RAM0_Instruction_Enable,
  output [7:0] RAM0_Instruction,
  output dx_enable_instruction,
  output [2:0] dx_instruction
);

  wire and_16_out, and_17_out, and_18_out, and_19_out, and_20_out, and_21_out, and_22_out, and_23_out,
       and_24_out, and_29_out, and_30_out, and_31_out, and_32_out, and_33_out, and_34_out, and_35_out,
       and_36_out, and_37_out, and_38_out, and_39_out, and_41_out, and_46_out, and_47_out, and_48_out,
       and_49_out, and_50_out, and_51_out, and_52_out, and_53_out, and_54_out, and_55_out, and_56_out,
       and_57_out, and_58_out, and_59_out, and_60_out, and_61_out, and_62_out, and_63_out, and_64_out,
       and_65_out, and_66_out, and_68_out, ax_enable_2_out, ax_enable_out, bx_enable_2_out, bx_enable_out,
       cx_enable_out, d_ff_1_qn, d_ff_2_qn, d_ff_3_qn, d_ff_4_qn, d_ff_5_qn, d_ff_6_qn, d_ff_7_qn, d_ff_8_qn,
       d_ff_9_qn, d_ff_10_qn, d_ff_11_qn, d_ff_12_qn, d_ff_13_qn, d_ff_14_qn, d_ff_15_qn, d_ff_16_qn,
       d_ff_17_qn, d_ff_18_qn, d_ff_19_qn, d_ff_20_qn, d_ff_21_q, d_ff_21_qn, d_ff_22_q, d_ff_22_qn,
       d_ff_23_q, d_ff_23_qn, d_ff_24_q, d_ff_24_qn, d_ff_25_q, d_ff_25_qn, d_ff_26_q, d_ff_26_qn, d_ff_27_q,
       d_ff_27_qn, d_ff_28_qn, d_ff_29_qn, d_ff_30_qn, d_ff_31_qn, d_ff_32_q, d_ff_32_qn, d_ff_33_q,
       d_ff_33_qn, d_ff_34_q, d_ff_34_qn, d_ff_35_qn, d_ff_36_qn, d_ff_37_qn, d_ff_38_qn, d_ff_39_qn,
       d_ff_40_qn, d_ff_41_q, d_ff_41_qn, d_ff_42_q, d_ff_42_qn, d_ff_43_q, d_ff_43_qn, d_ff_44_q,
       d_ff_44_qn, d_ff_45_q, d_ff_45_qn, d_ff_46_qn, d_ff_47_qn, d_ff_48_q, d_ff_48_qn, dx_enable_out,
       mov___ax_dx_out, mov_ax__ax_out, mov_ax__bx_out, mov_ax__cx_out, mov_ax__dx_out, mov_ax_bx_out,
       mov_ax_cx_out, mov_ax_value16_out, mov_bx_ax_out, mov_bx_cx_out, mov_bx_dx_out, mov_bx_value16_out,
       mov_cx_ax_out, mov_cx_bx_out, mov_cx_dx_out, mov_cx_value16_out, mov_dx_ax_out, mov_dx_bx_out,
       mov_dx_cx_out, mov_dx_value16_out, or_10_out, or_11_out, or_12_out, or_13_out, or_14_out, or_15_out,
       or_16_out, or_18_out, or_19_out, or_20_out, or_21_out, or_22_out, or_23_out, or_24_out, or_26_out,
       or_27_out, or_28_out, or_34_out, or_35_out, or_36_out;
  wire [2:0] and_8_out, and_9_out, and_10_out, ax_instruction_2_out, ax_instruction_out,
       bx_instruction_2_out, bx_instruction_out, cx_instruction_out, dx_instruction_out;
  wire [2:2] and_1_out, and_2_out, and_3_out, and_4_out, and_5_out, and_6_out, and_7_out, and_11_out,
       and_12_out, and_13_out, and_14_out, and_15_out, and_40_out, d_ff_1_q, d_ff_2_q, d_ff_3_q, d_ff_4_q,
       d_ff_5_q, d_ff_6_q, d_ff_7_q, d_ff_8_q, d_ff_9_q, d_ff_17_q, d_ff_28_q, d_ff_29_q, d_ff_35_q;
  wire [4:4] and_67_out;
  wire [5:4] and_25_out, and_27_out, and_42_out, and_44_out;
  wire [5:5] d_ff_10_q, d_ff_11_q, d_ff_18_q, d_ff_19_q, d_ff_20_q, d_ff_30_q, d_ff_31_q, d_ff_37_q,
       d_ff_39_q, d_ff_40_q, d_ff_46_q, d_ff_47_q, or_17_out;
  wire [6:6] or_9_out;
  wire [7:0] and_69_out, or_25_out, or_29_out, or_30_out, or_31_out;
  wire [7:7] d_ff_12_q, d_ff_13_q, d_ff_14_q, d_ff_15_q;
  wire [15:0] and_70_out;

  assign dx_instruction_out = {{2{d_ff_6_q[2]}}, 1'b0} | {3{and_1_out[2]}} | {3{and_4_out[2]}} | {3{and_3_out[2]}};  // OR_Gate dx_instruction, 3 bits wide
  or dx_enable (dx_enable_out, d_ff_6_q[2], d_ff_2_q[2], d_ff_1_q[2], d_ff_9_q[2]);
  or or_1 (ax_enable_instruction, and_52_out, d_ff_35_q[2], and_9_out[2], and_10_out[2], ax_enable_2_out);
  assign ax_instruction = {3{and_40_out[2]}} | {3{and_15_out[2]}} | {3{and_9_out[0]}} | {3{and_10_out[0]}} | ax_instruction_2_out;  // OR_Gate or_2, 3 bits wide
  or or_3 (bx_enable_instruction, and_17_out, d_ff_35_q[2], d_ff_28_q[2], d_ff_29_q[2], bx_enable_2_out);
  assign bx_instruction = {3{and_12_out[2]}} | {{2{d_ff_35_q[2]}}, and_15_out[2]} | {3{and_11_out[2]}} | {3{and_7_out[2]}} | bx_instruction_2_out;  // OR_Gate or_4, 3 bits wide
  or or_5 (cx_enable_instruction, and_18_out, and_9_out[2], d_ff_29_q[2], d_ff_17_q[2], cx_enable_out);
  assign cx_instruction = {3{and_13_out[2]}} | {{2{and_9_out[2]}}, and_9_out[0]} | {{2{d_ff_29_q[2]}}, and_7_out[2]} | {3{and_5_out[2]}} | cx_instruction_out;  // OR_Gate or_6, 3 bits wide
  or or_7 (dx_enable_instruction, and_19_out, and_10_out[2], and_8_out[2], d_ff_8_q[2], dx_enable_out);
  assign dx_instruction = {3{and_14_out[2]}} | {{2{and_10_out[2]}}, and_10_out[0]} | {{2{and_8_out[2]}}, and_8_out[0]} | {{2{d_ff_8_q[2]}}, and_2_out[2]} | dx_instruction_out;  // OR_Gate or_8, 3 bits wide
  assign cx_instruction_out = {{2{d_ff_5_q[2]}}, 1'b0} | {{2{d_ff_2_q[2]}}, and_1_out[2]} | {3{and_2_out[2]}} | {3{and_6_out[2]}};  // OR_Gate cx_instruction, 3 bits wide
  // OR_Gate bx_instruction has open pins: out=bx_instruction_out
  or cx_enable (cx_enable_out, d_ff_5_q[2], d_ff_2_q[2], d_ff_8_q[2], d_ff_7_q[2]);
  // OR_Gate bx_enable has open pins: out=bx_enable_out
  assign bx_instruction_2_out = {{2{d_ff_4_q[2]}}, 1'b0} | {{2{d_ff_1_q[2]}}, and_4_out[2]} | {{2{d_ff_7_q[2]}}, and_6_out[2]} | {3{and_8_out[0]}};  // OR_Gate bx_instruction_2, 3 bits wide
  assign ax_instruction_out = 3'b000;  // OR_Gate ax_instruction, 3 bits wide OR_Gate
  or bx_enable_2 (bx_enable_2_out, d_ff_4_q[2], d_ff_1_q[2], d_ff_7_q[2], and_8_out[2]);
  or ax_enable (ax_enable_out, d_ff_15_q[7], d_ff_14_q[7], d_ff_13_q[7], d_ff_12_q[7]);
  assign ax_instruction_2_out = ax_instruction_out | {{2{d_ff_3_q[2]}}, 1'b0} | {{2{d_ff_9_q[2]}}, and_3_out[2]} | {{2{d_ff_17_q[2]}}, and_5_out[2]} | {{2{d_ff_28_q[2]}}, and_11_out[2]};  // OR_Gate ax_instruction_2, 3 bits wide
  and and_1 (and_1_out[2], d_ff_2_q[2], mov_dx_cx_out);
  or ax_enable_2 (ax_enable_2_out, ax_enable_out, d_ff_3_q[2], d_ff_9_q[2], d_ff_17_q[2], d_ff_28_q[2]);
  and and_2 (and_2_out[2], d_ff_8_q[2], mov_cx_dx_out);
  and and_3 (and_3_out[2], d_ff_9_q[2], mov_dx_ax_out);
  and and_4 (and_4_out[2], d_ff_1_q[2], mov_dx_bx_out);
  and and_5 (and_5_out[2], d_ff_17_q[2], mov_cx_ax_out);
  and and_6 (and_6_out[2], d_ff_7_q[2], mov_cx_bx_out);
  and and_7 (and_7_out[2], d_ff_29_q[2], mov_bx_cx_out);
  and and_8 (and_8_out[0], and_8_out[2], mov_bx_dx_out);
  and and_9 (and_9_out[0], and_9_out[2], mov_ax_cx_out);
  and and_10 (and_10_out[0], and_10_out[2], mov___ax_dx_out);
  and and_11 (and_11_out[2], d_ff_28_q[2], mov_bx_ax_out);
  D_Flip_Flop d_ff_1 (.clk(CLK), .D(mov_dx_bx_out), .Q(d_ff_1_q[2]), .Qn(d_ff_1_qn));  // open: preset, en, reset
  D_Flip_Flop d_ff_2 (.clk(CLK), .D(mov_dx_cx_out), .Q(d_ff_2_q[2]), .Qn(d_ff_2_qn));  // open: preset, en, reset
  or or_9 (or_9_out[6], d_ff_6_q[2], d_ff_5_q[2], d_ff_4_q[2], d_ff_3_q[2]);
  D_Flip_Flop d_ff_3 (.clk(CLK), .D(mov_ax__ax_out), .Q(d_ff_3_q[2]), .Qn(d_ff_3_qn));  // open: preset, en, reset
  D_Flip_Flop d_ff_4 (.clk(CLK), .D(mov_ax__bx_out), .Q(d_ff_4_q[2]), .Qn(d_ff_4_qn));  // open: preset, en, reset
  D_Flip_Flop d_ff_5 (.clk(CLK), .D(mov_ax__cx_out), .Q(d_ff_5_q[2]), .Qn(d_ff_5_qn));  // open: preset, en, reset
  D_Flip_Flop d_ff_6 (.clk(CLK), .D(mov_ax__dx_out), .Q(d_ff_6_q[2]), .Qn(d_ff_6_qn));  // open: preset, en, reset
  and and_12 (and_12_out[2], ~and_17_out, or_19_out);  // AND_Gate
  and and_13 (and_13_out[2], ~and_18_out, or_20_out);  // AND_Gate
  and and_14 (and_14_out[2], ~and_19_out, or_21_out);  // AND_Gate
  and and_15 (and_15_out[2], d_ff_35_q[2], mov_ax_bx_out);
  D_Flip_Flop d_ff_7 (.clk(CLK), .D(mov_cx_bx_out), .Q(d_ff_7_q[2]), .Qn(d_ff_7_qn));  // open: preset, en, reset
  D_Flip_Flop d_ff_8 (.clk(CLK), .D(mov_cx_dx_out), .Q(d_ff_8_q[2]), .Qn(d_ff_8_qn));  // open: preset, en, reset
  D_Flip_Flop d_ff_9 (.clk(CLK), .D(mov_dx_ax_out), .Q(d_ff_9_q[2]), .Qn(d_ff_9_qn));  // open: preset, en, reset
  D_Flip_Flop d_ff_10 (.clk(CLK), .D(d_ff_1_q[2]), .Q(d_ff_10_q[5]), .Qn(d_ff_10_qn));  // open: preset, en, reset
  D_Flip_Flop d_ff_11 (.clk(CLK), .D(d_ff_2_q[2]), .Q(d_ff_11_q[5]), .Qn(d_ff_11_qn));  // open: preset, en, reset
  and and_16 (and_16_out, d_ff_11_qn, d_ff_2_qn);
  D_Flip_Flop d_ff_12 (.clk(CLK), .D(d_ff_3_q[2]), .Q(d_ff_12_q[7]), .Qn(d_ff_12_qn));  // open: preset, en, reset
  D_Flip_Flop d_ff_13 (.clk(CLK), .D(d_ff_4_q[2]), .Q(d_ff_13_q[7]), .Qn(d_ff_13_qn));  // open: preset, en, reset
  D_Flip_Flop d_ff_14 (.clk(CLK), .D(d_ff_5_q[2]), .Q(d_ff_14_q[7]), .Qn(d_ff_14_qn));  // open: preset, en, reset
  D_Flip_Flop d_ff_15 (.clk(CLK), .D(d_ff_6_q[2]), .Q(d_ff_15_q[7]), .Qn(d_ff_15_qn));  // open: preset, en, reset
  and and_17 (and_17_out, or_19_out, d_ff_32_q);
  or or_10 (or_10_out, d_ff_44_q, d_ff_26_q);
  and and_18 (and_18_out, or_20_out, d_ff_33_q);
  or or_11 (or_11_out, d_ff_45_q, d_ff_27_q);
  and and_19 (and_19_out, or_21_out, d_ff_34_q);
  D_Flip_Flop d_ff_16 (.clk(CLK), .D(mov_bx_dx_out), .Q(and_8_out[2]), .Qn(d_ff_16_qn));  // open: preset, en, reset
  D_Flip_Flop d_ff_17 (.clk(CLK), .D(mov_cx_ax_out), .Q(d_ff_17_q[2]), .Qn(d_ff_17_qn));  // open: preset, en, reset
  D_Flip_Flop d_ff_18 (.clk(CLK), .D(d_ff_7_q[2]), .Q(d_ff_18_q[5]), .Qn(d_ff_18_qn));  // open: preset, en, reset
  D_Flip_Flop d_ff_19 (.clk(CLK), .D(d_ff_8_q[2]), .Q(d_ff_19_q[5]), .Qn(d_ff_19_qn));  // open: preset, en, reset
  and and_20 (and_20_out, d_ff_19_qn, d_ff_8_qn);
  D_Flip_Flop d_ff_20 (.clk(CLK), .D(d_ff_9_q[2]), .Q(d_ff_20_q[5]), .Qn(d_ff_20_qn));  // open: preset, en, reset
  and and_21 (and_21_out, d_ff_20_qn, d_ff_9_qn);
  and and_22 (and_22_out, and_23_out, and_24_out);
  and and_23 (and_23_out, d_ff_10_qn, d_ff_1_qn);
  and and_24 (and_24_out, and_16_out, and_50_out);
  D_Flip_Flop d_ff_21 (.clk(CLK), .D(d_ff_12_q[7]), .Q(d_ff_21_q), .Qn(d_ff_21_qn));  // open: preset, en, reset
  D_Flip_Flop d_ff_22 (.clk(CLK), .D(d_ff_13_q[7]), .Q(d_ff_22_q), .Qn(d_ff_22_qn));  // open: preset, en, reset
  D_Flip_Flop d_ff_23 (.clk(CLK), .D(d_ff_14_q[7]), .Q(d_ff_23_q), .Qn(d_ff_23_qn));  // open: preset, en, reset
  D_Flip_Flop d_ff_24 (.clk(CLK), .D(d_ff_15_q[7]), .Q(d_ff_24_q), .Qn(d_ff_24_qn));  // open: preset, en, reset
  or or_12 (or_12_out, d_ff_48_q, d_ff_41_q, d_ff_42_q);
  or or_13 (or_13_out, d_ff_43_q, d_ff_25_q);
  or or_14 (or_14_out, d_ff_25_q, d_ff_32_q);
  D_Flip_Flop d_ff_25 (.clk(CLK), .D(mov_bx_value16_out), .Q(d_ff_25_q), .Qn(d_ff_25_qn));  // open: preset, en, reset
  and and_25 (and_25_out[4], or_15_out, or_20_out);
  and and_26 (and_25_out[5], or_10_out, or_20_out);
  or or_15 (or_15_out, d_ff_26_q, d_ff_33_q);
  D_Flip_Flop d_ff_26 (.clk(CLK), .D(mov_cx_value16_out), .Q(d_ff_26_q), .Qn(d_ff_26_qn));  // open: preset, en, reset
  and and_27 (and_27_out[4], or_16_out, or_21_out);
  and and_28 (and_27_out[5], or_11_out, or_21_out);
  or or_16 (or_16_out, d_ff_27_q, d_ff_34_q);
  D_Flip_Flop d_ff_27 (.clk(CLK), .D(mov_dx_value16_out), .Q(d_ff_27_q), .Qn(d_ff_27_qn));  // open: preset, en, reset
  D_Flip_Flop d_ff_28 (.clk(CLK), .D(mov_bx_ax_out), .Q(d_ff_28_q[2]), .Qn(d_ff_28_qn));  // open: preset, en, reset
  D_Flip_Flop d_ff_29 (.clk(CLK), .D(mov_bx_cx_out), .Q(d_ff_29_q[2]), .Qn(d_ff_29_qn));  // open: preset, en, reset
  D_Flip_Flop d_ff_30 (.clk(CLK), .D(and_8_out[2]), .Q(d_ff_30_q[5]), .Qn(d_ff_30_qn));  // open: preset, en, reset
  D_Flip_Flop d_ff_31 (.clk(CLK), .D(d_ff_17_q[2]), .Q(d_ff_31_q[5]), .Qn(d_ff_31_qn));  // open: preset, en, reset
  and and_29 (and_29_out, d_ff_31_qn, d_ff_17_qn);
  and and_30 (and_30_out, and_31_out, and_32_out);
  and and_31 (and_31_out, d_ff_18_qn, d_ff_7_qn);
  and and_32 (and_32_out, and_20_out, and_33_out);
  and and_33 (and_33_out, and_21_out, and_22_out);
  or or_17 (or_17_out[5], d_ff_21_q, d_ff_22_q, d_ff_23_q, d_ff_24_q);
  and and_34 (and_34_out, and_35_out, and_36_out);
  and and_35 (and_35_out, d_ff_22_qn, d_ff_13_qn, d_ff_4_qn);
  and and_36 (and_36_out, and_37_out, and_38_out);
  and and_37 (and_37_out, d_ff_23_qn, d_ff_14_qn, d_ff_5_qn);
  buf and_38 (and_38_out, and_39_out);  // AND_Gate
  and and_39 (and_39_out, d_ff_24_qn, d_ff_15_qn, d_ff_6_qn);
  and and_40 (and_40_out[2], d_ff_41_q, ~and_52_out);  // AND_Gate
  and and_41 (and_41_out, ~d_ff_41_q, d_ff_42_q);  // AND_Gate
  and and_42 (and_42_out[4], or_22_out, or_12_out);
  or or_18 (or_18_out, d_ff_48_q, and_41_out);
  and and_43 (and_42_out[5], or_18_out, or_12_out);
  and and_44 (and_44_out[4], or_14_out, or_19_out);
  and and_45 (and_44_out[5], or_13_out, or_19_out);
  or or_19 (or_19_out, d_ff_25_q, d_ff_32_q, d_ff_43_q);
  D_Flip_Flop d_ff_32 (.clk(CLK), .D(d_ff_25_q), .Q(d_ff_32_q), .Qn(d_ff_32_qn));  // open: preset, en, reset
  or or_20 (or_20_out, d_ff_26_q, d_ff_33_q, d_ff_44_q);
  D_Flip_Flop d_ff_33 (.clk(CLK), .D(d_ff_26_q), .Q(d_ff_33_q), .Qn(d_ff_33_qn));  // open: preset, en, reset
  or or_21 (or_21_out, d_ff_27_q, d_ff_34_q, d_ff_45_q);
  D_Flip_Flop d_ff_34 (.clk(CLK), .D(d_ff_27_q), .Q(d_ff_34_q), .Qn(d_ff_34_qn));  // open: preset, en, reset
  D_Flip_Flop d_ff_35 (.clk(CLK), .D(mov_ax_bx_out), .Q(d_ff_35_q[2]), .Qn(d_ff_35_qn));  // open: preset, en, reset
  D_Flip_Flop d_ff_36 (.clk(CLK), .D(mov_ax_cx_out), .Q(and_9_out[2]), .Qn(d_ff_36_qn));  // open: preset, en, reset
  D_Flip_Flop d_ff_37 (.clk(CLK), .D(and_10_out[2]), .Q(d_ff_37_q[5]), .Qn(d_ff_37_qn));  // open: preset, en, reset
  D_Flip_Flop d_ff_38 (.clk(CLK), .D(mov___ax_dx_out), .Q(and_10_out[2]), .Qn(d_ff_38_qn));  // open: preset, en, reset
  D_Flip_Flop d_ff_39 (.clk(CLK), .D(d_ff_28_q[2]), .Q(d_ff_39_q[5]), .Qn(d_ff_39_qn));  // open: preset, en, reset
  D_Flip_Flop d_ff_40 (.clk(CLK), .D(d_ff_29_q[2]), .Q(d_ff_40_q[5]), .Qn(d_ff_40_qn));  // open: preset, en, reset
  and and_46 (and_46_out, d_ff_40_qn, d_ff_29_qn);
  and and_47 (and_47_out, and_48_out, and_49_out);
  and and_48 (and_48_out, d_ff_30_qn, d_ff_16_qn);
  and and_49 (and_49_out, and_29_out, and_30_out);
  and and_50 (and_50_out, and_51_out, and_34_out);
  and and_51 (and_51_out, d_ff_21_qn, d_ff_12_qn, d_ff_3_qn);
  and and_52 (and_52_out, or_12_out, d_ff_41_q);
  D_Flip_Flop d_ff_41 (.clk(CLK), .D(d_ff_42_q), .Q(d_ff_41_q), .Qn(d_ff_41_qn));  // open: preset, en, reset
  D_Flip_Flop d_ff_42 (.clk(CLK), .D(mov_ax_value16_out), .Q(d_ff_42_q), .Qn(d_ff_42_qn));  // open: preset, en, reset
  or or_22 (or_22_out, d_ff_42_q, d_ff_41_q);
  D_Flip_Flop d_ff_43 (.clk(CLK), .D(d_ff_32_q), .Q(d_ff_43_q), .Qn(d_ff_43_qn));  // open: preset, en, reset
  or or_23 (or_23_out, d_ff_44_q, or_15_out, d_ff_26_q);
  D_Flip_Flop d_ff_44 (.clk(CLK), .D(d_ff_33_q), .Q(d_ff_44_q), .Qn(d_ff_44_qn));  // open: preset, en, reset
  and and_53 (and_53_out, d_ff_44_qn, d_ff_33_qn, d_ff_26_qn);
  or or_24 (or_24_out, d_ff_45_q, or_16_out, d_ff_27_q);
  D_Flip_Flop d_ff_45 (.clk(CLK), .D(d_ff_34_q), .Q(d_ff_45_q), .Qn(d_ff_45_qn));  // open: preset, en, reset
  and and_54 (and_54_out, d_ff_45_qn, d_ff_34_qn, d_ff_27_qn);
  D_Flip_Flop d_ff_46 (.clk(CLK), .D(d_ff_35_q[2]), .Q(d_ff_46_q[5]), .Qn(d_ff_46_qn));  // open: preset, en, reset
  D_Flip_Flop d_ff_47 (.clk(CLK), .D(and_9_out[2]), .Q(d_ff_47_q[5]), .Qn(d_ff_47_qn));  // open: preset, en, reset
  and and_55 (and_55_out, d_ff_47_qn, d_ff_36_qn);
  and and_56 (and_56_out, d_ff_37_qn, d_ff_38_qn);
  and and_57 (and_57_out, and_58_out, and_59_out);
  and and_58 (and_58_out, d_ff_39_qn, d_ff_28_qn);
  and and_59 (and_59_out, and_46_out, and_47_out);
  D_Flip_Flop d_ff_48 (.clk(CLK), .D(d_ff_41_q), .Q(d_ff_48_q), .Qn(d_ff_48_qn));  // open: preset, en, reset
  and and_60 (and_60_out, d_ff_48_qn, d_ff_41_qn, d_ff_42_qn);
  assign or_25_out = {2'b00, and_42_out, and_42_out[4], 3'b000} | {2'b00, and_44_out, and_44_out[4], 3'b000} | {2'b00, and_25_out, and_25_out[4], 3'b000} | {2'b00, and_27_out, and_27_out[4], 3'b000} | or_29_out;  // OR_Gate or_25, 8 bits wide
  or or_26 (or_26_out, d_ff_43_q, or_14_out, d_ff_25_q);
  and and_61 (and_61_out, d_ff_43_qn, d_ff_32_qn, d_ff_25_qn);
  and and_62 (and_62_out, and_54_out, and_63_out);
  and and_63 (and_63_out, and_64_out, and_65_out);
  and and_64 (and_64_out, d_ff_46_qn, d_ff_35_qn);
  and and_65 (and_65_out, and_55_out, and_66_out);
  and and_66 (and_66_out, and_56_out, and_57_out);
  and mov_ax_value16 (mov_ax_value16_out, and_70_out[0], ~and_70_out[1], ~and_70_out[2], ~and_70_out[3], ~and_70_out[4], ~and_70_out[5], ~and_70_out[6], ~and_70_out[7], ~and_70_out[8], ~and_70_out[9], ~and_70_out[10], ~and_70_out[11], ~and_70_out[12], ~and_70_out[13], ~and_70_out[14], ~and_70_out[15]);  // AND_Gate
  and and_67 (and_67_out[4], and_60_out, and_61_out, and_68_out);
  or or_27 (or_27_out, d_ff_48_q, or_22_out);
  and mov_bx_value16 (mov_bx_value16_out, ~and_70_out[0], and_70_out[1], ~and_70_out[2], ~and_70_out[3], ~and_70_out[4], ~and_70_out[5], ~and_70_out[6], ~and_70_out[7], ~and_70_out[8], ~and_70_out[9], ~and_70_out[10], ~and_70_out[11], ~and_70_out[12], ~and_70_out[13], ~and_70_out[14], ~and_70_out[15]);  // AND_Gate
  and and_68 (and_68_out, and_62_out, and_53_out);
  and mov_cx_value16 (mov_cx_value16_out, and_70_out[0], and_70_out[1], ~and_70_out[2], ~and_70_out[3], ~and_70_out[4], ~and_70_out[5], ~and_70_out[6], ~and_70_out[7], ~and_70_out[8], ~and_70_out[9], ~and_70_out[10], ~and_70_out[11], ~and_70_out[12], ~and_70_out[13], ~and_70_out[14], ~and_70_out[15]);  // AND_Gate
  and mov_dx_value16 (mov_dx_value16_out, ~and_70_out[0], ~and_70_out[1], and_70_out[2], ~and_70_out[3], ~and_70_out[4], ~and_70_out[5], ~and_70_out[6], ~and_70_out[7], ~and_70_out[8], ~and_70_out[9], ~and_70_out[10], ~and_70_out[11], ~and_70_out[12], ~and_70_out[13], ~and_70_out[14], ~and_70_out[15]);  // AND_Gate
  and mov_ax_bx (mov_ax_bx_out, and_70_out[0], ~and_70_out[1], and_70_out[2], ~and_70_out[3], ~and_70_out[4], ~and_70_out[5], ~and_70_out[6], ~and_70_out[7], ~and_70_out[8], ~and_70_out[9], ~and_70_out[10], ~and_70_out[11], ~and_70_out[12], ~and_70_out[13], ~and_70_out[14], ~and_70_out[15]);  // AND_Gate
  and mov_ax_cx (mov_ax_cx_out, ~and_70_out[0], and_70_out[1], and_70_out[2], ~and_70_out[3], ~and_70_out[4], ~and_70_out[5], ~and_70_out[6], ~and_70_out[7], ~and_70_out[8], ~and_70_out[9], ~and_70_out[10], ~and_70_out[11], ~and_70_out[12], ~and_70_out[14], ~and_70_out[14], ~and_70_out[15]);  // AND_Gate
  and mov___ax_dx (mov___ax_dx_out, and_70_out[0], and_70_out[1], and_70_out[2], ~and_70_out[3], ~and_70_out[4], ~and_70_out[5], ~and_70_out[6], ~and_70_out[7], ~and_70_out[8], ~and_70_out[9], ~and_70_out[10], ~and_70_out[11], ~and_70_out[12], ~and_70_out[14], ~and_70_out[14], ~and_70_out[15]);  // AND_Gate
  and mov_bx_ax (mov_bx_ax_out, ~and_70_out[0], ~and_70_out[1], ~and_70_out[2], and_70_out[3], ~and_70_out[4], ~and_70_out[5], ~and_70_out[6], ~and_70_out[7], ~and_70_out[8], ~and_70_out[9], ~and_70_out[10], ~and_70_out[11], ~and_70_out[12], ~and_70_out[14], ~and_70_out[14], ~and_70_out[15]);  // AND_Gate
  and mov_bx_cx (mov_bx_cx_out, and_70_out[0], ~and_70_out[1], ~and_70_out[2], and_70_out[3], ~and_70_out[4], ~and_70_out[5], ~and_70_out[6], ~and_70_out[7], ~and_70_out[8], ~and_70_out[9], ~and_70_out[10], ~and_70_out[11], ~and_70_out[12], ~and_70_out[14], ~and_70_out[14], ~and_70_out[15]);  // AND_Gate
  and mov_bx_dx (mov_bx_dx_out, ~and_70_out[0], and_70_out[1], ~and_70_out[2], and_70_out[3], ~and_70_out[4], ~and_70_out[5], ~and_70_out[6], ~and_70_out[7], ~and_70_out[8], ~and_70_out[9], ~and_70_out[10], ~and_70_out[11], ~and_70_out[12], ~and_70_out[14], ~and_70_out[14], ~and_70_out[15]);  // AND_Gate
  and mov_cx_ax (mov_cx_ax_out, and_70_out[0], and_70_out[1], ~and_70_out[2], and_70_out[3], ~and_70_out[4], ~and_70_out[5], ~and_70_out[6], ~and_70_out[7], ~and_70_out[8], ~and_70_out[9], ~and_70_out[10], ~and_70_out[11], ~and_70_out[12], ~and_70_out[14], ~and_70_out[14], ~and_70_out[15]);  // AND_Gate
  and mov_cx_bx (mov_cx_bx_out, ~and_70_out[0], ~and_70_out[1], and_70_out[2], and_70_out[3], ~and_70_out[4], ~and_70_out[5], ~and_70_out[6], ~and_70_out[7], ~and_70_out[8], ~and_70_out[9], ~and_70_out[10], ~and_70_out[11], ~and_70_out[12], ~and_70_out[14], ~and_70_out[14], ~and_70_out[15]);  // AND_Gate
  and mov_cx_dx (mov_cx_dx_out, and_70_out[0], ~and_70_out[1], and_70_out[2], and_70_out[3], ~and_70_out[4], ~and_70_out[5], ~and_70_out[6], ~and_70_out[7], ~and_70_out[8], ~and_70_out[9], ~and_70_out[10], ~and_70_out[11], ~and_70_out[12], ~and_70_out[14], ~and_70_out[14], ~and_70_out[15]);  // AND_Gate
  and mov_dx_ax (mov_dx_ax_out, ~and_70_out[0], and_70_out[1], and_70_out[2], and_70_out[3], ~and_70_out[4], ~and_70_out[5], ~and_70_out[6], ~and_70_out[7], ~and_70_out[8], ~and_70_out[9], ~and_70_out[10], ~and_70_out[11], ~and_70_out[12], ~and_70_out[14], ~and_70_out[14], ~and_70_out[15]);  // AND_Gate
  and mov_dx_bx (mov_dx_bx_out, and_70_out[0], and_70_out[1], and_70_out[2], and_70_out[3], ~and_70_out[4], ~and_70_out[5], ~and_70_out[6], ~and_70_out[7], ~and_70_out[8], ~and_70_out[9], ~and_70_out[10], ~and_70_out[11], ~and_70_out[12], ~and_70_out[14], ~and_70_out[14], ~and_70_out[15]);  // AND_Gate
  and mov_dx_cx (mov_dx_cx_out, ~and_70_out[0], ~and_70_out[1], ~and_70_out[2], ~and_70_out[3], and_70_out[4], ~and_70_out[5], ~and_70_out[6], ~and_70_out[7], ~and_70_out[8], ~and_70_out[9], ~and_70_out[10], ~and_70_out[11], ~and_70_out[12], ~and_70_out[14], ~and_70_out[14], ~and_70_out[15]);  // AND_Gate
  and mov_ax__ax (mov_ax__ax_out, and_70_out[0], ~and_70_out[1], ~and_70_out[2], ~and_70_out[3], and_70_out[4], ~and_70_out[5], ~and_70_out[6], ~and_70_out[7], ~and_70_out[8], ~and_70_out[9], ~and_70_out[10], ~and_70_out[11], ~and_70_out[12], ~and_70_out[14], ~and_70_out[14], ~and_70_out[15]);  // AND_Gate
  and mov_ax__bx (mov_ax__bx_out, ~and_70_out[0], and_70_out[1], ~and_70_out[2], ~and_70_out[3], and_70_out[4], ~and_70_out[5], ~and_70_out[6], ~and_70_out[7], ~and_70_out[8], ~and_70_out[9], ~and_70_out[10], ~and_70_out[11], ~and_70_out[12], ~and_70_out[14], ~and_70_out[14], ~and_70_out[15]);  // AND_Gate
  and mov_ax__cx (mov_ax__cx_out, and_70_out[0], and_70_out[1], ~and_70_out[2], ~and_70_out[3], and_70_out[4], ~and_70_out[5], ~and_70_out[6], ~and_70_out[7], ~and_70_out[8], ~and_70_out[9], ~and_70_out[10], ~and_70_out[11], ~and_70_out[12], ~and_70_out[14], ~and_70_out[14], ~and_70_out[15]);  // AND_Gate
  and mov_ax__dx (mov_ax__dx_out, ~and_70_out[0], ~and_70_out[1], and_70_out[2], ~and_70_out[3], and_70_out[4], ~and_70_out[5], ~and_70_out[6], ~and_70_out[7], ~and_70_out[8], ~and_70_out[9], ~and_70_out[10], ~and_70_out[11], ~and_70_out[12], ~and_70_out[14], ~and_70_out[14], ~and_70_out[15]);  // AND_Gate
  // AND_Gate mov_bx__ax has open pins: in0=and_70_out[0], in1=and_70_out[1], in2=and_70_out[2], in3=and_70_out[3], in4=and_70_out[4], in5=and_70_out[5], in6=and_70_out[6], in7=and_70_out[7], in8=and_70_out[8], in9=and_70_out[9], in10=and_70_out[10], in11=and_70_out[11], in12=and_70_out[12], in13=and_70_out[14], in14=and_70_out[14], in15=and_70_out[15], out=open
  or or_28 (or_28_out, or_27_out, or_26_out, or_23_out, or_24_out, or_34_out);
  assign and_69_out = 8'h18 & {3'b000, {2{and_67_out[4]}}, 3'b000};  // AND_Gate and_69, 8 bits wide
  assign or_29_out = {2'b00, d_ff_46_q[5], {5{1'b0}}} | {2'b00, d_ff_47_q[5], {5{1'b0}}} | {2'b00, d_ff_37_q[5], {5{1'b0}}} | {2'b00, d_ff_39_q[5], {5{1'b0}}} | {2'b00, d_ff_40_q[5], {5{1'b0}}} | {2'b00, d_ff_30_q[5], {5{1'b0}}} | {2'b00, d_ff_31_q[5], {5{1'b0}}} | {2'b00, d_ff_18_q[5], {5{1'b0}}} | or_30_out;  // OR_Gate or_29, 8 bits wide
  assign or_30_out = or_31_out | {d_ff_13_q[7], 2'b00, {2{d_ff_13_q[7]}}, 3'b000} | {2'b00, or_17_out[5], {5{1'b0}}} | {d_ff_12_q[7], 2'b00, {2{d_ff_12_q[7]}}, 3'b000} | {1'b0, or_9_out[6], {6{1'b0}}} | {2'b00, d_ff_11_q[5], {5{1'b0}}} | {2'b00, d_ff_10_q[5], {5{1'b0}}} | {2'b00, d_ff_20_q[5], {5{1'b0}}} | {2'b00, d_ff_19_q[5], {5{1'b0}}};  // OR_Gate or_30, 8 bits wide
  assign or_31_out = {d_ff_14_q[7], 2'b00, {2{d_ff_14_q[7]}}, 3'b000} | {d_ff_15_q[7], 2'b00, {2{d_ff_15_q[7]}}, 3'b000};  // OR_Gate or_31, 8 bits wide
  or or_32 (RAM0_Instruction_Enable, and_67_out[4], or_28_out);
  assign RAM0_Instruction = and_69_out | or_25_out;  // OR_Gate or_33, 8 bits wide
  or or_34 (or_34_out, d_ff_46_q[5], d_ff_47_q[5], d_ff_37_q[5], d_ff_39_q[5], d_ff_40_q[5], d_ff_30_q[5], d_ff_31_q[5], d_ff_18_q[5], or_35_out);
  or or_35 (or_35_out, or_36_out, d_ff_13_q[7], or_17_out[5], d_ff_12_q[7], or_9_out[6], d_ff_11_q[5], d_ff_10_q[5], d_ff_20_q[5], d_ff_19_q[5]);
  or or_36 (or_36_out, d_ff_14_q[7], d_ff_15_q[7]);
  assign and_70_out = {16{and_67_out[4]}} & Data_In;  // AND_Gate and_70, 16 bits wide

  // Notes on the sheet:
  //   Combine the Enable with the instruction line
  //   Get Address From Reg onto Bus
  //   Save Bus  to Temp Addr
  //   Use Temp Addr,Write To Bus and save to reg 
  //   Inc IP
  //   When not exec inc RAM
  //   Combine the Enable in with the instruction line
endmodule

module BUS_ALU (
  input  [15:0] BUS_In,
  input  Read_Write,
  input  CLK,
  input  Load_Enable,
  input  Load_Selector,
  input  Add_Sub,
  output [15:0] BUS_Out
);

  wire and_1_out, and_2_out, not_1_out;
  wire [15:0] adder_1_out, controlled_buffer_2_out, multiplexer_1_out, register_1_q, register_2_q,
       subtractor_1_out;

  assign BUS_Out = Read_Write ? multiplexer_1_out : 16'bz;  // Controlled_Buffer controlled_buffer_1
  assign controlled_buffer_2_out = not_1_out ? BUS_In : 16'bz;  // Controlled_Buffer controlled_buffer_2
  not not_1 (not_1_out, Read_Write);
  and and_1 (and_1_out, Load_Selector, Load_Enable);
  Register_part #(.width(16)) register_1 (
    .D(controlled_buffer_2_out), .en(and_1_out), .Q(register_1_q), .clk(CLK));  // open: clr
  Register_part #(.width(16)) register_2 (
    .D(controlled_buffer_2_out), .en(and_2_out), .Q(register_2_q), .clk(CLK));  // open: clr
  and and_2 (and_2_out, Load_Enable, ~Load_Selector);  // AND_Gate
  Adder #(.width(16)) adder_1 (.a(register_1_q), .b(register_2_q), .out(adder_1_out));  // open: cin, cout
  Subtractor #(.width(16)) subtractor_1 (
    .a(register_1_q), .b(register_2_q), .out(subtractor_1_out));  // open: bin, bout
  Multiplexer #(.width(16)) multiplexer_1 (
    .in0(adder_1_out), .in1(subtractor_1_out), .out(multiplexer_1_out), .sel(Add_Sub), .en(1'b1));
endmodule

module BUS_RAM (
  input  [15:0] Bus_In,
  input  CLK,
  input  [7:0] RAM_Instruction,
  input  RAM_Instruction_Enable,
  output [15:0] Bus_Out
);

  wire Inc_Address_out, jmp__data_out, Load_Temp_Address_out, mov_ip__ip_out, or_1_out, or_2_out, or_3_out,
       Read_To_BUS_At_IP_out, Read_Write_out, Store_at_IP_out, Use_Instruction_Pointer_Use_Temp_Address_out;
  wire [15:0] controlled_buffer_2_out, Instruction_Pointer_q, multiplexer_1_out, ram_1_data,
       Temp_Address_Pointer_q;

  and jmp__data (jmp__data_out, RAM_Instruction_Enable, RAM_Instruction[0]);
  and mov_ip__ip (mov_ip__ip_out, RAM_Instruction_Enable, RAM_Instruction[1]);
  and Store_at_IP (Store_at_IP_out, RAM_Instruction_Enable, RAM_Instruction[2]);
  and Read_To_BUS_At_IP (Read_To_BUS_At_IP_out, RAM_Instruction_Enable, RAM_Instruction[3]);
  and Read_Write (Read_Write_out, RAM_Instruction_Enable, RAM_Instruction[4]);
  and Inc_Address (Inc_Address_out, RAM_Instruction_Enable, RAM_Instruction[5]);
  and Load_Temp_Address (Load_Temp_Address_out, RAM_Instruction_Enable, RAM_Instruction[6]);
  nand Use_Instruction_Pointer_Use_Temp_Address (Use_Instruction_Pointer_Use_Temp_Address_out, RAM_Instruction_Enable, RAM_Instruction[7]);
  assign Bus_Out = Read_Write_out ? ram_1_data : 16'bz;  // Controlled_Buffer controlled_buffer_1
  assign controlled_buffer_2_out = mov_ip__ip_out ? ram_1_data : 16'bz;  // Controlled_Buffer controlled_buffer_2
  assign controlled_buffer_2_out = or_1_out ? Bus_In : 16'bz;  // Controlled_Buffer controlled_buffer_3
  or or_1 (or_1_out, Store_at_IP_out, Load_Temp_Address_out, jmp__data_out);
  Register_part #(.width(16)) Temp_Address_Pointer (
    .D(controlled_buffer_2_out), .en(Load_Temp_Address_out), .Q(Temp_Address_Pointer_q), .clk(CLK));  // open: clr
  or or_2 (or_2_out, jmp__data_out, mov_ip__ip_out);
  Counter #(.width(16), .max('hffff)) Instruction_Pointer (
    .load(or_2_out), .D(controlled_buffer_2_out), .count(Inc_Address_out), .Q(Instruction_Pointer_q),
    .clk(CLK));  // open: carry, clr
  Multiplexer #(.width(16), .enable("false")) multiplexer_1 (
    .in0(Temp_Address_Pointer_q), .in1(Instruction_Pointer_q), .out(multiplexer_1_out),
    .sel(Use_Instruction_Pointer_Use_Temp_Address_out));
  or or_3 (or_3_out, mov_ip__ip_out, Read_To_BUS_At_IP_out);
  RAM #(.addrWidth(16), .dataWidth(16), .bus("separate")) ram_1 (
    .addr(multiplexer_1_out), .din(controlled_buffer_2_out), .data(ram_1_data), .str(Store_at_IP_out),
    .clk(CLK), .ld(or_3_out));  // open: sel, clr
endmodule

module BUS_GPU (
  input  [15:0] Bus_In,
  input  CLK,
  input  Set_Pixel_Bank,
  input  Bank_Selector,
  output [15:0] Bus_Out
);

  wire and_1_out, decoder_1_out0, decoder_1_out1, decoder_1_out2, decoder_1_out3, decoder_1_out4,
       decoder_1_out5, decoder_1_out6, decoder_1_out7, decoder_1_out8, decoder_1_out9, decoder_1_out10,
       decoder_1_out11, decoder_1_out12, decoder_1_out13, decoder_1_out14, decoder_1_out15, decoder_1_out16,
       decoder_1_out17, decoder_1_out18, decoder_1_out19, decoder_1_out20, decoder_1_out21, decoder_1_out22,
       decoder_1_out23, decoder_1_out24, decoder_1_out25, decoder_1_out26, decoder_1_out27, decoder_1_out28,
       decoder_1_out29, decoder_1_out30, decoder_1_out31, decoder_2_out0, decoder_2_out1, decoder_2_out2,
       decoder_2_out3, decoder_2_out4, decoder_2_out5, decoder_2_out6, decoder_2_out7, decoder_2_out8,
       decoder_2_out9, decoder_2_out10, decoder_2_out11, decoder_2_out12, decoder_2_out13, decoder_2_out14,
       decoder_2_out15, decoder_2_out16, decoder_2_out17, decoder_2_out18, decoder_2_out19, decoder_2_out20,
       decoder_2_out21, decoder_2_out22, decoder_2_out23, decoder_2_out24, decoder_2_out25, decoder_2_out26,
       decoder_2_out27, decoder_2_out28, decoder_2_out29, decoder_2_out30, decoder_2_out31, undriven;
  wire [4:0] controlled_buffer_2_out, register_1_q, register_2_q;
  wire [15:0] undriven_2;
  wire [15:5] controlled_buffer_2_out_2;
  wire [31:0] bus_gpu_register_1_out_5, bus_gpu_register_2_out_5, bus_gpu_register_3_out_5,
       bus_gpu_register_4_out_5, bus_gpu_register_5_out_5, bus_gpu_register_6_out_5,
       bus_gpu_register_7_out_5, bus_gpu_register_8_out_5, bus_gpu_register_9_out_5,
       bus_gpu_register_10_out_5, bus_gpu_register_11_out_5, bus_gpu_register_12_out_5,
       bus_gpu_register_13_out_5, bus_gpu_register_14_out_5, bus_gpu_register_15_out_5,
       bus_gpu_register_16_out_5, bus_gpu_register_17_out_5, bus_gpu_register_18_out_5,
       bus_gpu_register_19_out_5, bus_gpu_register_20_out_5, bus_gpu_register_21_out_5,
       bus_gpu_register_22_out_5, bus_gpu_register_23_out_5, bus_gpu_register_24_out_5,
       bus_gpu_register_25_out_5, bus_gpu_register_26_out_5, bus_gpu_register_27_out_5,
       bus_gpu_register_28_out_5, bus_gpu_register_29_out_5, bus_gpu_register_30_out_5,
       bus_gpu_register_31_out_5, bus_gpu_register_32_out_5;

  assign Bus_Out = undriven ? undriven_2 : 16'bz;  // Controlled_Buffer controlled_buffer_1
  assign {controlled_buffer_2_out_2, controlled_buffer_2_out} = Set_Pixel_Bank ? Bus_In : 16'bz;  // Controlled_Buffer controlled_buffer_2
  Register_part #(.width(5)) register_1 (
    .D(controlled_buffer_2_out), .en(Bank_Selector), .Q(register_1_q), .clk(CLK));  // open: clr
  Decoder_part #(.select(5), .enable("false")) decoder_1 (
    .out0(decoder_1_out0), .out1(decoder_1_out1), .out2(decoder_1_out2), .out3(decoder_1_out3),
    .out4(decoder_1_out4), .out5(decoder_1_out5), .out6(decoder_1_out6), .out7(decoder_1_out7),
    .out8(decoder_1_out8), .out9(decoder_1_out9), .out10(decoder_1_out10), .out11(decoder_1_out11),
    .out12(decoder_1_out12), .out13(decoder_1_out13), .out14(decoder_1_out14), .out15(decoder_1_out15),
    .out16(decoder_1_out16), .out17(decoder_1_out17), .out18(decoder_1_out18), .out19(decoder_1_out19),
    .out20(decoder_1_out20), .out21(decoder_1_out21), .out22(decoder_1_out22), .out23(decoder_1_out23),
    .out24(decoder_1_out24), .out25(decoder_1_out25), .out26(decoder_1_out26), .out27(decoder_1_out27),
    .out28(decoder_1_out28), .out29(decoder_1_out29), .out30(decoder_1_out30), .out31(decoder_1_out31),
    .sel(register_1_q));
  and and_1 (and_1_out, Set_Pixel_Bank, ~Bank_Selector);  // AND_Gate
  Register_part #(.width(5)) register_2 (
    .D(controlled_buffer_2_out), .en(and_1_out), .Q(register_2_q), .clk(CLK));  // open: clr
  Decoder_part #(.select(5), .enable("false")) decoder_2 (
    .out0(decoder_2_out0), .out1(decoder_2_out1), .out2(decoder_2_out2), .out3(decoder_2_out3),
    .out4(decoder_2_out4), .out5(decoder_2_out5), .out6(decoder_2_out6), .out7(decoder_2_out7),
    .out8(decoder_2_out8), .out9(decoder_2_out9), .out10(decoder_2_out10), .out11(decoder_2_out11),
    .out12(decoder_2_out12), .out13(decoder_2_out13), .out14(decoder_2_out14), .out15(decoder_2_out15),
    .out16(decoder_2_out16), .out17(decoder_2_out17), .out18(decoder_2_out18), .out19(decoder_2_out19),
    .out20(decoder_2_out20), .out21(decoder_2_out21), .out22(decoder_2_out22), .out23(decoder_2_out23),
    .out24(decoder_2_out24), .out25(decoder_2_out25), .out26(decoder_2_out26), .out27(decoder_2_out27),
    .out28(decoder_2_out28), .out29(decoder_2_out29), .out30(decoder_2_out30), .out31(decoder_2_out31),
    .sel(register_2_q));
  DotMatrix #(.matrixcols(32), .matrixrows(32)) dotmatrix_1 (
    .col0(bus_gpu_register_1_out_5), .col1(bus_gpu_register_2_out_5), .col2(bus_gpu_register_3_out_5),
    .col3(bus_gpu_register_4_out_5), .col4(bus_gpu_register_5_out_5), .col5(bus_gpu_register_6_out_5),
    .col6(bus_gpu_register_7_out_5), .col7(bus_gpu_register_8_out_5), .col8(bus_gpu_register_9_out_5),
    .col9(bus_gpu_register_10_out_5), .col10(bus_gpu_register_11_out_5), .col11(bus_gpu_register_12_out_5),
    .col12(bus_gpu_register_13_out_5), .col13(bus_gpu_register_14_out_5), .col14(bus_gpu_register_15_out_5),
    .col15(bus_gpu_register_16_out_5), .col16(bus_gpu_register_17_out_5), .col17(bus_gpu_register_18_out_5),
    .col18(bus_gpu_register_19_out_5), .col19(bus_gpu_register_20_out_5), .col20(bus_gpu_register_21_out_5),
    .col21(bus_gpu_register_22_out_5), .col22(bus_gpu_register_23_out_5), .col23(bus_gpu_register_24_out_5),
    .col24(bus_gpu_register_25_out_5), .col25(bus_gpu_register_26_out_5), .col26(bus_gpu_register_27_out_5),
    .col27(bus_gpu_register_28_out_5), .col28(bus_gpu_register_29_out_5), .col29(bus_gpu_register_30_out_5),
    .col30(bus_gpu_register_31_out_5), .col31(bus_gpu_register_32_out_5));
  BUS_GPU_Register bus_gpu_register_1 (
    .Data_In({controlled_buffer_2_out_2, controlled_buffer_2_out}), .CLK(CLK), .Write_Enable(decoder_1_out0),
    .Write_Select(decoder_2_out0), .out_5(bus_gpu_register_1_out_5));
  BUS_GPU_Register bus_gpu_register_2 (
    .Data_In({controlled_buffer_2_out_2, controlled_buffer_2_out}), .CLK(CLK), .Write_Enable(decoder_1_out1),
    .Write_Select(decoder_2_out1), .out_5(bus_gpu_register_2_out_5));
  BUS_GPU_Register bus_gpu_register_3 (
    .Data_In({controlled_buffer_2_out_2, controlled_buffer_2_out}), .CLK(CLK), .Write_Enable(decoder_1_out2),
    .Write_Select(decoder_2_out2), .out_5(bus_gpu_register_3_out_5));
  BUS_GPU_Register bus_gpu_register_4 (
    .Data_In({controlled_buffer_2_out_2, controlled_buffer_2_out}), .CLK(CLK), .Write_Enable(decoder_1_out3),
    .Write_Select(decoder_2_out3), .out_5(bus_gpu_register_4_out_5));
  BUS_GPU_Register bus_gpu_register_5 (
    .Data_In({controlled_buffer_2_out_2, controlled_buffer_2_out}), .CLK(CLK), .Write_Enable(decoder_1_out4),
    .Write_Select(decoder_2_out4), .out_5(bus_gpu_register_5_out_5));
  BUS_GPU_Register bus_gpu_register_6 (
    .Data_In({controlled_buffer_2_out_2, controlled_buffer_2_out}), .CLK(CLK), .Write_Enable(decoder_1_out5),
    .Write_Select(decoder_2_out5), .out_5(bus_gpu_register_6_out_5));
  BUS_GPU_Register bus_gpu_register_7 (
    .Data_In({controlled_buffer_2_out_2, controlled_buffer_2_out}), .CLK(CLK), .Write_Enable(decoder_1_out6),
    .Write_Select(decoder_2_out6), .out_5(bus_gpu_register_7_out_5));
  BUS_GPU_Register bus_gpu_register_8 (
    .Data_In({controlled_buffer_2_out_2, controlled_buffer_2_out}), .CLK(CLK), .Write_Enable(decoder_1_out7),
    .Write_Select(decoder_2_out7), .out_5(bus_gpu_register_8_out_5));
  BUS_GPU_Register bus_gpu_register_9 (
    .Data_In({controlled_buffer_2_out_2, controlled_buffer_2_out}), .CLK(CLK), .Write_Enable(decoder_1_out8),
    .Write_Select(decoder_2_out8), .out_5(bus_gpu_register_9_out_5));
  BUS_GPU_Register bus_gpu_register_10 (
    .Data_In({controlled_buffer_2_out_2, controlled_buffer_2_out}), .CLK(CLK), .Write_Enable(decoder_1_out9),
    .Write_Select(decoder_2_out9), .out_5(bus_gpu_register_10_out_5));
  BUS_GPU_Register bus_gpu_register_11 (
    .Data_In({controlled_buffer_2_out_2, controlled_buffer_2_out}), .CLK(CLK),
    .Write_Enable(decoder_1_out10), .Write_Select(decoder_2_out10), .out_5(bus_gpu_register_11_out_5));
  BUS_GPU_Register bus_gpu_register_12 (
    .Data_In({controlled_buffer_2_out_2, controlled_buffer_2_out}), .CLK(CLK),
    .Write_Enable(decoder_1_out11), .Write_Select(decoder_2_out11), .out_5(bus_gpu_register_12_out_5));
  BUS_GPU_Register bus_gpu_register_13 (
    .Data_In({controlled_buffer_2_out_2, controlled_buffer_2_out}), .CLK(CLK),
    .Write_Enable(decoder_1_out12), .Write_Select(decoder_2_out12), .out_5(bus_gpu_register_13_out_5));
  BUS_GPU_Register bus_gpu_register_14 (
    .Data_In({controlled_buffer_2_out_2, controlled_buffer_2_out}), .CLK(CLK),
    .Write_Enable(decoder_1_out13), .Write_Select(decoder_2_out13), .out_5(bus_gpu_register_14_out_5));
  BUS_GPU_Register bus_gpu_register_15 (
    .Data_In({controlled_buffer_2_out_2, controlled_buffer_2_out}), .CLK(CLK),
    .Write_Enable(decoder_1_out14), .Write_Select(decoder_2_out14), .out_5(bus_gpu_register_15_out_5));
  BUS_GPU_Register bus_gpu_register_16 (
    .Data_In({controlled_buffer_2_out_2, controlled_buffer_2_out}), .CLK(CLK),
    .Write_Enable(decoder_1_out15), .Write_Select(decoder_2_out15), .out_5(bus_gpu_register_16_out_5));
  BUS_GPU_Register bus_gpu_register_17 (
    .Data_In({controlled_buffer_2_out_2, controlled_buffer_2_out}), .CLK(CLK),
    .Write_Enable(decoder_1_out16), .Write_Select(decoder_2_out16), .out_5(bus_gpu_register_17_out_5));
  BUS_GPU_Register bus_gpu_register_18 (
    .Data_In({controlled_buffer_2_out_2, controlled_buffer_2_out}), .CLK(CLK),
    .Write_Enable(decoder_1_out17), .Write_Select(decoder_2_out17), .out_5(bus_gpu_register_18_out_5));
  BUS_GPU_Register bus_gpu_register_19 (
    .Data_In({controlled_buffer_2_out_2, controlled_buffer_2_out}), .CLK(CLK),
    .Write_Enable(decoder_1_out18), .Write_Select(decoder_2_out18), .out_5(bus_gpu_register_19_out_5));
  BUS_GPU_Register bus_gpu_register_20 (
    .Data_In({controlled_buffer_2_out_2, controlled_buffer_2_out}), .CLK(CLK),
    .Write_Enable(decoder_1_out19), .Write_Select(decoder_2_out19), .out_5(bus_gpu_register_20_out_5));
  BUS_GPU_Register bus_gpu_register_21 (
    .Data_In({controlled_buffer_2_out_2, controlled_buffer_2_out}), .CLK(CLK),
    .Write_Enable(decoder_1_out20), .Write_Select(decoder_2_out20), .out_5(bus_gpu_register_21_out_5));
  BUS_GPU_Register bus_gpu_register_22 (
    .Data_In({controlled_buffer_2_out_2, controlled_buffer_2_out}), .CLK(CLK),
    .Write_Enable(decoder_1_out21), .Write_Select(decoder_2_out21), .out_5(bus_gpu_register_22_out_5));
  BUS_GPU_Register bus_gpu_register_23 (
    .Data_In({controlled_buffer_2_out_2, controlled_buffer_2_out}), .CLK(CLK),
    .Write_Enable(decoder_1_out22), .Write_Select(decoder_2_out22), .out_5(bus_gpu_register_23_out_5));
  BUS_GPU_Register bus_gpu_register_24 (
    .Data_In({controlled_buffer_2_out_2, controlled_buffer_2_out}), .CLK(CLK),
    .Write_Enable(decoder_1_out23), .Write_Select(decoder_2_out23), .out_5(bus_gpu_register_24_out_5));
  BUS_GPU_Register bus_gpu_register_25 (
    .Data_In({controlled_buffer_2_out_2, controlled_buffer_2_out}), .CLK(CLK),
    .Write_Enable(decoder_1_out24), .Write_Select(decoder_2_out24), .out_5(bus_gpu_register_25_out_5));
  BUS_GPU_Register bus_gpu_register_26 (
    .Data_In({controlled_buffer_2_out_2, controlled_buffer_2_out}), .CLK(CLK),
    .Write_Enable(decoder_1_out25), .Write_Select(decoder_2_out25), .out_5(bus_gpu_register_26_out_5));
  BUS_GPU_Register bus_gpu_register_27 (
    .Data_In({controlled_buffer_2_out_2, controlled_buffer_2_out}), .CLK(CLK),
    .Write_Enable(decoder_1_out26), .Write_Select(decoder_2_out26), .out_5(bus_gpu_register_27_out_5));
  BUS_GPU_Register bus_gpu_register_28 (
    .Data_In({controlled_buffer_2_out_2, controlled_buffer_2_out}), .CLK(CLK),
    .Write_Enable(decoder_1_out27), .Write_Select(decoder_2_out27), .out_5(bus_gpu_register_28_out_5));
  BUS_GPU_Register bus_gpu_register_29 (
    .Data_In({controlled_buffer_2_out_2, controlled_buffer_2_out}), .CLK(CLK),
    .Write_Enable(decoder_1_out28), .Write_Select(decoder_2_out28), .out_5(bus_gpu_register_29_out_5));
  BUS_GPU_Register bus_gpu_register_30 (
    .Data_In({controlled_buffer_2_out_2, controlled_buffer_2_out}), .CLK(CLK),
    .Write_Enable(decoder_1_out29), .Write_Select(decoder_2_out29), .out_5(bus_gpu_register_30_out_5));
  BUS_GPU_Register bus_gpu_register_31 (
    .Data_In({controlled_buffer_2_out_2, controlled_buffer_2_out}), .CLK(CLK),
    .Write_Enable(decoder_1_out30), .Write_Select(decoder_2_out30), .out_5(bus_gpu_register_31_out_5));
  BUS_GPU_Register bus_gpu_register_32 (
    .Data_In({controlled_buffer_2_out_2, controlled_buffer_2_out}), .CLK(CLK),
    .Write_Enable(decoder_1_out31), .Write_Select(decoder_2_out31), .out_5(bus_gpu_register_32_out_5));
endmodule

module BUS_GPU_Register (
  input  [15:0] Data_In,
  input  CLK,
  input  Write_Enable,
  input  Write_Select,
  output [31:0] out_5
);

  wire and_1_out, and_2_out;

  and and_1 (and_1_out, Write_Enable, ~Write_Select);  // AND_Gate
  and and_2 (and_2_out, Write_Enable, Write_Select);
  Register_part #(.width(16)) register_1 (.D(Data_In), .en(and_1_out), .Q(out_5[15:0]), .clk(CLK));  // open: clr
  Register_part #(.width(16)) register_2 (.D(Data_In), .en(and_2_out), .Q(out_5[31:16]), .clk(CLK));  // open: clr
endmodule

module BUS_Command_Unit_V2 (
  input  [15:0] BUS_In,
  input  CLK,
  output ax_enable,
  output [2:0] ax_instruction,
  output bx_enable,
  output [2:0] bx_instruction,
  output cx_enable,
  output [2:0] cx_instruction,
  output dx_enable,
  output [2:0] dx_instruction,
  output RAM_Enable,
  output [7:0] RAM_Instruction
);

  wire and_1_out, and_2_out, and_3_out, controlled_buffer_3_out, d_ff_1_qn, d_ff_2_q, d_ff_2_qn, not_1_out,
       not_3_out;
  wire [5:4] d_ff_1_q;
  wire [7:0] controlled_buffer_4_out, controlled_buffer_5_out;
  wire [31:0] and_4_out, not_2_out;

  buf and_1 (and_1_out, and_2_out);  // AND_Gate
  assign ax_enable = d_ff_1_q[4] ? d_ff_1_q[4] : 1'bz;  // Controlled_Buffer controlled_buffer_1
  D_Flip_Flop d_ff_1 (.clk(CLK), .D(and_1_out), .Q(d_ff_1_q[4]), .Qn(d_ff_1_qn));  // open: preset, en, reset
  and and_2 (and_2_out, BUS_In[0], ~BUS_In[8]);  // AND_Gate
  assign ax_instruction = not_1_out ? 3'b000 : 3'bz;  // Controlled_Buffer controlled_buffer_2
  D_Flip_Flop d_ff_2 (.clk(CLK), .D(d_ff_1_q[4]), .Q(d_ff_2_q), .Qn(d_ff_2_qn));  // open: preset, en, reset
  not not_1 (not_1_out, and_3_out);
  and and_3 (and_3_out, d_ff_2_qn, d_ff_1_qn);
  or or_1 (d_ff_1_q[5], d_ff_2_q, d_ff_1_q[4]);
  assign controlled_buffer_3_out = d_ff_1_q[5] ? d_ff_1_q[5] : 1'bz;  // Controlled_Buffer controlled_buffer_3
  assign controlled_buffer_4_out = d_ff_1_q[5] ? {2'b00, d_ff_1_q, d_ff_1_q[4], 3'b000} : 8'bz;  // Controlled_Buffer controlled_buffer_4
  not not_2 (not_2_out[0], and_3_out);
  not not_3 (not_3_out, and_3_out);
  assign controlled_buffer_5_out = not_3_out ? controlled_buffer_4_out : 8'bz;  // Controlled_Buffer controlled_buffer_5
  or or_2 (RAM_Enable, controlled_buffer_3_out, and_3_out);
  assign and_4_out = not_2_out & {32{1'b1}};  // AND_Gate and_4, 32 bits wide
  Multiplexer #(.width(8), .enable("false")) multiplexer_1 (
    .in0(8'h18), .in1(controlled_buffer_5_out), .out(RAM_Instruction), .sel(not_3_out));
  // Probe on and_4_out
endmodule
module BUS_Command_Unit_V3 (
  input  CLK,
  input  [15:0] Data_In,
  input  [1:0] Comparison_Line,
  output ax_enable_instruction,
  output [2:0] ax_instruction,
  output bx_enable_instruction,
  output [2:0] bx_instruction,
  output cx_enable_instruction,
  output [2:0] cx_instruction,
  output RAM0_Instruction_Enable,
  output [7:0] RAM0_Instruction,
  output dx_enable_instruction,
  output [2:0] dx_instruction,
  output Math_Unit_Enable,
  output [3:0] Math_Unit_Instruction,
  output Comparison_Enable,
  output Comparison_Instruction
);

  wire add_ax_ax_out, add_ax_bx_out, add_ax_cx_out, add_ax_dx_out, add_bx_ax_out, add_bx_bx_out,
       add_bx_cx_out, add_bx_dx_out, add_cx_ax_out, add_cx_bx_out, add_cx_cx_out, add_cx_dx_out,
       add_dx_ax_out, add_dx_bx_out, add_dx_cx_out, add_dx_dx_out, and_1_out, and_2_out, and_3_out,
       and_4_out, and_5_out, and_6_out, and_7_out, and_8_out, and_9_out, and_10_out, and_11_out, and_12_out,
       and_13_out, and_14_out, and_15_out, and_16_out, and_17_out, and_18_out, and_19_out, and_20_out,
       and_21_out, and_22_out, and_23_out, and_24_out, and_25_out, and_27_out, and_28_out, and_29_out,
       and_30_out, and_31_out, and_32_out, and_33_out, and_34_out, and_35_out, and_36_out, and_37_out,
       and_38_out, and_39_out, and_40_out, and_41_out, and_42_out, and_43_out, and_44_out, and_45_out,
       and_46_out, and_47_out, and_48_out, and_49_out, and_50_out, and_51_out, and_52_out, and_53_out,
       and_54_out, and_55_out, and_56_out, and_57_out, and_58_out, and_59_out, and_60_out, and_61_out,
       and_62_out, and_63_out, and_64_out, and_65_out, and_66_out, and_67_out, and_68_out, and_69_out,
       and_70_out, and_71_out, and_72_out, and_73_out, and_74_out, and_75_out, and_76_out, and_77_out,
       and_78_out, and_79_out, and_80_out, and_81_out, and_82_out, and_83_out, and_84_out, and_85_out,
       and_86_out, and_87_out, and_88_out, and_89_out, and_90_out, and_91_out, and_92_out, and_93_out,
       and_94_out, and_95_out, and_96_out, and_97_out, and_98_out, and_99_out, and_100_out, and_101_out,
       and_102_out, and_103_out, and_104_out, and_105_out, and_106_out, and_107_out, and_108_out,
       and_109_out, and_110_out, and_111_out, and_112_out, and_113_out, and_114_out, and_115_out,
       and_116_out, and_117_out, and_118_out, and_119_out, and_120_out, and_121_out, and_122_out,
       and_123_out, and_124_out, and_125_out, and_126_out, and_127_out, and_128_out, and_129_out,
       and_130_out, and_131_out, and_132_out, and_133_out, and_134_out, and_135_out, and_136_out,
       and_137_out, and_138_out, and_139_out, and_140_out, and_141_out, and_142_out, and_143_out,
       and_144_out, and_145_out, and_146_out, and_147_out, and_148_out, and_149_out, and_150_out,
       and_151_out, and_152_out, and_153_out, cmp_ax_bx_out, command_unit_cmp_instruction_1_ram_enable,
       command_unit_cmp_instruction_1_running_instruction, d_ff_1_q, d_ff_1_qn, d_ff_2_q, d_ff_2_qn,
       d_ff_3_q, d_ff_3_qn, d_ff_4_qn, d_ff_5_qn, d_ff_6_qn, d_ff_7_qn, d_ff_8_qn, d_ff_9_qn, d_ff_10_qn,
       d_ff_11_qn, d_ff_12_qn, d_ff_13_qn, d_ff_14_qn, d_ff_15_qn, d_ff_16_qn, d_ff_17_qn, d_ff_18_qn,
       d_ff_19_qn, d_ff_20_qn, d_ff_21_qn, d_ff_22_qn, d_ff_23_qn, d_ff_24_qn, d_ff_25_qn, d_ff_26_qn,
       d_ff_27_qn, d_ff_28_qn, d_ff_29_qn, d_ff_30_qn, d_ff_31_qn, d_ff_32_qn, d_ff_33_qn, d_ff_34_qn,
       d_ff_35_qn, d_ff_36_qn, d_ff_37_qn, d_ff_38_qn, d_ff_39_qn, d_ff_40_qn, d_ff_41_qn, d_ff_42_qn,
       d_ff_43_qn, d_ff_44_qn, d_ff_45_qn, d_ff_46_qn, d_ff_47_qn, d_ff_48_q, d_ff_48_qn, d_ff_49_q,
       d_ff_49_qn, d_ff_50_q, d_ff_50_qn, d_ff_51_q, d_ff_51_qn, d_ff_52_q, d_ff_52_qn, d_ff_53_q,
       d_ff_53_qn, d_ff_54_q, d_ff_54_qn, d_ff_55_q, d_ff_55_qn, d_ff_56_q, d_ff_56_qn, d_ff_57_q,
       d_ff_57_qn, d_ff_58_q, d_ff_58_qn, d_ff_59_q, d_ff_59_qn, d_ff_60_q, d_ff_60_qn, d_ff_61_q,
       d_ff_61_qn, d_ff_62_q, d_ff_62_qn, d_ff_63_q, d_ff_63_qn, d_ff_64_qn, d_ff_65_qn, d_ff_66_qn,
       d_ff_67_qn, d_ff_68_qn, d_ff_69_qn, d_ff_70_qn, d_ff_71_qn, d_ff_72_qn, d_ff_73_qn, d_ff_74_qn,
       d_ff_75_qn, d_ff_76_q, d_ff_76_qn, d_ff_77_qn, d_ff_78_qn, d_ff_79_qn, d_ff_80_qn, d_ff_81_qn,
       d_ff_82_qn, d_ff_83_qn, d_ff_84_qn, d_ff_85_qn, d_ff_86_qn, d_ff_87_qn, d_ff_88_qn, d_ff_89_qn,
       d_ff_90_qn, d_ff_91_qn, d_ff_92_qn, d_ff_93_qn, d_ff_94_qn, d_ff_95_qn, d_ff_96_qn, d_ff_97_qn,
       d_ff_98_qn, d_ff_99_qn, d_ff_100_qn, d_ff_101_qn, d_ff_102_qn, d_ff_103_qn, d_ff_104_qn, d_ff_105_qn,
       d_ff_106_qn, d_ff_107_qn, d_ff_108_qn, d_ff_109_qn, d_ff_110_qn, d_ff_111_qn, d_ff_112_qn,
       d_ff_113_qn, d_ff_114_qn, d_ff_115_qn, d_ff_116_qn, d_ff_117_qn, d_ff_118_qn, d_ff_119_qn,
       d_ff_120_qn, d_ff_121_qn, d_ff_122_qn, d_ff_123_qn, d_ff_124_qn, d_ff_125_qn, d_ff_126_qn,
       d_ff_127_qn, d_ff_128_qn, d_ff_129_qn, d_ff_130_qn, d_ff_131_qn, d_ff_132_qn, d_ff_133_qn,
       d_ff_134_qn, d_ff_135_qn, d_ff_136_qn, d_ff_137_qn, d_ff_138_qn, d_ff_139_qn, d_ff_140_q, d_ff_140_qn,
       d_ff_141_q, d_ff_141_qn, d_ff_142_q, d_ff_142_qn, d_ff_143_q, d_ff_143_qn, d_ff_144_q, d_ff_144_qn,
       d_ff_145_q, d_ff_145_qn, d_ff_146_q, d_ff_146_qn, d_ff_147_q, d_ff_147_qn, d_ff_148_q, d_ff_148_qn,
       d_ff_149_q, d_ff_149_qn, d_ff_150_q, d_ff_150_qn, d_ff_151_q, d_ff_151_qn, d_ff_152_q, d_ff_152_qn,
       d_ff_153_qn, d_ff_154_q, d_ff_154_qn, d_ff_155_q, d_ff_155_qn, d_ff_156_q, d_ff_156_qn, d_ff_157_qn,
       d_ff_158_qn, d_ff_159_qn, d_ff_160_qn, d_ff_161_qn, d_ff_162_qn, d_ff_163_qn, d_ff_164_qn,
       d_ff_165_qn, d_ff_166_qn, d_ff_167_qn, d_ff_168_qn, d_ff_169_qn, d_ff_170_qn, d_ff_171_qn,
       d_ff_172_qn, d_ff_173_qn, d_ff_174_qn, d_ff_175_qn, d_ff_176_qn, d_ff_177_qn, d_ff_178_qn,
       d_ff_179_qn, d_ff_180_qn, d_ff_181_qn, d_ff_182_qn, d_ff_183_qn, d_ff_184_qn, d_ff_185_qn,
       d_ff_186_qn, d_ff_187_qn, d_ff_188_qn, d_ff_189_qn, d_ff_190_qn, d_ff_191_qn, d_ff_192_qn,
       d_ff_193_qn, d_ff_194_qn, d_ff_195_qn, d_ff_196_qn, d_ff_197_qn, d_ff_198_qn, d_ff_199_qn,
       d_ff_200_qn, d_ff_201_qn, d_ff_202_qn, d_ff_203_qn, d_ff_204_qn, d_ff_205_qn, d_ff_206_qn,
       d_ff_207_qn, d_ff_208_qn, d_ff_209_qn, d_ff_210_qn, d_ff_211_qn, d_ff_212_qn, d_ff_213_qn,
       d_ff_214_qn, d_ff_215_qn, d_ff_216_qn, d_ff_217_qn, d_ff_218_qn, d_ff_219_qn, d_ff_220_qn,
       d_ff_221_qn, d_ff_222_qn, d_ff_223_qn, d_ff_224_qn, d_ff_225_qn, d_ff_226_qn, d_ff_227_qn,
       d_ff_228_qn, d_ff_229_qn, d_ff_230_qn, d_ff_231_qn, d_ff_232_qn, d_ff_233_qn, d_ff_234_qn,
       d_ff_235_qn, d_ff_236_qn, d_ff_237_qn, d_ff_238_qn, d_ff_239_qn, d_ff_240_qn, d_ff_241_qn,
       d_ff_242_qn, d_ff_243_qn, d_ff_244_qn, mov__ax__ax_out, mov__ax__bx_out, mov__ax__cx_out,
       mov__ax__dx_out, mov__bx__ax_out, mov__bx__bx_out, mov__bx__cx_out, mov__bx__dx_out, mov__cx__ax_out,
       mov__cx__bx_out, mov__cx__cx_out, mov__cx__dx_out, mov__dx__ax_out, mov__dx__bx_out, mov__dx__cx_out,
       mov__dx__dx_out, mov_ax__ax_out, mov_ax__bx_out, mov_ax__cx_out, mov_ax__dx_out, mov_ax_bx_out,
       mov_ax_cx_out, mov_ax_dx_out, mov_ax_value16_out, mov_bx__ax_out, mov_bx__bx_out, mov_bx__cx_out,
       mov_bx__dx_out, mov_bx_ax_out, mov_bx_cx_out, mov_bx_dx_out, mov_bx_value16_out, mov_cx__ax_out,
       mov_cx__bx_out, mov_cx__cx_out, mov_cx__dx_out, mov_cx_ax_out, mov_cx_bx_out, mov_cx_dx_out,
       mov_cx_value16_out, mov_dx__ax_out, mov_dx__bx_out, mov_dx__cx_out, mov_dx__dx_out, mov_dx_ax_out,
       mov_dx_bx_out, mov_dx_cx_out, mov_dx_value16_out, not_1_out, not_2_out, not_3_out, or_1_out, or_4_out,
       or_6_out, or_8_out, or_9_out, or_11_out, or_14_out, or_16_out, or_17_out, or_20_out, or_22_out,
       or_23_out, or_25_out, or_27_out, or_29_out, or_31_out, or_34_out, or_35_out, or_38_out, or_40_out,
       or_41_out, or_43_out, or_45_out, or_47_out, or_49_out, or_52_out, or_53_out, or_55_out, or_58_out,
       or_60_out, or_62_out, or_63_out, or_66_out, or_76_out, or_77_out, or_80_out, or_81_out, or_83_out,
       or_86_out, or_87_out, or_89_out, or_91_out, or_94_out, or_96_out, or_97_out, or_99_out, or_101_out,
       or_103_out, or_106_out, or_107_out, or_110_out, or_112_out, or_114_out, or_116_out, or_118_out,
       or_119_out, or_121_out, or_124_out, or_126_out, or_128_out, or_130_out, or_132_out, or_134_out,
       or_135_out, or_138_out, or_139_out, or_143_out, or_145_out, or_147_out, or_148_out, or_151_out,
       or_152_out, or_154_out, or_157_out, or_159_out, or_161_out, or_162_out, or_165_out, or_166_out,
       or_169_out, or_171_out, or_172_out, or_174_out, or_176_out, or_178_out, or_180_out, or_182_out,
       or_185_out, or_186_out, or_188_out, or_191_out, or_193_out, or_195_out, or_197_out, or_199_out,
       or_201_out, or_202_out, or_204_out, or_207_out, or_208_out, or_210_out, or_212_out, or_214_out,
       or_217_out, or_218_out, or_221_out, or_223_out, or_224_out, or_227_out, or_228_out, or_230_out,
       or_233_out, or_234_out, or_237_out, or_238_out, or_240_out, or_243_out, or_245_out, or_246_out,
       or_248_out, or_251_out, or_253_out, or_255_out, or_256_out, or_259_out, or_260_out, or_263_out,
       or_264_out, or_266_out, or_269_out, or_270_out, or_272_out, or_273_out, or_274_out, or_275_out,
       or_276_out, or_277_out, or_278_out, or_279_out, or_280_out, or_281_out, or_282_out, or_283_out,
       or_284_out, or_285_out, or_286_out, or_287_out, or_288_out, or_289_out, or_290_out, or_291_out,
       or_292_out, or_293_out, or_294_out, or_295_out, or_296_out, or_297_out, or_298_out, or_299_out,
       or_300_out, or_301_out, or_302_out, or_303_out, or_307_out, or_324_out, or_330_out, or_336_out,
       or_342_out, or_429_out, or_431_out, or_433_out, or_434_out, or_435_out, or_436_out, or_437_out,
       or_438_out, or_439_out, or_440_out, or_441_out, or_442_out, or_443_out, or_444_out, or_445_out,
       or_446_out, or_447_out, or_448_out, or_449_out, or_450_out, or_451_out, or_452_out, or_453_out,
       or_454_out, or_455_out, or_456_out, or_457_out, or_458_out, or_459_out, or_460_out, or_461_out,
       or_462_out, or_463_out, or_464_out, or_465_out, or_466_out, or_467_out, or_468_out, or_469_out,
       or_470_out, or_471_out, or_472_out, or_473_out, or_474_out, or_475_out, or_476_out, or_477_out,
       or_478_out, or_479_out, or_480_out, or_481_out, or_482_out, or_483_out, or_484_out, or_485_out,
       or_486_out, or_487_out, or_488_out, or_489_out, or_490_out, or_491_out, or_492_out, or_493_out,
       or_494_out, or_495_out, or_496_out, or_497_out, or_498_out, or_499_out, or_500_out, or_501_out,
       or_502_out, or_503_out, or_504_out, or_506_out, or_509_out, or_538_out, or_568_out, or_569_out,
       or_570_out, or_571_out, or_572_out, or_573_out, or_574_out, or_575_out, or_576_out, or_577_out,
       or_578_out, or_579_out, or_580_out, or_581_out, or_582_out, or_583_out, or_584_out, or_585_out,
       or_586_out, or_587_out, or_588_out, or_589_out, or_590_out, or_591_out, or_592_out, or_593_out,
       or_594_out, sub_ax_bx_out, sub_ax_cx_out, sub_ax_dx_out, sub_bx_ax_out, sub_bx_cx_out, sub_bx_dx_out,
       sub_cx_ax_out, sub_cx_bx_out, sub_cx_dx_out, sub_dx_ax_out, sub_dx_bx_out, sub_dx_cx_out;
  wire [2:0] or_2_out, or_3_out, or_5_out, or_7_out, or_10_out, or_12_out, or_13_out, or_15_out, or_18_out,
       or_19_out, or_21_out, or_24_out, or_26_out, or_28_out, or_30_out, or_32_out, or_33_out, or_36_out,
       or_37_out, or_39_out, or_42_out, or_44_out, or_46_out, or_48_out, or_50_out, or_51_out, or_54_out,
       or_56_out, or_57_out, or_59_out, or_61_out, or_64_out, or_65_out, or_75_out, or_78_out, or_79_out,
       or_82_out, or_84_out, or_85_out, or_88_out, or_90_out, or_92_out, or_93_out, or_95_out, or_98_out,
       or_100_out, or_102_out, or_104_out, or_105_out, or_108_out, or_109_out, or_111_out, or_113_out,
       or_115_out, or_117_out, or_120_out, or_122_out, or_123_out, or_125_out, or_127_out, or_129_out,
       or_131_out, or_133_out, or_136_out, or_137_out, or_140_out, or_141_out, or_142_out, or_144_out,
       or_146_out, or_149_out, or_150_out, or_153_out, or_155_out, or_156_out, or_158_out, or_160_out,
       or_163_out, or_164_out, or_167_out, or_168_out, or_170_out, or_173_out, or_175_out, or_177_out,
       or_179_out, or_181_out, or_183_out, or_184_out, or_187_out, or_189_out, or_190_out, or_192_out,
       or_194_out, or_196_out, or_198_out, or_200_out, or_203_out, or_205_out, or_206_out, or_209_out,
       or_211_out, or_213_out, or_215_out, or_216_out, or_219_out, or_220_out, or_222_out, or_225_out,
       or_226_out, or_229_out, or_231_out, or_232_out, or_235_out, or_236_out, or_239_out, or_241_out,
       or_242_out, or_244_out, or_247_out, or_249_out, or_250_out, or_252_out, or_254_out, or_257_out,
       or_258_out, or_261_out, or_262_out, or_265_out, or_267_out, or_268_out, or_271_out;
  wire [2:2] d_ff_4_q, d_ff_5_q, d_ff_6_q, d_ff_7_q, d_ff_8_q, d_ff_9_q, d_ff_10_q, d_ff_11_q, d_ff_12_q,
       d_ff_13_q, d_ff_14_q, d_ff_15_q, d_ff_16_q, d_ff_17_q, d_ff_18_q, d_ff_19_q, d_ff_20_q, d_ff_21_q,
       d_ff_22_q, d_ff_23_q, d_ff_24_q, d_ff_25_q, d_ff_26_q, d_ff_27_q, d_ff_28_q, d_ff_29_q, d_ff_30_q,
       d_ff_31_q, or_308_out, or_309_out, or_310_out, or_311_out, or_312_out, or_313_out, or_314_out,
       or_315_out, or_316_out, or_317_out, or_318_out, or_319_out, or_320_out, or_321_out, or_322_out,
       or_323_out, or_325_out, or_326_out, or_327_out, or_328_out, or_329_out, or_331_out, or_332_out,
       or_333_out, or_334_out, or_335_out, or_337_out, or_338_out, or_339_out, or_340_out, or_341_out,
       or_343_out, or_344_out, or_345_out, or_346_out, or_347_out, or_348_out, or_349_out, or_350_out,
       or_351_out, or_352_out, or_353_out, or_354_out, or_355_out;
  wire [3:0] d_ff_64_q, d_ff_65_q, d_ff_66_q, d_ff_67_q, d_ff_68_q, d_ff_69_q, d_ff_70_q, d_ff_71_q,
       d_ff_72_q, d_ff_73_q, d_ff_74_q, d_ff_75_q, d_ff_124_q, d_ff_125_q, d_ff_126_q, d_ff_127_q,
       d_ff_128_q, d_ff_129_q, d_ff_130_q, d_ff_131_q, d_ff_132_q, d_ff_133_q, d_ff_134_q, d_ff_135_q,
       d_ff_136_q, d_ff_137_q, d_ff_138_q, d_ff_139_q, or_539_out, or_540_out, or_541_out, or_542_out,
       or_543_out, or_544_out, or_545_out, or_546_out, or_547_out, or_548_out, or_549_out, or_550_out,
       or_551_out, or_552_out, or_553_out, or_554_out, or_555_out, or_556_out, or_557_out, or_558_out,
       or_559_out, or_560_out, or_561_out, or_562_out, or_563_out, or_564_out, or_565_out;
  wire [4:4] and_26_out;
  wire [5:4] d_ff_77_q, d_ff_78_q, d_ff_79_q, d_ff_153_q;
  wire [5:5] d_ff_80_q, d_ff_81_q, d_ff_82_q, d_ff_83_q, d_ff_84_q, d_ff_85_q, d_ff_86_q, d_ff_87_q,
       d_ff_88_q, d_ff_89_q, d_ff_90_q, d_ff_91_q, d_ff_217_q, d_ff_218_q, d_ff_219_q, d_ff_220_q,
       d_ff_221_q, d_ff_222_q, d_ff_223_q, d_ff_224_q, d_ff_225_q, d_ff_226_q, d_ff_227_q, d_ff_228_q,
       d_ff_229_q, d_ff_230_q, d_ff_231_q, d_ff_232_q, d_ff_233_q, d_ff_234_q, d_ff_235_q, d_ff_236_q,
       d_ff_237_q, d_ff_238_q, d_ff_239_q, d_ff_240_q, d_ff_241_q, d_ff_242_q, d_ff_243_q, d_ff_244_q;
  wire [7:0] command_unit_cmp_instruction_1_ram_instruction, or_357_out, or_358_out, or_359_out, or_360_out,
       or_361_out, or_362_out, or_363_out, or_364_out, or_365_out, or_366_out, or_367_out, or_368_out,
       or_369_out, or_370_out, or_371_out, or_372_out, or_373_out, or_374_out, or_375_out, or_376_out,
       or_377_out, or_378_out, or_379_out, or_380_out, or_381_out, or_382_out, or_383_out, or_384_out,
       or_385_out, or_386_out, or_387_out, or_388_out, or_389_out, or_390_out, or_391_out, or_392_out,
       or_393_out, or_394_out, or_395_out, or_396_out, or_397_out, or_398_out, or_399_out, or_400_out,
       or_401_out, or_402_out, or_403_out, or_404_out, or_405_out, or_406_out, or_407_out, or_408_out,
       or_409_out, or_410_out, or_411_out, or_412_out, or_413_out, or_414_out, or_415_out, or_416_out,
       or_417_out, or_418_out, or_419_out, or_420_out, or_421_out, or_422_out, or_423_out, or_424_out,
       or_425_out, or_426_out, or_427_out, or_428_out, or_430_out, or_432_out, or_505_out, or_507_out,
       or_508_out;
  wire [7:5] d_ff_157_q, d_ff_158_q, d_ff_159_q, d_ff_160_q, d_ff_161_q, d_ff_162_q, d_ff_163_q, d_ff_164_q,
       d_ff_165_q, d_ff_166_q, d_ff_167_q, d_ff_168_q, d_ff_169_q, d_ff_170_q, d_ff_171_q, d_ff_172_q,
       d_ff_173_q, d_ff_174_q, d_ff_175_q, d_ff_176_q, d_ff_177_q, d_ff_178_q, d_ff_179_q, d_ff_180_q,
       d_ff_181_q, d_ff_182_q, d_ff_183_q, d_ff_184_q, d_ff_185_q, d_ff_186_q, d_ff_187_q, d_ff_188_q;
  wire [15:0] and_154_out;

  or or_1 (or_1_out, or_4_out, d_ff_6_q[2]);
  assign or_2_out = or_3_out | {{2{d_ff_6_q[2]}}, 1'b0};  // OR_Gate or_2, 3 bits wide
  assign or_3_out = or_5_out | {{2{d_ff_9_q[2]}}, 1'b0};  // OR_Gate or_3, 3 bits wide
  or or_4 (or_4_out, or_6_out, d_ff_9_q[2]);
  assign or_5_out = or_7_out | {{2{d_ff_12_q[2]}}, 1'b0};  // OR_Gate or_5, 3 bits wide
  or or_6 (or_6_out, or_8_out, d_ff_12_q[2]);
  assign or_7_out = or_10_out | 3'b000;  // OR_Gate or_7, 3 bits wide
  or or_8 (or_8_out, or_9_out, d_ff_13_q[2]);
  or or_9 (or_9_out, or_11_out, d_ff_14_q[2]);
  assign or_10_out = or_12_out | 3'b000;  // OR_Gate or_10, 3 bits wide
  or or_11 (or_11_out, or_14_out, d_ff_15_q[2]);
  assign or_12_out = or_13_out | 3'b000;  // OR_Gate or_12, 3 bits wide
  assign or_13_out = or_15_out | {{2{d_ff_19_q[2]}}, 1'b0};  // OR_Gate or_13, 3 bits wide
  or or_14 (or_14_out, or_16_out, d_ff_19_q[2]);
  assign or_15_out = or_18_out | {{2{d_ff_23_q[2]}}, 1'b0};  // OR_Gate or_15, 3 bits wide
  or or_16 (or_16_out, or_17_out, d_ff_23_q[2]);
  or or_17 (or_17_out, or_20_out, d_ff_27_q[2]);
  assign or_18_out = or_19_out | {{2{d_ff_27_q[2]}}, 1'b0};  // OR_Gate or_18, 3 bits wide
  assign or_19_out = or_21_out | {{2{d_ff_28_q[2]}}, 1'b0};  // OR_Gate or_19, 3 bits wide
  or or_20 (or_20_out, or_22_out, d_ff_169_q[7]);
  assign or_21_out = or_24_out | {{2{d_ff_29_q[2]}}, 1'b0};  // OR_Gate or_21, 3 bits wide
  or or_22 (or_22_out, or_23_out, d_ff_170_q[7]);
  or or_23 (or_23_out, or_25_out, d_ff_171_q[7]);
  assign or_24_out = or_26_out | {{2{d_ff_30_q[2]}}, 1'b0};  // OR_Gate or_24, 3 bits wide
  or or_25 (or_25_out, or_27_out, or_275_out);
  assign or_26_out = or_28_out | {{2{d_ff_31_q[2]}}, 1'b0};  // OR_Gate or_26, 3 bits wide
  or or_27 (or_27_out, or_29_out, d_ff_176_q[7]);
  assign or_28_out = or_30_out | {{2{or_311_out[2]}}, 1'b0};  // OR_Gate or_28, 3 bits wide
  or or_29 (or_29_out, or_31_out, d_ff_180_q[7]);
  assign or_30_out = or_32_out | {{2{or_315_out[2]}}, 1'b0};  // OR_Gate or_30, 3 bits wide
  or or_31 (or_31_out, or_34_out, d_ff_184_q[7]);
  assign or_32_out = or_33_out | {{2{or_319_out[2]}}, 1'b0};  // OR_Gate or_32, 3 bits wide
  assign or_33_out = or_36_out | {{2{or_320_out[2]}}, 1'b0};  // OR_Gate or_33, 3 bits wide
  or or_34 (or_34_out, or_35_out, d_ff_185_q[6]);
  or or_35 (or_35_out, or_38_out, d_ff_186_q[6]);
  assign or_36_out = or_37_out | {{2{or_321_out[2]}}, 1'b0};  // OR_Gate or_36, 3 bits wide
  assign or_37_out = or_39_out | {{2{or_322_out[2]}}, 1'b0};  // OR_Gate or_37, 3 bits wide
  or or_38 (or_38_out, or_40_out, d_ff_187_q[6]);
  assign or_39_out = or_42_out | {{2{or_323_out[2]}}, 1'b0};  // OR_Gate or_39, 3 bits wide
  or or_40 (or_40_out, or_41_out, or_279_out);
  or or_41 (or_41_out, or_43_out, d_ff_51_q);
  assign or_42_out = or_44_out | {{2{or_328_out[2]}}, 1'b0};  // OR_Gate or_42, 3 bits wide
  or or_43 (or_43_out, or_45_out, d_ff_55_q);
  assign or_44_out = or_46_out | {{2{or_333_out[2]}}, 1'b0};  // OR_Gate or_44, 3 bits wide
  or or_45 (or_45_out, or_47_out, d_ff_59_q);
  assign or_46_out = or_48_out | {{2{or_338_out[2]}}, 1'b0};  // OR_Gate or_46, 3 bits wide
  or or_47 (or_47_out, or_49_out, or_289_out);
  assign or_48_out = or_50_out | {{2{or_339_out[2]}}, 1'b0};  // OR_Gate or_48, 3 bits wide
  or or_49 (or_49_out, or_52_out, or_290_out);
  assign or_50_out = or_51_out | {{2{or_340_out[2]}}, 1'b0};  // OR_Gate or_50, 3 bits wide
  assign or_51_out = or_54_out | {{2{or_341_out[2]}}, 1'b0};  // OR_Gate or_51, 3 bits wide
  or or_52 (or_52_out, or_53_out, or_291_out);
  or or_53 (or_53_out, or_55_out, or_342_out);
  assign or_54_out = or_56_out | {{2{or_343_out[2]}}, 1'b0};  // OR_Gate or_54, 3 bits wide
  or or_55 (or_55_out, or_58_out, d_ff_66_q[0]);
  assign or_56_out = or_57_out | {{2{or_346_out[2]}}, 1'b0};  // OR_Gate or_56, 3 bits wide
  assign or_57_out = or_59_out | {{2{or_349_out[2]}}, 1'b0};  // OR_Gate or_57, 3 bits wide
  or or_58 (or_58_out, or_60_out, d_ff_69_q[0]);
  assign or_59_out = or_61_out | {{2{or_352_out[2]}}, 1'b0};  // OR_Gate or_59, 3 bits wide
  or or_60 (or_60_out, or_62_out, d_ff_72_q[0]);
  assign or_61_out = or_64_out | {{2{or_353_out[2]}}, 1'b0};  // OR_Gate or_61, 3 bits wide
  or or_62 (or_62_out, or_63_out, or_301_out);
  or or_63 (or_63_out, or_66_out, or_302_out);
  assign or_64_out = or_65_out | {{2{or_354_out[2]}}, 1'b0};  // OR_Gate or_64, 3 bits wide
  assign or_65_out = {{2{or_355_out[2]}}, 1'b0};  // OR_Gate or_65, 3 bits wide OR_Gate
  buf or_66 (or_66_out, or_303_out);  // OR_Gate
  or or_67 (ax_enable_instruction, d_ff_153_q[4], or_272_out);
  assign ax_instruction = 3'b000 | or_206_out;  // OR_Gate or_68, 3 bits wide
  or or_69 (bx_enable_instruction, d_ff_77_q[4], or_207_out);
  assign bx_instruction = 3'b000 | or_141_out;  // OR_Gate or_70, 3 bits wide
  or or_71 (cx_enable_instruction, d_ff_78_q[4], or_76_out);
  assign cx_instruction = 3'b000 | or_75_out;  // OR_Gate or_72, 3 bits wide
  or or_73 (dx_enable_instruction, d_ff_79_q[4], or_1_out);
  assign dx_instruction = 3'b000 | or_2_out;  // OR_Gate or_74, 3 bits wide
  assign or_75_out = or_78_out | {{2{d_ff_5_q[2]}}, 1'b0};  // OR_Gate or_75, 3 bits wide
  or or_76 (or_76_out, or_77_out, d_ff_5_q[2]);
  or or_77 (or_77_out, or_80_out, d_ff_8_q[2]);
  assign or_78_out = or_79_out | {{2{d_ff_8_q[2]}}, 1'b0};  // OR_Gate or_78, 3 bits wide
  assign or_79_out = or_82_out | 3'b000;  // OR_Gate or_79, 3 bits wide
  or or_80 (or_80_out, or_81_out, d_ff_10_q[2]);
  or or_81 (or_81_out, or_83_out, d_ff_11_q[2]);
  assign or_82_out = or_84_out | 3'b000;  // OR_Gate or_82, 3 bits wide
  or or_83 (or_83_out, or_86_out, d_ff_12_q[2]);
  assign or_84_out = or_85_out | 3'b000;  // OR_Gate or_84, 3 bits wide
  assign or_85_out = or_88_out | {{2{d_ff_15_q[2]}}, 1'b0};  // OR_Gate or_85, 3 bits wide
  or or_86 (or_86_out, or_87_out, d_ff_15_q[2]);
  or or_87 (or_87_out, or_89_out, d_ff_18_q[2]);
  assign or_88_out = or_90_out | {{2{d_ff_18_q[2]}}, 1'b0};  // OR_Gate or_88, 3 bits wide
  or or_89 (or_89_out, or_91_out, d_ff_22_q[2]);
  assign or_90_out = or_92_out | {{2{d_ff_22_q[2]}}, 1'b0};  // OR_Gate or_90, 3 bits wide
  or or_91 (or_91_out, or_94_out, d_ff_165_q[7]);
  assign or_92_out = or_93_out | {{2{d_ff_24_q[2]}}, 1'b0};  // OR_Gate or_92, 3 bits wide
  assign or_93_out = or_95_out | {{2{d_ff_25_q[2]}}, 1'b0};  // OR_Gate or_93, 3 bits wide
  or or_94 (or_94_out, or_96_out, d_ff_166_q[7]);
  assign or_95_out = or_98_out | {{2{d_ff_26_q[2]}}, 1'b0};  // OR_Gate or_95, 3 bits wide
  or or_96 (or_96_out, or_97_out, or_274_out);
  or or_97 (or_97_out, or_99_out, d_ff_168_q[7]);
  assign or_98_out = or_100_out | {{2{d_ff_27_q[2]}}, 1'b0};  // OR_Gate or_98, 3 bits wide
  or or_99 (or_99_out, or_101_out, d_ff_30_q[2]);
  assign or_100_out = or_102_out | {{2{d_ff_30_q[2]}}, 1'b0};  // OR_Gate or_100, 3 bits wide
  or or_101 (or_101_out, or_103_out, d_ff_175_q[7]);
  assign or_102_out = or_104_out | {{2{or_310_out[2]}}, 1'b0};  // OR_Gate or_102, 3 bits wide
  or or_103 (or_103_out, or_106_out, d_ff_179_q[7]);
  assign or_104_out = or_105_out | {{2{or_314_out[2]}}, 1'b0};  // OR_Gate or_104, 3 bits wide
  assign or_105_out = or_108_out | {{2{or_316_out[2]}}, 1'b0};  // OR_Gate or_105, 3 bits wide
  or or_106 (or_106_out, or_107_out, d_ff_181_q[6]);
  or or_107 (or_107_out, or_110_out, d_ff_182_q[6]);
  assign or_108_out = or_109_out | {{2{or_317_out[2]}}, 1'b0};  // OR_Gate or_108, 3 bits wide
  assign or_109_out = or_111_out | {{2{or_318_out[2]}}, 1'b0};  // OR_Gate or_109, 3 bits wide
  or or_110 (or_110_out, or_112_out, or_278_out);
  assign or_111_out = or_113_out | {{2{or_319_out[2]}}, 1'b0};  // OR_Gate or_111, 3 bits wide
  or or_112 (or_112_out, or_114_out, d_ff_184_q[6]);
  assign or_113_out = or_115_out | {{2{or_322_out[2]}}, 1'b0};  // OR_Gate or_113, 3 bits wide
  or or_114 (or_114_out, or_116_out, d_ff_187_q[7]);
  assign or_115_out = or_117_out | {{2{or_327_out[2]}}, 1'b0};  // OR_Gate or_115, 3 bits wide
  or or_116 (or_116_out, or_118_out, d_ff_50_q);
  assign or_117_out = or_120_out | {{2{or_332_out[2]}}, 1'b0};  // OR_Gate or_117, 3 bits wide
  or or_118 (or_118_out, or_119_out, d_ff_54_q);
  or or_119 (or_119_out, or_121_out, or_286_out);
  assign or_120_out = or_122_out | {{2{or_334_out[2]}}, 1'b0};  // OR_Gate or_120, 3 bits wide
  or or_121 (or_121_out, or_124_out, or_287_out);
  assign or_122_out = or_123_out | {{2{or_335_out[2]}}, 1'b0};  // OR_Gate or_122, 3 bits wide
  assign or_123_out = or_125_out | {{2{or_337_out[2]}}, 1'b0};  // OR_Gate or_123, 3 bits wide
  or or_124 (or_124_out, or_126_out, or_336_out);
  assign or_125_out = or_127_out | {{2{or_338_out[2]}}, 1'b0};  // OR_Gate or_125, 3 bits wide
  or or_126 (or_126_out, or_128_out, or_288_out);
  assign or_127_out = or_129_out | {{2{or_341_out[2]}}, 1'b0};  // OR_Gate or_127, 3 bits wide
  or or_128 (or_128_out, or_130_out, d_ff_62_q);
  assign or_129_out = or_131_out | {{2{or_345_out[2]}}, 1'b0};  // OR_Gate or_129, 3 bits wide
  or or_130 (or_130_out, or_132_out, d_ff_65_q[0]);
  assign or_131_out = or_133_out | {{2{or_348_out[2]}}, 1'b0};  // OR_Gate or_131, 3 bits wide
  or or_132 (or_132_out, or_134_out, d_ff_68_q[0]);
  assign or_133_out = or_136_out | {{2{or_350_out[2]}}, 1'b0};  // OR_Gate or_133, 3 bits wide
  or or_134 (or_134_out, or_135_out, or_298_out);
  or or_135 (or_135_out, or_138_out, or_299_out);
  assign or_136_out = or_137_out | {{2{or_351_out[2]}}, 1'b0};  // OR_Gate or_136, 3 bits wide
  assign or_137_out = or_140_out | {{2{or_352_out[2]}}, 1'b0};  // OR_Gate or_137, 3 bits wide
  or or_138 (or_138_out, or_139_out, or_300_out);
  buf or_139 (or_139_out, d_ff_75_q[0]);  // OR_Gate
  assign or_140_out = {{2{or_355_out[2]}}, 1'b0};  // OR_Gate or_140, 3 bits wide OR_Gate
  assign or_141_out = or_142_out | {{2{d_ff_4_q[2]}}, 1'b0};  // OR_Gate or_141, 3 bits wide
  assign or_142_out = or_144_out | 3'b000;  // OR_Gate or_142, 3 bits wide
  or or_143 (or_143_out, or_145_out, d_ff_7_q[2]);
  assign or_144_out = or_146_out | 3'b000;  // OR_Gate or_144, 3 bits wide
  or or_145 (or_145_out, or_147_out, d_ff_8_q[2]);
  assign or_146_out = or_149_out | 3'b000;  // OR_Gate or_146, 3 bits wide
  or or_147 (or_147_out, or_148_out, d_ff_9_q[2]);
  or or_148 (or_148_out, or_151_out, d_ff_11_q[2]);
  assign or_149_out = or_150_out | {{2{d_ff_11_q[2]}}, 1'b0};  // OR_Gate or_149, 3 bits wide
  assign or_150_out = or_153_out | {{2{d_ff_14_q[2]}}, 1'b0};  // OR_Gate or_150, 3 bits wide
  or or_151 (or_151_out, or_152_out, d_ff_14_q[2]);
  or or_152 (or_152_out, or_154_out, d_ff_17_q[2]);
  assign or_153_out = or_155_out | {{2{d_ff_17_q[2]}}, 1'b0};  // OR_Gate or_153, 3 bits wide
  or or_154 (or_154_out, or_157_out, d_ff_161_q[7]);
  assign or_155_out = or_156_out | {{2{d_ff_20_q[2]}}, 1'b0};  // OR_Gate or_155, 3 bits wide
  assign or_156_out = or_158_out | {{2{d_ff_21_q[2]}}, 1'b0};  // OR_Gate or_156, 3 bits wide
  or or_157 (or_157_out, or_159_out, or_273_out);
  assign or_158_out = or_160_out | {{2{d_ff_22_q[2]}}, 1'b0};  // OR_Gate or_158, 3 bits wide
  or or_159 (or_159_out, or_161_out, d_ff_163_q[7]);
  assign or_160_out = or_163_out | {{2{d_ff_23_q[2]}}, 1'b0};  // OR_Gate or_160, 3 bits wide
  or or_161 (or_161_out, or_162_out, d_ff_164_q[7]);
  or or_162 (or_162_out, or_165_out, d_ff_25_q[2]);
  assign or_163_out = or_164_out | {{2{d_ff_25_q[2]}}, 1'b0};  // OR_Gate or_163, 3 bits wide
  assign or_164_out = or_167_out | {{2{d_ff_29_q[2]}}, 1'b0};  // OR_Gate or_164, 3 bits wide
  or or_165 (or_165_out, or_166_out, d_ff_29_q[2]);
  or or_166 (or_166_out, or_169_out, d_ff_174_q[7]);
  assign or_167_out = or_168_out | {{2{or_309_out[2]}}, 1'b0};  // OR_Gate or_167, 3 bits wide
  assign or_168_out = or_170_out | {{2{or_312_out[2]}}, 1'b0};  // OR_Gate or_168, 3 bits wide
  or or_169 (or_169_out, or_171_out, d_ff_177_q[6]);
  assign or_170_out = or_173_out | {{2{or_313_out[2]}}, 1'b0};  // OR_Gate or_170, 3 bits wide
  or or_171 (or_171_out, or_172_out, or_277_out);
  or or_172 (or_172_out, or_174_out, d_ff_179_q[6]);
  assign or_173_out = or_175_out | {{2{or_314_out[2]}}, 1'b0};  // OR_Gate or_173, 3 bits wide
  or or_174 (or_174_out, or_176_out, d_ff_180_q[6]);
  assign or_175_out = or_177_out | {{2{or_315_out[2]}}, 1'b0};  // OR_Gate or_175, 3 bits wide
  or or_176 (or_176_out, or_178_out, d_ff_182_q[7]);
  assign or_177_out = or_179_out | {{2{or_317_out[2]}}, 1'b0};  // OR_Gate or_177, 3 bits wide
  or or_178 (or_178_out, or_180_out, d_ff_186_q[7]);
  assign or_179_out = or_181_out | {{2{or_321_out[2]}}, 1'b0};  // OR_Gate or_179, 3 bits wide
  or or_180 (or_180_out, or_182_out, d_ff_49_q);
  assign or_181_out = or_183_out | {{2{or_326_out[2]}}, 1'b0};  // OR_Gate or_181, 3 bits wide
  or or_182 (or_182_out, or_185_out, or_283_out);
  assign or_183_out = or_184_out | {{2{or_329_out[2]}}, 1'b0};  // OR_Gate or_183, 3 bits wide
  assign or_184_out = or_187_out | {{2{or_331_out[2]}}, 1'b0};  // OR_Gate or_184, 3 bits wide
  or or_185 (or_185_out, or_186_out, or_330_out);
  or or_186 (or_186_out, or_188_out, or_284_out);
  assign or_187_out = or_189_out | {{2{or_332_out[2]}}, 1'b0};  // OR_Gate or_187, 3 bits wide
  or or_188 (or_188_out, or_191_out, or_285_out);
  assign or_189_out = or_190_out | {{2{or_333_out[2]}}, 1'b0};  // OR_Gate or_189, 3 bits wide
  assign or_190_out = or_192_out | {{2{or_335_out[2]}}, 1'b0};  // OR_Gate or_190, 3 bits wide
  or or_191 (or_191_out, or_193_out, d_ff_57_q);
  assign or_192_out = or_194_out | {{2{or_340_out[2]}}, 1'b0};  // OR_Gate or_192, 3 bits wide
  or or_193 (or_193_out, or_195_out, d_ff_61_q);
  assign or_194_out = or_196_out | {{2{or_344_out[2]}}, 1'b0};  // OR_Gate or_194, 3 bits wide
  or or_195 (or_195_out, or_197_out, d_ff_64_q[0]);
  assign or_196_out = or_198_out | {{2{or_347_out[2]}}, 1'b0};  // OR_Gate or_196, 3 bits wide
  or or_197 (or_197_out, or_199_out, or_295_out);
  assign or_198_out = or_200_out | {{2{or_348_out[2]}}, 1'b0};  // OR_Gate or_198, 3 bits wide
  or or_199 (or_199_out, or_201_out, or_296_out);
  assign or_200_out = or_203_out | {{2{or_349_out[2]}}, 1'b0};  // OR_Gate or_200, 3 bits wide
  or or_201 (or_201_out, or_202_out, or_297_out);
  or or_202 (or_202_out, or_204_out, d_ff_71_q[0]);
  assign or_203_out = or_205_out | {{2{or_351_out[2]}}, 1'b0};  // OR_Gate or_203, 3 bits wide
  buf or_204 (or_204_out, d_ff_74_q[0]);  // OR_Gate
  assign or_205_out = {{2{or_354_out[2]}}, 1'b0};  // OR_Gate or_205, 3 bits wide OR_Gate
  assign or_206_out = or_209_out | 3'b000;  // OR_Gate or_206, 3 bits wide
  or or_207 (or_207_out, or_143_out, d_ff_4_q[2]);
  or or_208 (or_208_out, or_210_out, d_ff_5_q[2]);
  assign or_209_out = or_211_out | 3'b000;  // OR_Gate or_209, 3 bits wide
  or or_210 (or_210_out, or_212_out, d_ff_6_q[2]);
  assign or_211_out = or_213_out | 3'b000;  // OR_Gate or_211, 3 bits wide
  or or_212 (or_212_out, or_214_out, d_ff_7_q[2]);
  assign or_213_out = or_215_out | {{2{d_ff_7_q[2]}}, 1'b0};  // OR_Gate or_213, 3 bits wide
  or or_214 (or_214_out, or_217_out, d_ff_10_q[2]);
  assign or_215_out = or_216_out | {{2{d_ff_10_q[2]}}, 1'b0};  // OR_Gate or_215, 3 bits wide
  assign or_216_out = or_219_out | {{2{d_ff_13_q[2]}}, 1'b0};  // OR_Gate or_216, 3 bits wide
  or or_217 (or_217_out, or_218_out, d_ff_13_q[2]);
  or or_218 (or_218_out, or_221_out, or_307_out);
  assign or_219_out = or_220_out | {{2{d_ff_16_q[2]}}, 1'b0};  // OR_Gate or_219, 3 bits wide
  assign or_220_out = or_222_out | {{2{d_ff_17_q[2]}}, 1'b0};  // OR_Gate or_220, 3 bits wide
  or or_221 (or_221_out, or_223_out, d_ff_158_q[7]);
  assign or_222_out = or_225_out | {{2{d_ff_18_q[2]}}, 1'b0};  // OR_Gate or_222, 3 bits wide
  or or_223 (or_223_out, or_224_out, d_ff_159_q[7]);
  or or_224 (or_224_out, or_227_out, d_ff_160_q[7]);
  assign or_225_out = or_226_out | {{2{d_ff_19_q[2]}}, 1'b0};  // OR_Gate or_225, 3 bits wide
  assign or_226_out = or_229_out | {{2{d_ff_20_q[2]}}, 1'b0};  // OR_Gate or_226, 3 bits wide
  or or_227 (or_227_out, or_228_out, d_ff_20_q[2]);
  or or_228 (or_228_out, or_230_out, d_ff_24_q[2]);
  assign or_229_out = or_231_out | {{2{d_ff_24_q[2]}}, 1'b0};  // OR_Gate or_229, 3 bits wide
  or or_230 (or_230_out, or_233_out, d_ff_28_q[2]);
  assign or_231_out = or_232_out | {{2{d_ff_28_q[2]}}, 1'b0};  // OR_Gate or_231, 3 bits wide
  assign or_232_out = or_235_out | {{2{or_308_out[2]}}, 1'b0};  // OR_Gate or_232, 3 bits wide
  or or_233 (or_233_out, or_234_out, or_276_out);
  or or_234 (or_234_out, or_237_out, d_ff_174_q[6]);
  assign or_235_out = or_236_out | {{2{or_309_out[2]}}, 1'b0};  // OR_Gate or_235, 3 bits wide
  assign or_236_out = or_239_out | {{2{or_310_out[2]}}, 1'b0};  // OR_Gate or_236, 3 bits wide
  or or_237 (or_237_out, or_238_out, d_ff_175_q[6]);
  or or_238 (or_238_out, or_240_out, d_ff_176_q[6]);
  assign or_239_out = or_241_out | {{2{or_311_out[2]}}, 1'b0};  // OR_Gate or_239, 3 bits wide
  or or_240 (or_240_out, or_243_out, d_ff_177_q[7]);
  assign or_241_out = or_242_out | {{2{or_312_out[2]}}, 1'b0};  // OR_Gate or_241, 3 bits wide
  assign or_242_out = or_244_out | {{2{or_316_out[2]}}, 1'b0};  // OR_Gate or_242, 3 bits wide
  or or_243 (or_243_out, or_245_out, d_ff_181_q[7]);
  assign or_244_out = or_247_out | {{2{or_320_out[2]}}, 1'b0};  // OR_Gate or_244, 3 bits wide
  or or_245 (or_245_out, or_246_out, d_ff_185_q[7]);
  or or_246 (or_246_out, or_248_out, or_324_out);
  assign or_247_out = or_249_out | {{2{or_325_out[2]}}, 1'b0};  // OR_Gate or_247, 3 bits wide
  or or_248 (or_248_out, or_251_out, or_280_out);
  assign or_249_out = or_250_out | {{2{or_326_out[2]}}, 1'b0};  // OR_Gate or_249, 3 bits wide
  assign or_250_out = or_252_out | {{2{or_327_out[2]}}, 1'b0};  // OR_Gate or_250, 3 bits wide
  or or_251 (or_251_out, or_253_out, or_281_out);
  assign or_252_out = or_254_out | {{2{or_328_out[2]}}, 1'b0};  // OR_Gate or_252, 3 bits wide
  or or_253 (or_253_out, or_255_out, or_282_out);
  assign or_254_out = or_257_out | {{2{or_329_out[2]}}, 1'b0};  // OR_Gate or_254, 3 bits wide
  or or_255 (or_255_out, or_256_out, d_ff_52_q);
  or or_256 (or_256_out, or_259_out, d_ff_56_q);
  assign or_257_out = or_258_out | {{2{or_334_out[2]}}, 1'b0};  // OR_Gate or_257, 3 bits wide
  assign or_258_out = or_261_out | {{2{or_339_out[2]}}, 1'b0};  // OR_Gate or_258, 3 bits wide
  or or_259 (or_259_out, or_260_out, d_ff_60_q);
  or or_260 (or_260_out, or_263_out, or_292_out);
  assign or_261_out = or_262_out | {{2{or_344_out[2]}}, 1'b0};  // OR_Gate or_261, 3 bits wide
  assign or_262_out = or_265_out | {{2{or_345_out[2]}}, 1'b0};  // OR_Gate or_262, 3 bits wide
  or or_263 (or_263_out, or_264_out, or_293_out);
  or or_264 (or_264_out, or_266_out, or_294_out);
  assign or_265_out = or_267_out | {{2{or_346_out[2]}}, 1'b0};  // OR_Gate or_265, 3 bits wide
  or or_266 (or_266_out, or_269_out, d_ff_67_q[0]);
  assign or_267_out = or_268_out | {{2{or_347_out[2]}}, 1'b0};  // OR_Gate or_267, 3 bits wide
  assign or_268_out = or_271_out | {{2{or_350_out[2]}}, 1'b0};  // OR_Gate or_268, 3 bits wide
  or or_269 (or_269_out, or_270_out, d_ff_70_q[0]);
  buf or_270 (or_270_out, d_ff_73_q[0]);  // OR_Gate
  assign or_271_out = {{2{or_353_out[2]}}, 1'b0};  // OR_Gate or_271, 3 bits wide OR_Gate
  or or_272 (or_272_out, or_208_out, d_ff_4_q[2]);
  or or_273 (or_273_out, d_ff_21_q[2], d_ff_162_q[7]);
  or or_274 (or_274_out, d_ff_26_q[2], d_ff_167_q[7]);
  or or_275 (or_275_out, d_ff_31_q[2], d_ff_172_q[7]);
  or or_276 (or_276_out, d_ff_173_q[7], or_308_out[2]);
  or or_277 (or_277_out, d_ff_178_q[7], or_313_out[2]);
  or or_278 (or_278_out, d_ff_183_q[7], or_318_out[2]);
  or or_279 (or_279_out, d_ff_188_q[7], or_323_out[2]);
  or or_280 (or_280_out, d_ff_125_q[2], d_ff_125_q[0]);
  or or_281 (or_281_out, d_ff_126_q[2], d_ff_126_q[0]);
  or or_282 (or_282_out, d_ff_127_q[2], d_ff_127_q[0]);
  or or_283 (or_283_out, d_ff_128_q[2], d_ff_128_q[0]);
  or or_284 (or_284_out, d_ff_130_q[2], d_ff_130_q[0]);
  or or_285 (or_285_out, d_ff_131_q[2], d_ff_131_q[0]);
  or or_286 (or_286_out, d_ff_132_q[2], d_ff_132_q[0]);
  or or_287 (or_287_out, d_ff_133_q[2], d_ff_133_q[0]);
  or or_288 (or_288_out, d_ff_135_q[2], d_ff_135_q[0]);
  or or_289 (or_289_out, d_ff_136_q[2], d_ff_136_q[0]);
  or or_290 (or_290_out, d_ff_137_q[2], d_ff_137_q[0]);
  or or_291 (or_291_out, d_ff_138_q[2], d_ff_138_q[0]);
  or or_292 (or_292_out, d_ff_64_q[2], d_ff_140_q);
  or or_293 (or_293_out, d_ff_65_q[2], d_ff_141_q);
  or or_294 (or_294_out, d_ff_66_q[2], d_ff_142_q);
  or or_295 (or_295_out, d_ff_67_q[2], d_ff_143_q);
  or or_296 (or_296_out, d_ff_68_q[2], d_ff_144_q);
  or or_297 (or_297_out, d_ff_69_q[2], d_ff_145_q);
  or or_298 (or_298_out, d_ff_70_q[2], d_ff_146_q);
  or or_299 (or_299_out, d_ff_71_q[2], d_ff_147_q);
  or or_300 (or_300_out, d_ff_72_q[2], d_ff_148_q);
  or or_301 (or_301_out, d_ff_73_q[2], d_ff_149_q);
  or or_302 (or_302_out, d_ff_74_q[2], d_ff_150_q);
  or or_303 (or_303_out, d_ff_75_q[2], d_ff_151_q);
  or or_304 (d_ff_153_q[5], d_ff_76_q, d_ff_152_q);
  D_Flip_Flop d_ff_1 (.clk(CLK), .D(mov_bx_value16_out), .Q(d_ff_1_q), .Qn(d_ff_1_qn));  // open: preset, en, reset
  or or_305 (d_ff_77_q[5], d_ff_1_q, d_ff_154_q);
  D_Flip_Flop d_ff_2 (.clk(CLK), .D(mov_cx_value16_out), .Q(d_ff_2_q), .Qn(d_ff_2_qn));  // open: preset, en, reset
  or or_306 (d_ff_79_q[5], d_ff_156_q, d_ff_3_q);
  D_Flip_Flop d_ff_3 (.clk(CLK), .D(mov_dx_value16_out), .Q(d_ff_3_q), .Qn(d_ff_3_qn));  // open: preset, en, reset
  D_Flip_Flop d_ff_4 (.clk(CLK), .D(mov_ax_bx_out), .Q(d_ff_4_q[2]), .Qn(d_ff_4_qn));  // open: preset, en, reset
  D_Flip_Flop d_ff_5 (.clk(CLK), .D(mov_ax_cx_out), .Q(d_ff_5_q[2]), .Qn(d_ff_5_qn));  // open: preset, en, reset
  D_Flip_Flop d_ff_6 (.clk(CLK), .D(mov_ax_dx_out), .Q(d_ff_6_q[2]), .Qn(d_ff_6_qn));  // open: preset, en, reset
  D_Flip_Flop d_ff_7 (.clk(CLK), .D(mov_bx_ax_out), .Q(d_ff_7_q[2]), .Qn(d_ff_7_qn));  // open: preset, en, reset
  D_Flip_Flop d_ff_8 (.clk(CLK), .D(mov_bx_cx_out), .Q(d_ff_8_q[2]), .Qn(d_ff_8_qn));  // open: preset, en, reset
  D_Flip_Flop d_ff_9 (.clk(CLK), .D(mov_bx_dx_out), .Q(d_ff_9_q[2]), .Qn(d_ff_9_qn));  // open: preset, en, reset
  D_Flip_Flop d_ff_10 (.clk(CLK), .D(mov_cx_ax_out), .Q(d_ff_10_q[2]), .Qn(d_ff_10_qn));  // open: preset, en, reset
  D_Flip_Flop d_ff_11 (.clk(CLK), .D(mov_cx_bx_out), .Q(d_ff_11_q[2]), .Qn(d_ff_11_qn));  // open: preset, en, reset
  D_Flip_Flop d_ff_12 (.clk(CLK), .D(mov_cx_dx_out), .Q(d_ff_12_q[2]), .Qn(d_ff_12_qn));  // open: preset, en, reset
  D_Flip_Flop d_ff_13 (.clk(CLK), .D(mov_dx_ax_out), .Q(d_ff_13_q[2]), .Qn(d_ff_13_qn));  // open: preset, en, reset
  D_Flip_Flop d_ff_14 (.clk(CLK), .D(mov_dx_bx_out), .Q(d_ff_14_q[2]), .Qn(d_ff_14_qn));  // open: preset, en, reset
  D_Flip_Flop d_ff_15 (.clk(CLK), .D(mov_dx_cx_out), .Q(d_ff_15_q[2]), .Qn(d_ff_15_qn));  // open: preset, en, reset
  or or_307 (or_307_out, d_ff_16_q[2], d_ff_157_q[7]);
  D_Flip_Flop d_ff_16 (.clk(CLK), .D(mov_ax__ax_out), .Q(d_ff_16_q[2]), .Qn(d_ff_16_qn));  // open: preset, en, reset
  D_Flip_Flop d_ff_17 (.clk(CLK), .D(mov_ax__bx_out), .Q(d_ff_17_q[2]), .Qn(d_ff_17_qn));  // open: preset, en, reset
  D_Flip_Flop d_ff_18 (.clk(CLK), .D(mov_ax__cx_out), .Q(d_ff_18_q[2]), .Qn(d_ff_18_qn));  // open: preset, en, reset
  D_Flip_Flop d_ff_19 (.clk(CLK), .D(mov_ax__dx_out), .Q(d_ff_19_q[2]), .Qn(d_ff_19_qn));  // open: preset, en, reset
  D_Flip_Flop d_ff_20 (.clk(CLK), .D(mov_bx__ax_out), .Q(d_ff_20_q[2]), .Qn(d_ff_20_qn));  // open: preset, en, reset
  D_Flip_Flop d_ff_21 (.clk(CLK), .D(mov_bx__bx_out), .Q(d_ff_21_q[2]), .Qn(d_ff_21_qn));  // open: preset, en, reset
  D_Flip_Flop d_ff_22 (.clk(CLK), .D(mov_bx__cx_out), .Q(d_ff_22_q[2]), .Qn(d_ff_22_qn));  // open: preset, en, reset
  D_Flip_Flop d_ff_23 (.clk(CLK), .D(mov_bx__dx_out), .Q(d_ff_23_q[2]), .Qn(d_ff_23_qn));  // open: preset, en, reset
  D_Flip_Flop d_ff_24 (.clk(CLK), .D(mov_cx__ax_out), .Q(d_ff_24_q[2]), .Qn(d_ff_24_qn));  // open: preset, en, reset
  D_Flip_Flop d_ff_25 (.clk(CLK), .D(mov_cx__bx_out), .Q(d_ff_25_q[2]), .Qn(d_ff_25_qn));  // open: preset, en, reset
  D_Flip_Flop d_ff_26 (.clk(CLK), .D(mov_cx__cx_out), .Q(d_ff_26_q[2]), .Qn(d_ff_26_qn));  // open: preset, en, reset
  D_Flip_Flop d_ff_27 (.clk(CLK), .D(mov_cx__dx_out), .Q(d_ff_27_q[2]), .Qn(d_ff_27_qn));  // open: preset, en, reset
  D_Flip_Flop d_ff_28 (.clk(CLK), .D(mov_dx__ax_out), .Q(d_ff_28_q[2]), .Qn(d_ff_28_qn));  // open: preset, en, reset
  D_Flip_Flop d_ff_29 (.clk(CLK), .D(mov_dx__bx_out), .Q(d_ff_29_q[2]), .Qn(d_ff_29_qn));  // open: preset, en, reset
  D_Flip_Flop d_ff_30 (.clk(CLK), .D(mov_dx__cx_out), .Q(d_ff_30_q[2]), .Qn(d_ff_30_qn));  // open: preset, en, reset
  D_Flip_Flop d_ff_31 (.clk(CLK), .D(mov_dx__dx_out), .Q(d_ff_31_q[2]), .Qn(d_ff_31_qn));  // open: preset, en, reset
  or or_308 (or_308_out[2], d_ff_173_q[6], d_ff_173_q[7]);
  D_Flip_Flop d_ff_32 (.clk(CLK), .D(mov__ax__ax_out), .Q(d_ff_173_q[6]), .Qn(d_ff_32_qn));  // open: preset, en, reset
  or or_309 (or_309_out[2], d_ff_174_q[7], d_ff_174_q[6]);
  D_Flip_Flop d_ff_33 (.clk(CLK), .D(mov__ax__bx_out), .Q(d_ff_174_q[6]), .Qn(d_ff_33_qn));  // open: preset, en, reset
  or or_310 (or_310_out[2], d_ff_175_q[7], d_ff_175_q[6]);
  D_Flip_Flop d_ff_34 (.clk(CLK), .D(mov__ax__cx_out), .Q(d_ff_175_q[6]), .Qn(d_ff_34_qn));  // open: preset, en, reset
  or or_311 (or_311_out[2], d_ff_176_q[7], d_ff_176_q[6]);
  D_Flip_Flop d_ff_35 (.clk(CLK), .D(mov__ax__dx_out), .Q(d_ff_176_q[6]), .Qn(d_ff_35_qn));  // open: preset, en, reset
  or or_312 (or_312_out[2], d_ff_177_q[7], d_ff_177_q[6]);
  D_Flip_Flop d_ff_36 (.clk(CLK), .D(mov__bx__ax_out), .Q(d_ff_177_q[6]), .Qn(d_ff_36_qn));  // open: preset, en, reset
  or or_313 (or_313_out[2], d_ff_178_q[6], d_ff_178_q[7]);
  D_Flip_Flop d_ff_37 (.clk(CLK), .D(mov__bx__bx_out), .Q(d_ff_178_q[6]), .Qn(d_ff_37_qn));  // open: preset, en, reset
  or or_314 (or_314_out[2], d_ff_179_q[7], d_ff_179_q[6]);
  D_Flip_Flop d_ff_38 (.clk(CLK), .D(mov__bx__cx_out), .Q(d_ff_179_q[6]), .Qn(d_ff_38_qn));  // open: preset, en, reset
  or or_315 (or_315_out[2], d_ff_180_q[7], d_ff_180_q[6]);
  D_Flip_Flop d_ff_39 (.clk(CLK), .D(mov__bx__dx_out), .Q(d_ff_180_q[6]), .Qn(d_ff_39_qn));  // open: preset, en, reset
  or or_316 (or_316_out[2], d_ff_181_q[7], d_ff_181_q[6]);
  D_Flip_Flop d_ff_40 (.clk(CLK), .D(mov__cx__ax_out), .Q(d_ff_181_q[6]), .Qn(d_ff_40_qn));  // open: preset, en, reset
  or or_317 (or_317_out[2], d_ff_182_q[7], d_ff_182_q[6]);
  D_Flip_Flop d_ff_41 (.clk(CLK), .D(mov__cx__bx_out), .Q(d_ff_182_q[6]), .Qn(d_ff_41_qn));  // open: preset, en, reset
  or or_318 (or_318_out[2], d_ff_183_q[6], d_ff_183_q[7]);
  D_Flip_Flop d_ff_42 (.clk(CLK), .D(mov__cx__cx_out), .Q(d_ff_183_q[6]), .Qn(d_ff_42_qn));  // open: preset, en, reset
  or or_319 (or_319_out[2], d_ff_184_q[7], d_ff_184_q[6]);
  D_Flip_Flop d_ff_43 (.clk(CLK), .D(mov__cx__dx_out), .Q(d_ff_184_q[6]), .Qn(d_ff_43_qn));  // open: preset, en, reset
  or or_320 (or_320_out[2], d_ff_185_q[7], d_ff_185_q[6]);
  D_Flip_Flop d_ff_44 (.clk(CLK), .D(mov__dx__ax_out), .Q(d_ff_185_q[6]), .Qn(d_ff_44_qn));  // open: preset, en, reset
  or or_321 (or_321_out[2], d_ff_186_q[7], d_ff_186_q[6]);
  D_Flip_Flop d_ff_45 (.clk(CLK), .D(mov__dx__bx_out), .Q(d_ff_186_q[6]), .Qn(d_ff_45_qn));  // open: preset, en, reset
  or or_322 (or_322_out[2], d_ff_187_q[7], d_ff_187_q[6]);
  D_Flip_Flop d_ff_46 (.clk(CLK), .D(mov__dx__cx_out), .Q(d_ff_187_q[6]), .Qn(d_ff_46_qn));  // open: preset, en, reset
  or or_323 (or_323_out[2], d_ff_188_q[6], d_ff_188_q[7]);
  D_Flip_Flop d_ff_47 (.clk(CLK), .D(mov__dx__dx_out), .Q(d_ff_188_q[6]), .Qn(d_ff_47_qn));  // open: preset, en, reset
  or or_324 (or_324_out, d_ff_124_q[0], d_ff_48_q, d_ff_124_q[2]);
  or or_325 (or_325_out[2], d_ff_124_q[0], d_ff_48_q);
  D_Flip_Flop d_ff_48 (.clk(CLK), .D(add_ax_ax_out), .Q(d_ff_48_q), .Qn(d_ff_48_qn));  // open: preset, en, reset
  or or_326 (or_326_out[2], d_ff_125_q[0], d_ff_49_q);
  D_Flip_Flop d_ff_49 (.clk(CLK), .D(add_ax_bx_out), .Q(d_ff_49_q), .Qn(d_ff_49_qn));  // open: preset, en, reset
  or or_327 (or_327_out[2], d_ff_126_q[0], d_ff_50_q);
  D_Flip_Flop d_ff_50 (.clk(CLK), .D(add_ax_cx_out), .Q(d_ff_50_q), .Qn(d_ff_50_qn));  // open: preset, en, reset
  or or_328 (or_328_out[2], d_ff_127_q[0], d_ff_51_q);
  D_Flip_Flop d_ff_51 (.clk(CLK), .D(add_ax_dx_out), .Q(d_ff_51_q), .Qn(d_ff_51_qn));  // open: preset, en, reset
  or or_329 (or_329_out[2], d_ff_128_q[0], d_ff_52_q);
  D_Flip_Flop d_ff_52 (.clk(CLK), .D(add_bx_ax_out), .Q(d_ff_52_q), .Qn(d_ff_52_qn));  // open: preset, en, reset
  or or_330 (or_330_out, d_ff_129_q[0], d_ff_53_q, d_ff_129_q[2]);
  or or_331 (or_331_out[2], d_ff_129_q[0], d_ff_53_q);
  D_Flip_Flop d_ff_53 (.clk(CLK), .D(add_bx_bx_out), .Q(d_ff_53_q), .Qn(d_ff_53_qn));  // open: preset, en, reset
  or or_332 (or_332_out[2], d_ff_130_q[0], d_ff_54_q);
  D_Flip_Flop d_ff_54 (.clk(CLK), .D(add_bx_cx_out), .Q(d_ff_54_q), .Qn(d_ff_54_qn));  // open: preset, en, reset
  or or_333 (or_333_out[2], d_ff_131_q[0], d_ff_55_q);
  D_Flip_Flop d_ff_55 (.clk(CLK), .D(add_bx_dx_out), .Q(d_ff_55_q), .Qn(d_ff_55_qn));  // open: preset, en, reset
  or or_334 (or_334_out[2], d_ff_132_q[0], d_ff_56_q);
  D_Flip_Flop d_ff_56 (.clk(CLK), .D(add_cx_ax_out), .Q(d_ff_56_q), .Qn(d_ff_56_qn));  // open: preset, en, reset
  or or_335 (or_335_out[2], d_ff_133_q[0], d_ff_57_q);
  D_Flip_Flop d_ff_57 (.clk(CLK), .D(add_cx_bx_out), .Q(d_ff_57_q), .Qn(d_ff_57_qn));  // open: preset, en, reset
  or or_336 (or_336_out, d_ff_134_q[0], d_ff_58_q, d_ff_134_q[2]);
  or or_337 (or_337_out[2], d_ff_134_q[0], d_ff_58_q);
  D_Flip_Flop d_ff_58 (.clk(CLK), .D(add_cx_cx_out), .Q(d_ff_58_q), .Qn(d_ff_58_qn));  // open: preset, en, reset
  or or_338 (or_338_out[2], d_ff_135_q[0], d_ff_59_q);
  D_Flip_Flop d_ff_59 (.clk(CLK), .D(add_cx_dx_out), .Q(d_ff_59_q), .Qn(d_ff_59_qn));  // open: preset, en, reset
  or or_339 (or_339_out[2], d_ff_136_q[0], d_ff_60_q);
  D_Flip_Flop d_ff_60 (.clk(CLK), .D(add_dx_ax_out), .Q(d_ff_60_q), .Qn(d_ff_60_qn));  // open: preset, en, reset
  or or_340 (or_340_out[2], d_ff_137_q[0], d_ff_61_q);
  D_Flip_Flop d_ff_61 (.clk(CLK), .D(add_dx_bx_out), .Q(d_ff_61_q), .Qn(d_ff_61_qn));  // open: preset, en, reset
  or or_341 (or_341_out[2], d_ff_138_q[0], d_ff_62_q);
  D_Flip_Flop d_ff_62 (.clk(CLK), .D(add_dx_cx_out), .Q(d_ff_62_q), .Qn(d_ff_62_qn));  // open: preset, en, reset
  or or_342 (or_342_out, d_ff_139_q[0], d_ff_63_q, d_ff_139_q[2]);
  or or_343 (or_343_out[2], d_ff_139_q[0], d_ff_63_q);
  D_Flip_Flop d_ff_63 (.clk(CLK), .D(add_dx_dx_out), .Q(d_ff_63_q), .Qn(d_ff_63_qn));  // open: preset, en, reset
  or or_344 (or_344_out[2], d_ff_140_q, d_ff_64_q[0]);
  D_Flip_Flop d_ff_64 (.clk(CLK), .D(sub_ax_bx_out), .Q(d_ff_64_q[0]), .Qn(d_ff_64_qn));  // open: preset, en, reset
  or or_345 (or_345_out[2], d_ff_141_q, d_ff_65_q[0]);
  D_Flip_Flop d_ff_65 (.clk(CLK), .D(sub_ax_cx_out), .Q(d_ff_65_q[0]), .Qn(d_ff_65_qn));  // open: preset, en, reset
  or or_346 (or_346_out[2], d_ff_142_q, d_ff_66_q[0]);
  D_Flip_Flop d_ff_66 (.clk(CLK), .D(sub_ax_dx_out), .Q(d_ff_66_q[0]), .Qn(d_ff_66_qn));  // open: preset, en, reset
  or or_347 (or_347_out[2], d_ff_143_q, d_ff_67_q[0]);
  D_Flip_Flop d_ff_67 (.clk(CLK), .D(sub_bx_ax_out), .Q(d_ff_67_q[0]), .Qn(d_ff_67_qn));  // open: preset, en, reset
  or or_348 (or_348_out[2], d_ff_144_q, d_ff_68_q[0]);
  D_Flip_Flop d_ff_68 (.clk(CLK), .D(sub_bx_cx_out), .Q(d_ff_68_q[0]), .Qn(d_ff_68_qn));  // open: preset, en, reset
  or or_349 (or_349_out[2], d_ff_145_q, d_ff_69_q[0]);
  D_Flip_Flop d_ff_69 (.clk(CLK), .D(sub_bx_dx_out), .Q(d_ff_69_q[0]), .Qn(d_ff_69_qn));  // open: preset, en, reset
  or or_350 (or_350_out[2], d_ff_146_q, d_ff_70_q[0]);
  D_Flip_Flop d_ff_70 (.clk(CLK), .D(sub_cx_ax_out), .Q(d_ff_70_q[0]), .Qn(d_ff_70_qn));  // open: preset, en, reset
  or or_351 (or_351_out[2], d_ff_147_q, d_ff_71_q[0]);
  D_Flip_Flop d_ff_71 (.clk(CLK), .D(sub_cx_bx_out), .Q(d_ff_71_q[0]), .Qn(d_ff_71_qn));  // open: preset, en, reset
  or or_352 (or_352_out[2], d_ff_148_q, d_ff_72_q[0]);
  D_Flip_Flop d_ff_72 (.clk(CLK), .D(sub_cx_dx_out), .Q(d_ff_72_q[0]), .Qn(d_ff_72_qn));  // open: preset, en, reset
  or or_353 (or_353_out[2], d_ff_149_q, d_ff_73_q[0]);
  D_Flip_Flop d_ff_73 (.clk(CLK), .D(sub_dx_ax_out), .Q(d_ff_73_q[0]), .Qn(d_ff_73_qn));  // open: preset, en, reset
  or or_354 (or_354_out[2], d_ff_150_q, d_ff_74_q[0]);
  D_Flip_Flop d_ff_74 (.clk(CLK), .D(sub_dx_bx_out), .Q(d_ff_74_q[0]), .Qn(d_ff_74_qn));  // open: preset, en, reset
  or or_355 (or_355_out[2], d_ff_151_q, d_ff_75_q[0]);
  D_Flip_Flop d_ff_75 (.clk(CLK), .D(sub_dx_cx_out), .Q(d_ff_75_q[0]), .Qn(d_ff_75_qn));  // open: preset, en, reset
  Command_Unit_CMP_Instruction command_unit_cmp_instruction_1 (
    .Enable(cmp_ax_bx_out), .CLK(CLK),
    .Running_Instruction(command_unit_cmp_instruction_1_running_instruction),
    .RAM_Enable(command_unit_cmp_instruction_1_ram_enable),
    .RAM_Instruction(command_unit_cmp_instruction_1_ram_instruction));  // open: Comparison_Enable, Comparison_Instruction, Base_Register_Enable, Base_Register_Instruction, Other_Register_Enable, Other_Register_Instruction
  D_Flip_Flop d_ff_76 (.clk(CLK), .D(mov_ax_value16_out), .Q(d_ff_76_q), .Qn(d_ff_76_qn));  // open: preset, en, reset
  D_Flip_Flop d_ff_77 (.clk(CLK), .D(d_ff_1_q), .Q(d_ff_77_q[4]), .Qn(d_ff_77_qn));  // open: preset, en, reset
  or or_356 (d_ff_78_q[5], d_ff_155_q, d_ff_2_q);
  D_Flip_Flop d_ff_78 (.clk(CLK), .D(d_ff_2_q), .Q(d_ff_78_q[4]), .Qn(d_ff_78_qn));  // open: preset, en, reset
  D_Flip_Flop d_ff_79 (.clk(CLK), .D(d_ff_3_q), .Q(d_ff_79_q[4]), .Qn(d_ff_79_qn));  // open: preset, en, reset
  assign or_357_out = {2'b00, d_ff_80_q[5], {5{1'b0}}} | or_358_out;  // OR_Gate or_357, 8 bits wide
  D_Flip_Flop d_ff_80 (.clk(CLK), .D(d_ff_4_q[2]), .Q(d_ff_80_q[5]), .Qn(d_ff_80_qn));  // open: preset, en, reset
  assign or_358_out = {2'b00, d_ff_81_q[5], {5{1'b0}}} | or_359_out;  // OR_Gate or_358, 8 bits wide
  D_Flip_Flop d_ff_81 (.clk(CLK), .D(d_ff_5_q[2]), .Q(d_ff_81_q[5]), .Qn(d_ff_81_qn));  // open: preset, en, reset
  assign or_359_out = {2'b00, d_ff_82_q[5], {5{1'b0}}} | or_360_out;  // OR_Gate or_359, 8 bits wide
  D_Flip_Flop d_ff_82 (.clk(CLK), .D(d_ff_6_q[2]), .Q(d_ff_82_q[5]), .Qn(d_ff_82_qn));  // open: preset, en, reset
  assign or_360_out = {2'b00, d_ff_83_q[5], {5{1'b0}}} | or_361_out;  // OR_Gate or_360, 8 bits wide
  D_Flip_Flop d_ff_83 (.clk(CLK), .D(d_ff_7_q[2]), .Q(d_ff_83_q[5]), .Qn(d_ff_83_qn));  // open: preset, en, reset
  assign or_361_out = {2'b00, d_ff_84_q[5], {5{1'b0}}} | or_362_out;  // OR_Gate or_361, 8 bits wide
  D_Flip_Flop d_ff_84 (.clk(CLK), .D(d_ff_8_q[2]), .Q(d_ff_84_q[5]), .Qn(d_ff_84_qn));  // open: preset, en, reset
  assign or_362_out = {2'b00, d_ff_85_q[5], {5{1'b0}}} | or_363_out;  // OR_Gate or_362, 8 bits wide
  D_Flip_Flop d_ff_85 (.clk(CLK), .D(d_ff_9_q[2]), .Q(d_ff_85_q[5]), .Qn(d_ff_85_qn));  // open: preset, en, reset
  assign or_363_out = {2'b00, d_ff_86_q[5], {5{1'b0}}} | or_364_out;  // OR_Gate or_363, 8 bits wide
  D_Flip_Flop d_ff_86 (.clk(CLK), .D(d_ff_10_q[2]), .Q(d_ff_86_q[5]), .Qn(d_ff_86_qn));  // open: preset, en, reset
  assign or_364_out = {2'b00, d_ff_87_q[5], {5{1'b0}}} | or_365_out;  // OR_Gate or_364, 8 bits wide
  D_Flip_Flop d_ff_87 (.clk(CLK), .D(d_ff_11_q[2]), .Q(d_ff_87_q[5]), .Qn(d_ff_87_qn));  // open: preset, en, reset
  assign or_365_out = {2'b00, d_ff_88_q[5], {5{1'b0}}} | or_366_out;  // OR_Gate or_365, 8 bits wide
  D_Flip_Flop d_ff_88 (.clk(CLK), .D(d_ff_12_q[2]), .Q(d_ff_88_q[5]), .Qn(d_ff_88_qn));  // open: preset, en, reset
  assign or_366_out = {2'b00, d_ff_89_q[5], {5{1'b0}}} | or_367_out;  // OR_Gate or_366, 8 bits wide
  D_Flip_Flop d_ff_89 (.clk(CLK), .D(d_ff_13_q[2]), .Q(d_ff_89_q[5]), .Qn(d_ff_89_qn));  // open: preset, en, reset
  assign or_367_out = {2'b00, d_ff_90_q[5], {5{1'b0}}} | or_368_out;  // OR_Gate or_367, 8 bits wide
  D_Flip_Flop d_ff_90 (.clk(CLK), .D(d_ff_14_q[2]), .Q(d_ff_90_q[5]), .Qn(d_ff_90_qn));  // open: preset, en, reset
  assign or_368_out = {2'b00, d_ff_91_q[5], {5{1'b0}}} | or_369_out;  // OR_Gate or_368, 8 bits wide
  D_Flip_Flop d_ff_91 (.clk(CLK), .D(d_ff_15_q[2]), .Q(d_ff_91_q[5]), .Qn(d_ff_91_qn));  // open: preset, en, reset
  assign or_369_out = {d_ff_157_q[7], d_ff_16_q[2], d_ff_157_q[5], {2{d_ff_157_q[7]}}, 3'b000} | or_370_out;  // OR_Gate or_369, 8 bits wide
  D_Flip_Flop d_ff_92 (.clk(CLK), .D(d_ff_16_q[2]), .Q(d_ff_157_q[7]), .Qn(d_ff_92_qn));  // open: preset, en, reset
  assign or_370_out = {d_ff_158_q[7], d_ff_17_q[2], d_ff_158_q[5], {2{d_ff_158_q[7]}}, 3'b000} | or_371_out;  // OR_Gate or_370, 8 bits wide
  D_Flip_Flop d_ff_93 (.clk(CLK), .D(d_ff_17_q[2]), .Q(d_ff_158_q[7]), .Qn(d_ff_93_qn));  // open: preset, en, reset
  assign or_371_out = {d_ff_159_q[7], d_ff_18_q[2], d_ff_159_q[5], {2{d_ff_159_q[7]}}, 3'b000} | or_372_out;  // OR_Gate or_371, 8 bits wide
  D_Flip_Flop d_ff_94 (.clk(CLK), .D(d_ff_18_q[2]), .Q(d_ff_159_q[7]), .Qn(d_ff_94_qn));  // open: preset, en, reset
  assign or_372_out = {d_ff_160_q[7], d_ff_19_q[2], d_ff_160_q[5], {2{d_ff_160_q[7]}}, 3'b000} | or_373_out;  // OR_Gate or_372, 8 bits wide
  D_Flip_Flop d_ff_95 (.clk(CLK), .D(d_ff_19_q[2]), .Q(d_ff_160_q[7]), .Qn(d_ff_95_qn));  // open: preset, en, reset
  assign or_373_out = {d_ff_161_q[7], d_ff_20_q[2], d_ff_161_q[5], {2{d_ff_161_q[7]}}, 3'b000} | or_374_out;  // OR_Gate or_373, 8 bits wide
  D_Flip_Flop d_ff_96 (.clk(CLK), .D(d_ff_20_q[2]), .Q(d_ff_161_q[7]), .Qn(d_ff_96_qn));  // open: preset, en, reset
  assign or_374_out = {d_ff_162_q[7], d_ff_21_q[2], d_ff_162_q[5], {2{d_ff_162_q[7]}}, 3'b000} | or_375_out;  // OR_Gate or_374, 8 bits wide
  D_Flip_Flop d_ff_97 (.clk(CLK), .D(d_ff_21_q[2]), .Q(d_ff_162_q[7]), .Qn(d_ff_97_qn));  // open: preset, en, reset
  assign or_375_out = {d_ff_163_q[7], d_ff_22_q[2], d_ff_163_q[5], {2{d_ff_163_q[7]}}, 3'b000} | or_376_out;  // OR_Gate or_375, 8 bits wide
  D_Flip_Flop d_ff_98 (.clk(CLK), .D(d_ff_22_q[2]), .Q(d_ff_163_q[7]), .Qn(d_ff_98_qn));  // open: preset, en, reset
  assign or_376_out = {d_ff_164_q[7], d_ff_23_q[2], d_ff_164_q[5], {2{d_ff_164_q[7]}}, 3'b000} | or_377_out;  // OR_Gate or_376, 8 bits wide
  D_Flip_Flop d_ff_99 (.clk(CLK), .D(d_ff_23_q[2]), .Q(d_ff_164_q[7]), .Qn(d_ff_99_qn));  // open: preset, en, reset
  assign or_377_out = {d_ff_165_q[7], d_ff_24_q[2], d_ff_165_q[5], {2{d_ff_165_q[7]}}, 3'b000} | or_378_out;  // OR_Gate or_377, 8 bits wide
  D_Flip_Flop d_ff_100 (.clk(CLK), .D(d_ff_24_q[2]), .Q(d_ff_165_q[7]), .Qn(d_ff_100_qn));  // open: preset, en, reset
  assign or_378_out = {d_ff_166_q[7], d_ff_25_q[2], d_ff_166_q[5], {2{d_ff_166_q[7]}}, 3'b000} | or_379_out;  // OR_Gate or_378, 8 bits wide
  D_Flip_Flop d_ff_101 (.clk(CLK), .D(d_ff_25_q[2]), .Q(d_ff_166_q[7]), .Qn(d_ff_101_qn));  // open: preset, en, reset
  assign or_379_out = {d_ff_167_q[7], d_ff_26_q[2], d_ff_167_q[5], {2{d_ff_167_q[7]}}, 3'b000} | or_380_out;  // OR_Gate or_379, 8 bits wide
  D_Flip_Flop d_ff_102 (.clk(CLK), .D(d_ff_26_q[2]), .Q(d_ff_167_q[7]), .Qn(d_ff_102_qn));  // open: preset, en, reset
  assign or_380_out = {d_ff_168_q[7], d_ff_27_q[2], d_ff_168_q[5], {2{d_ff_168_q[7]}}, 3'b000} | or_381_out;  // OR_Gate or_380, 8 bits wide
  D_Flip_Flop d_ff_103 (.clk(CLK), .D(d_ff_27_q[2]), .Q(d_ff_168_q[7]), .Qn(d_ff_103_qn));  // open: preset, en, reset
  assign or_381_out = {d_ff_169_q[7], d_ff_28_q[2], d_ff_169_q[5], {2{d_ff_169_q[7]}}, 3'b000} | or_382_out;  // OR_Gate or_381, 8 bits wide
  D_Flip_Flop d_ff_104 (.clk(CLK), .D(d_ff_28_q[2]), .Q(d_ff_169_q[7]), .Qn(d_ff_104_qn));  // open: preset, en, reset
  assign or_382_out = {d_ff_170_q[7], d_ff_29_q[2], d_ff_170_q[5], {2{d_ff_170_q[7]}}, 3'b000} | or_383_out;  // OR_Gate or_382, 8 bits wide
  D_Flip_Flop d_ff_105 (.clk(CLK), .D(d_ff_29_q[2]), .Q(d_ff_170_q[7]), .Qn(d_ff_105_qn));  // open: preset, en, reset
  assign or_383_out = {d_ff_171_q[7], d_ff_30_q[2], d_ff_171_q[5], {2{d_ff_171_q[7]}}, 3'b000} | or_384_out;  // OR_Gate or_383, 8 bits wide
  D_Flip_Flop d_ff_106 (.clk(CLK), .D(d_ff_30_q[2]), .Q(d_ff_171_q[7]), .Qn(d_ff_106_qn));  // open: preset, en, reset
  assign or_384_out = {d_ff_172_q[7], d_ff_31_q[2], d_ff_172_q[5], {2{d_ff_172_q[7]}}, 3'b000} | or_385_out;  // OR_Gate or_384, 8 bits wide
  D_Flip_Flop d_ff_107 (.clk(CLK), .D(d_ff_31_q[2]), .Q(d_ff_172_q[7]), .Qn(d_ff_107_qn));  // open: preset, en, reset
  assign or_385_out = {d_ff_173_q, 2'b00, d_ff_173_q[7], 2'b00} | or_386_out;  // OR_Gate or_385, 8 bits wide
  D_Flip_Flop d_ff_108 (.clk(CLK), .D(d_ff_173_q[6]), .Q(d_ff_173_q[7]), .Qn(d_ff_108_qn));  // open: preset, en, reset
  assign or_386_out = {d_ff_174_q, 2'b00, d_ff_174_q[7], 2'b00} | or_387_out;  // OR_Gate or_386, 8 bits wide
  D_Flip_Flop d_ff_109 (.clk(CLK), .D(d_ff_174_q[6]), .Q(d_ff_174_q[7]), .Qn(d_ff_109_qn));  // open: preset, en, reset
  assign or_387_out = {d_ff_175_q, 2'b00, d_ff_175_q[7], 2'b00} | or_388_out;  // OR_Gate or_387, 8 bits wide
  D_Flip_Flop d_ff_110 (.clk(CLK), .D(d_ff_175_q[6]), .Q(d_ff_175_q[7]), .Qn(d_ff_110_qn));  // open: preset, en, reset
  assign or_388_out = {d_ff_176_q, 2'b00, d_ff_176_q[7], 2'b00} | or_389_out;  // OR_Gate or_388, 8 bits wide
  D_Flip_Flop d_ff_111 (.clk(CLK), .D(d_ff_176_q[6]), .Q(d_ff_176_q[7]), .Qn(d_ff_111_qn));  // open: preset, en, reset
  assign or_389_out = {d_ff_177_q, 2'b00, d_ff_177_q[7], 2'b00} | or_390_out;  // OR_Gate or_389, 8 bits wide
  D_Flip_Flop d_ff_112 (.clk(CLK), .D(d_ff_177_q[6]), .Q(d_ff_177_q[7]), .Qn(d_ff_112_qn));  // open: preset, en, reset
  assign or_390_out = {d_ff_178_q, 2'b00, d_ff_178_q[7], 2'b00} | or_391_out;  // OR_Gate or_390, 8 bits wide
  D_Flip_Flop d_ff_113 (.clk(CLK), .D(d_ff_178_q[6]), .Q(d_ff_178_q[7]), .Qn(d_ff_113_qn));  // open: preset, en, reset
  assign or_391_out = {d_ff_179_q, 2'b00, d_ff_179_q[7], 2'b00} | or_392_out;  // OR_Gate or_391, 8 bits wide
  D_Flip_Flop d_ff_114 (.clk(CLK), .D(d_ff_179_q[6]), .Q(d_ff_179_q[7]), .Qn(d_ff_114_qn));  // open: preset, en, reset
  assign or_392_out = {d_ff_180_q, 2'b00, d_ff_180_q[7], 2'b00} | or_393_out;  // OR_Gate or_392, 8 bits wide
  D_Flip_Flop d_ff_115 (.clk(CLK), .D(d_ff_180_q[6]), .Q(d_ff_180_q[7]), .Qn(d_ff_115_qn));  // open: preset, en, reset
  assign or_393_out = {d_ff_181_q, 2'b00, d_ff_181_q[7], 2'b00} | or_394_out;  // OR_Gate or_393, 8 bits wide
  D_Flip_Flop d_ff_116 (.clk(CLK), .D(d_ff_181_q[6]), .Q(d_ff_181_q[7]), .Qn(d_ff_116_qn));  // open: preset, en, reset
  assign or_394_out = {d_ff_182_q, 2'b00, d_ff_182_q[7], 2'b00} | or_395_out;  // OR_Gate or_394, 8 bits wide
  D_Flip_Flop d_ff_117 (.clk(CLK), .D(d_ff_182_q[6]), .Q(d_ff_182_q[7]), .Qn(d_ff_117_qn));  // open: preset, en, reset
  assign or_395_out = {d_ff_183_q, 2'b00, d_ff_183_q[7], 2'b00} | or_396_out;  // OR_Gate or_395, 8 bits wide
  D_Flip_Flop d_ff_118 (.clk(CLK), .D(d_ff_183_q[6]), .Q(d_ff_183_q[7]), .Qn(d_ff_118_qn));  // open: preset, en, reset
  assign or_396_out = {d_ff_184_q, 2'b00, d_ff_184_q[7], 2'b00} | or_397_out;  // OR_Gate or_396, 8 bits wide
  D_Flip_Flop d_ff_119 (.clk(CLK), .D(d_ff_184_q[6]), .Q(d_ff_184_q[7]), .Qn(d_ff_119_qn));  // open: preset, en, reset
  assign or_397_out = {d_ff_185_q, 2'b00, d_ff_185_q[7], 2'b00} | or_398_out;  // OR_Gate or_397, 8 bits wide
  D_Flip_Flop d_ff_120 (.clk(CLK), .D(d_ff_185_q[6]), .Q(d_ff_185_q[7]), .Qn(d_ff_120_qn));  // open: preset, en, reset
  assign or_398_out = {d_ff_186_q, 2'b00, d_ff_186_q[7], 2'b00} | or_399_out;  // OR_Gate or_398, 8 bits wide
  D_Flip_Flop d_ff_121 (.clk(CLK), .D(d_ff_186_q[6]), .Q(d_ff_186_q[7]), .Qn(d_ff_121_qn));  // open: preset, en, reset
  assign or_399_out = {d_ff_187_q, 2'b00, d_ff_187_q[7], 2'b00} | or_400_out;  // OR_Gate or_399, 8 bits wide
  D_Flip_Flop d_ff_122 (.clk(CLK), .D(d_ff_187_q[6]), .Q(d_ff_187_q[7]), .Qn(d_ff_122_qn));  // open: preset, en, reset
  assign or_400_out = {d_ff_188_q, 2'b00, d_ff_188_q[7], 2'b00} | or_401_out;  // OR_Gate or_400, 8 bits wide
  D_Flip_Flop d_ff_123 (.clk(CLK), .D(d_ff_188_q[6]), .Q(d_ff_188_q[7]), .Qn(d_ff_123_qn));  // open: preset, en, reset
  assign or_401_out = or_402_out | {2'b00, d_ff_217_q[5], {5{1'b0}}};  // OR_Gate or_401, 8 bits wide
  D_Flip_Flop d_ff_124 (.clk(CLK), .D(d_ff_48_q), .Q(d_ff_124_q[0]), .Qn(d_ff_124_qn));  // open: preset, en, reset
  assign or_402_out = or_403_out | {2'b00, d_ff_218_q[5], {5{1'b0}}};  // OR_Gate or_402, 8 bits wide
  D_Flip_Flop d_ff_125 (.clk(CLK), .D(d_ff_49_q), .Q(d_ff_125_q[0]), .Qn(d_ff_125_qn));  // open: preset, en, reset
  assign or_403_out = or_404_out | {2'b00, d_ff_219_q[5], {5{1'b0}}};  // OR_Gate or_403, 8 bits wide
  D_Flip_Flop d_ff_126 (.clk(CLK), .D(d_ff_50_q), .Q(d_ff_126_q[0]), .Qn(d_ff_126_qn));  // open: preset, en, reset
  assign or_404_out = or_405_out | {2'b00, d_ff_220_q[5], {5{1'b0}}};  // OR_Gate or_404, 8 bits wide
  D_Flip_Flop d_ff_127 (.clk(CLK), .D(d_ff_51_q), .Q(d_ff_127_q[0]), .Qn(d_ff_127_qn));  // open: preset, en, reset
  assign or_405_out = or_406_out | {2'b00, d_ff_221_q[5], {5{1'b0}}};  // OR_Gate or_405, 8 bits wide
  D_Flip_Flop d_ff_128 (.clk(CLK), .D(d_ff_52_q), .Q(d_ff_128_q[0]), .Qn(d_ff_128_qn));  // open: preset, en, reset
  assign or_406_out = or_407_out | {2'b00, d_ff_222_q[5], {5{1'b0}}};  // OR_Gate or_406, 8 bits wide
  D_Flip_Flop d_ff_129 (.clk(CLK), .D(d_ff_53_q), .Q(d_ff_129_q[0]), .Qn(d_ff_129_qn));  // open: preset, en, reset
  assign or_407_out = or_408_out | {2'b00, d_ff_223_q[5], {5{1'b0}}};  // OR_Gate or_407, 8 bits wide
  D_Flip_Flop d_ff_130 (.clk(CLK), .D(d_ff_54_q), .Q(d_ff_130_q[0]), .Qn(d_ff_130_qn));  // open: preset, en, reset
  assign or_408_out = or_409_out | {2'b00, d_ff_224_q[5], {5{1'b0}}};  // OR_Gate or_408, 8 bits wide
  D_Flip_Flop d_ff_131 (.clk(CLK), .D(d_ff_55_q), .Q(d_ff_131_q[0]), .Qn(d_ff_131_qn));  // open: preset, en, reset
  assign or_409_out = or_410_out | {2'b00, d_ff_225_q[5], {5{1'b0}}};  // OR_Gate or_409, 8 bits wide
  D_Flip_Flop d_ff_132 (.clk(CLK), .D(d_ff_56_q), .Q(d_ff_132_q[0]), .Qn(d_ff_132_qn));  // open: preset, en, reset
  assign or_410_out = or_411_out | {2'b00, d_ff_226_q[5], {5{1'b0}}};  // OR_Gate or_410, 8 bits wide
  D_Flip_Flop d_ff_133 (.clk(CLK), .D(d_ff_57_q), .Q(d_ff_133_q[0]), .Qn(d_ff_133_qn));  // open: preset, en, reset
  assign or_411_out = or_412_out | {2'b00, d_ff_227_q[5], {5{1'b0}}};  // OR_Gate or_411, 8 bits wide
  D_Flip_Flop d_ff_134 (.clk(CLK), .D(d_ff_58_q), .Q(d_ff_134_q[0]), .Qn(d_ff_134_qn));  // open: preset, en, reset
  assign or_412_out = or_413_out | {2'b00, d_ff_228_q[5], {5{1'b0}}};  // OR_Gate or_412, 8 bits wide
  D_Flip_Flop d_ff_135 (.clk(CLK), .D(d_ff_59_q), .Q(d_ff_135_q[0]), .Qn(d_ff_135_qn));  // open: preset, en, reset
  assign or_413_out = or_414_out | {2'b00, d_ff_229_q[5], {5{1'b0}}};  // OR_Gate or_413, 8 bits wide
  D_Flip_Flop d_ff_136 (.clk(CLK), .D(d_ff_60_q), .Q(d_ff_136_q[0]), .Qn(d_ff_136_qn));  // open: preset, en, reset
  assign or_414_out = or_415_out | {2'b00, d_ff_230_q[5], {5{1'b0}}};  // OR_Gate or_414, 8 bits wide
  D_Flip_Flop d_ff_137 (.clk(CLK), .D(d_ff_61_q), .Q(d_ff_137_q[0]), .Qn(d_ff_137_qn));  // open: preset, en, reset
  assign or_415_out = or_416_out | {2'b00, d_ff_231_q[5], {5{1'b0}}};  // OR_Gate or_415, 8 bits wide
  D_Flip_Flop d_ff_138 (.clk(CLK), .D(d_ff_62_q), .Q(d_ff_138_q[0]), .Qn(d_ff_138_qn));  // open: preset, en, reset
  assign or_416_out = or_417_out | {2'b00, d_ff_232_q[5], {5{1'b0}}};  // OR_Gate or_416, 8 bits wide
  D_Flip_Flop d_ff_139 (.clk(CLK), .D(d_ff_63_q), .Q(d_ff_139_q[0]), .Qn(d_ff_139_qn));  // open: preset, en, reset
  assign or_417_out = or_418_out | {2'b00, d_ff_233_q[5], {5{1'b0}}};  // OR_Gate or_417, 8 bits wide
  D_Flip_Flop d_ff_140 (.clk(CLK), .D(d_ff_64_q[0]), .Q(d_ff_140_q), .Qn(d_ff_140_qn));  // open: preset, en, reset
  assign or_418_out = or_419_out | {2'b00, d_ff_234_q[5], {5{1'b0}}};  // OR_Gate or_418, 8 bits wide
  D_Flip_Flop d_ff_141 (.clk(CLK), .D(d_ff_65_q[0]), .Q(d_ff_141_q), .Qn(d_ff_141_qn));  // open: preset, en, reset
  assign or_419_out = or_420_out | {2'b00, d_ff_235_q[5], {5{1'b0}}};  // OR_Gate or_419, 8 bits wide
  D_Flip_Flop d_ff_142 (.clk(CLK), .D(d_ff_66_q[0]), .Q(d_ff_142_q), .Qn(d_ff_142_qn));  // open: preset, en, reset
  assign or_420_out = or_421_out | {2'b00, d_ff_236_q[5], {5{1'b0}}};  // OR_Gate or_420, 8 bits wide
  D_Flip_Flop d_ff_143 (.clk(CLK), .D(d_ff_67_q[0]), .Q(d_ff_143_q), .Qn(d_ff_143_qn));  // open: preset, en, reset
  assign or_421_out = or_422_out | {2'b00, d_ff_237_q[5], {5{1'b0}}};  // OR_Gate or_421, 8 bits wide
  D_Flip_Flop d_ff_144 (.clk(CLK), .D(d_ff_68_q[0]), .Q(d_ff_144_q), .Qn(d_ff_144_qn));  // open: preset, en, reset
  assign or_422_out = or_423_out | {2'b00, d_ff_238_q[5], {5{1'b0}}};  // OR_Gate or_422, 8 bits wide
  D_Flip_Flop d_ff_145 (.clk(CLK), .D(d_ff_69_q[0]), .Q(d_ff_145_q), .Qn(d_ff_145_qn));  // open: preset, en, reset
  assign or_423_out = or_424_out | {2'b00, d_ff_239_q[5], {5{1'b0}}};  // OR_Gate or_423, 8 bits wide
  D_Flip_Flop d_ff_146 (.clk(CLK), .D(d_ff_70_q[0]), .Q(d_ff_146_q), .Qn(d_ff_146_qn));  // open: preset, en, reset
  assign or_424_out = or_425_out | {2'b00, d_ff_240_q[5], {5{1'b0}}};  // OR_Gate or_424, 8 bits wide
  D_Flip_Flop d_ff_147 (.clk(CLK), .D(d_ff_71_q[0]), .Q(d_ff_147_q), .Qn(d_ff_147_qn));  // open: preset, en, reset
  assign or_425_out = or_426_out | {2'b00, d_ff_241_q[5], {5{1'b0}}};  // OR_Gate or_425, 8 bits wide
  D_Flip_Flop d_ff_148 (.clk(CLK), .D(d_ff_72_q[0]), .Q(d_ff_148_q), .Qn(d_ff_148_qn));  // open: preset, en, reset
  assign or_426_out = or_427_out | {2'b00, d_ff_242_q[5], {5{1'b0}}};  // OR_Gate or_426, 8 bits wide
  D_Flip_Flop d_ff_149 (.clk(CLK), .D(d_ff_73_q[0]), .Q(d_ff_149_q), .Qn(d_ff_149_qn));  // open: preset, en, reset
  assign or_427_out = or_428_out | {2'b00, d_ff_243_q[5], {5{1'b0}}};  // OR_Gate or_427, 8 bits wide
  D_Flip_Flop d_ff_150 (.clk(CLK), .D(d_ff_74_q[0]), .Q(d_ff_150_q), .Qn(d_ff_150_qn));  // open: preset, en, reset
  assign or_428_out = or_505_out | {2'b00, d_ff_244_q[5], {5{1'b0}}};  // OR_Gate or_428, 8 bits wide
  D_Flip_Flop d_ff_151 (.clk(CLK), .D(d_ff_75_q[0]), .Q(d_ff_151_q), .Qn(d_ff_151_qn));  // open: preset, en, reset
  D_Flip_Flop d_ff_152 (.clk(CLK), .D(d_ff_153_q[4]), .Q(d_ff_152_q), .Qn(d_ff_152_qn));  // open: preset, en, reset
  D_Flip_Flop d_ff_153 (.clk(CLK), .D(d_ff_76_q), .Q(d_ff_153_q[4]), .Qn(d_ff_153_qn));  // open: preset, en, reset
  or or_429 (or_429_out, not_2_out, or_509_out);
  D_Flip_Flop d_ff_154 (.clk(CLK), .D(d_ff_77_q[4]), .Q(d_ff_154_q), .Qn(d_ff_154_qn));  // open: preset, en, reset
  assign or_430_out = {2'b00, d_ff_78_q, d_ff_78_q[4], 3'b000} | or_432_out;  // OR_Gate or_430, 8 bits wide
  D_Flip_Flop d_ff_155 (.clk(CLK), .D(d_ff_78_q[4]), .Q(d_ff_155_q), .Qn(d_ff_155_qn));  // open: preset, en, reset
  or or_431 (or_431_out, not_1_out, or_433_out);
  assign or_432_out = {2'b00, d_ff_79_q, d_ff_79_q[4], 3'b000} | or_357_out;  // OR_Gate or_432, 8 bits wide
  not not_1 (not_1_out, and_1_out);
  D_Flip_Flop d_ff_156 (.clk(CLK), .D(d_ff_79_q[4]), .Q(d_ff_156_q), .Qn(d_ff_156_qn));  // open: preset, en, reset
  and and_1 (and_1_out, d_ff_156_qn, d_ff_79_qn, d_ff_3_qn);
  or or_433 (or_433_out, d_ff_80_q[5], or_434_out);
  and and_2 (and_2_out, and_3_out, and_4_out);
  and and_3 (and_3_out, d_ff_80_qn, d_ff_4_qn);
  or or_434 (or_434_out, or_435_out, d_ff_81_q[5]);
  and and_4 (and_4_out, and_5_out, and_6_out);
  and and_5 (and_5_out, d_ff_81_qn, d_ff_5_qn);
  or or_435 (or_435_out, or_436_out, d_ff_82_q[5]);
  and and_6 (and_6_out, and_7_out, and_8_out);
  and and_7 (and_7_out, d_ff_82_qn, d_ff_6_qn);
  or or_436 (or_436_out, or_437_out, d_ff_83_q[5]);
  and and_8 (and_8_out, and_9_out, and_10_out);
  and and_9 (and_9_out, d_ff_83_qn, d_ff_7_qn);
  or or_437 (or_437_out, or_438_out, d_ff_84_q[5]);
  and and_10 (and_10_out, and_11_out, and_12_out);
  and and_11 (and_11_out, d_ff_84_qn, d_ff_8_qn);
  or or_438 (or_438_out, or_439_out, d_ff_85_q[5]);
  and and_12 (and_12_out, and_13_out, and_14_out);
  and and_13 (and_13_out, d_ff_85_qn, d_ff_9_qn);
  or or_439 (or_439_out, or_440_out, d_ff_86_q[5]);
  and and_14 (and_14_out, and_15_out, and_16_out);
  and and_15 (and_15_out, d_ff_86_qn, d_ff_10_qn);
  or or_440 (or_440_out, or_441_out, d_ff_87_q[5]);
  and and_16 (and_16_out, and_17_out, and_18_out);
  and and_17 (and_17_out, d_ff_87_qn, d_ff_11_qn);
  or or_441 (or_441_out, or_442_out, d_ff_88_q[5]);
  and and_18 (and_18_out, and_19_out, and_20_out);
  and and_19 (and_19_out, d_ff_88_qn, d_ff_12_qn);
  or or_442 (or_442_out, or_443_out, d_ff_89_q[5]);
  and and_20 (and_20_out, and_21_out, and_22_out);
  and and_21 (and_21_out, d_ff_89_qn, d_ff_13_qn);
  or or_443 (or_443_out, or_444_out, d_ff_90_q[5]);
  and and_22 (and_22_out, and_23_out, and_24_out);
  and and_23 (and_23_out, d_ff_90_qn, d_ff_14_qn);
  or or_444 (or_444_out, or_445_out, d_ff_91_q[5]);
  and and_24 (and_24_out, and_25_out, and_33_out);
  and and_25 (and_25_out, d_ff_91_qn, d_ff_15_qn);
  or or_445 (or_445_out, ~and_34_out, or_446_out);  // OR_Gate
  D_Flip_Flop d_ff_157 (.clk(CLK), .D(d_ff_157_q[7]), .Q(d_ff_157_q[5]), .Qn(d_ff_157_qn));  // open: preset, en, reset
  or or_446 (or_446_out, ~and_36_out, or_447_out);  // OR_Gate
  D_Flip_Flop d_ff_158 (.clk(CLK), .D(d_ff_158_q[7]), .Q(d_ff_158_q[5]), .Qn(d_ff_158_qn));  // open: preset, en, reset
  or or_447 (or_447_out, ~and_38_out, or_448_out);  // OR_Gate
  D_Flip_Flop d_ff_159 (.clk(CLK), .D(d_ff_159_q[7]), .Q(d_ff_159_q[5]), .Qn(d_ff_159_qn));  // open: preset, en, reset
  or or_448 (or_448_out, ~and_40_out, or_449_out);  // OR_Gate
  D_Flip_Flop d_ff_160 (.clk(CLK), .D(d_ff_160_q[7]), .Q(d_ff_160_q[5]), .Qn(d_ff_160_qn));  // open: preset, en, reset
  or or_449 (or_449_out, ~and_42_out, or_450_out);  // OR_Gate
  D_Flip_Flop d_ff_161 (.clk(CLK), .D(d_ff_161_q[7]), .Q(d_ff_161_q[5]), .Qn(d_ff_161_qn));  // open: preset, en, reset
  or or_450 (or_450_out, ~and_44_out, or_451_out);  // OR_Gate
  D_Flip_Flop d_ff_162 (.clk(CLK), .D(d_ff_162_q[7]), .Q(d_ff_162_q[5]), .Qn(d_ff_162_qn));  // open: preset, en, reset
  or or_451 (or_451_out, ~and_46_out, or_452_out);  // OR_Gate
  D_Flip_Flop d_ff_163 (.clk(CLK), .D(d_ff_163_q[7]), .Q(d_ff_163_q[5]), .Qn(d_ff_163_qn));  // open: preset, en, reset
  or or_452 (or_452_out, ~and_48_out, or_453_out);  // OR_Gate
  D_Flip_Flop d_ff_164 (.clk(CLK), .D(d_ff_164_q[7]), .Q(d_ff_164_q[5]), .Qn(d_ff_164_qn));  // open: preset, en, reset
  or or_453 (or_453_out, ~and_50_out, or_454_out);  // OR_Gate
  D_Flip_Flop d_ff_165 (.clk(CLK), .D(d_ff_165_q[7]), .Q(d_ff_165_q[5]), .Qn(d_ff_165_qn));  // open: preset, en, reset
  or or_454 (or_454_out, ~and_52_out, or_455_out);  // OR_Gate
  D_Flip_Flop d_ff_166 (.clk(CLK), .D(d_ff_166_q[7]), .Q(d_ff_166_q[5]), .Qn(d_ff_166_qn));  // open: preset, en, reset
  or or_455 (or_455_out, ~and_54_out, or_456_out);  // OR_Gate
  D_Flip_Flop d_ff_167 (.clk(CLK), .D(d_ff_167_q[7]), .Q(d_ff_167_q[5]), .Qn(d_ff_167_qn));  // open: preset, en, reset
  or or_456 (or_456_out, ~and_56_out, or_457_out);  // OR_Gate
  D_Flip_Flop d_ff_168 (.clk(CLK), .D(d_ff_168_q[7]), .Q(d_ff_168_q[5]), .Qn(d_ff_168_qn));  // open: preset, en, reset
  or or_457 (or_457_out, ~and_58_out, or_458_out);  // OR_Gate
  D_Flip_Flop d_ff_169 (.clk(CLK), .D(d_ff_169_q[7]), .Q(d_ff_169_q[5]), .Qn(d_ff_169_qn));  // open: preset, en, reset
  or or_458 (or_458_out, ~and_60_out, or_459_out);  // OR_Gate
  D_Flip_Flop d_ff_170 (.clk(CLK), .D(d_ff_170_q[7]), .Q(d_ff_170_q[5]), .Qn(d_ff_170_qn));  // open: preset, en, reset
  or or_459 (or_459_out, ~and_62_out, or_460_out);  // OR_Gate
  D_Flip_Flop d_ff_171 (.clk(CLK), .D(d_ff_171_q[7]), .Q(d_ff_171_q[5]), .Qn(d_ff_171_qn));  // open: preset, en, reset
  or or_460 (or_460_out, ~and_64_out, or_461_out);  // OR_Gate
  D_Flip_Flop d_ff_172 (.clk(CLK), .D(d_ff_172_q[7]), .Q(d_ff_172_q[5]), .Qn(d_ff_172_qn));  // open: preset, en, reset
  or or_461 (or_461_out, ~and_66_out, or_462_out);  // OR_Gate
  D_Flip_Flop d_ff_173 (.clk(CLK), .D(d_ff_173_q[7]), .Q(d_ff_173_q[5]), .Qn(d_ff_173_qn));  // open: preset, en, reset
  or or_462 (or_462_out, ~and_68_out, or_463_out);  // OR_Gate
  D_Flip_Flop d_ff_174 (.clk(CLK), .D(d_ff_174_q[7]), .Q(d_ff_174_q[5]), .Qn(d_ff_174_qn));  // open: preset, en, reset
  or or_463 (or_463_out, ~and_70_out, or_464_out);  // OR_Gate
  D_Flip_Flop d_ff_175 (.clk(CLK), .D(d_ff_175_q[7]), .Q(d_ff_175_q[5]), .Qn(d_ff_175_qn));  // open: preset, en, reset
  or or_464 (or_464_out, ~and_72_out, or_465_out);  // OR_Gate
  D_Flip_Flop d_ff_176 (.clk(CLK), .D(d_ff_176_q[7]), .Q(d_ff_176_q[5]), .Qn(d_ff_176_qn));  // open: preset, en, reset
  or or_465 (or_465_out, ~and_74_out, or_466_out);  // OR_Gate
  D_Flip_Flop d_ff_177 (.clk(CLK), .D(d_ff_177_q[7]), .Q(d_ff_177_q[5]), .Qn(d_ff_177_qn));  // open: preset, en, reset
  or or_466 (or_466_out, ~and_76_out, or_467_out);  // OR_Gate
  D_Flip_Flop d_ff_178 (.clk(CLK), .D(d_ff_178_q[7]), .Q(d_ff_178_q[5]), .Qn(d_ff_178_qn));  // open: preset, en, reset
  or or_467 (or_467_out, ~and_78_out, or_468_out);  // OR_Gate
  D_Flip_Flop d_ff_179 (.clk(CLK), .D(d_ff_179_q[7]), .Q(d_ff_179_q[5]), .Qn(d_ff_179_qn));  // open: preset, en, reset
  or or_468 (or_468_out, ~and_80_out, or_469_out);  // OR_Gate
  D_Flip_Flop d_ff_180 (.clk(CLK), .D(d_ff_180_q[7]), .Q(d_ff_180_q[5]), .Qn(d_ff_180_qn));  // open: preset, en, reset
  or or_469 (or_469_out, ~and_82_out, or_470_out);  // OR_Gate
  D_Flip_Flop d_ff_181 (.clk(CLK), .D(d_ff_181_q[7]), .Q(d_ff_181_q[5]), .Qn(d_ff_181_qn));  // open: preset, en, reset
  or or_470 (or_470_out, ~and_84_out, or_471_out);  // OR_Gate
  D_Flip_Flop d_ff_182 (.clk(CLK), .D(d_ff_182_q[7]), .Q(d_ff_182_q[5]), .Qn(d_ff_182_qn));  // open: preset, en, reset
  or or_471 (or_471_out, ~and_86_out, or_472_out);  // OR_Gate
  D_Flip_Flop d_ff_183 (.clk(CLK), .D(d_ff_183_q[7]), .Q(d_ff_183_q[5]), .Qn(d_ff_183_qn));  // open: preset, en, reset
  or or_472 (or_472_out, ~and_88_out, or_473_out);  // OR_Gate
  D_Flip_Flop d_ff_184 (.clk(CLK), .D(d_ff_184_q[7]), .Q(d_ff_184_q[5]), .Qn(d_ff_184_qn));  // open: preset, en, reset
  or or_473 (or_473_out, ~and_90_out, or_474_out);  // OR_Gate
  D_Flip_Flop d_ff_185 (.clk(CLK), .D(d_ff_185_q[7]), .Q(d_ff_185_q[5]), .Qn(d_ff_185_qn));  // open: preset, en, reset
  or or_474 (or_474_out, ~and_92_out, or_475_out);  // OR_Gate
  D_Flip_Flop d_ff_186 (.clk(CLK), .D(d_ff_186_q[7]), .Q(d_ff_186_q[5]), .Qn(d_ff_186_qn));  // open: preset, en, reset
  or or_475 (or_475_out, ~and_94_out, or_476_out);  // OR_Gate
  D_Flip_Flop d_ff_187 (.clk(CLK), .D(d_ff_187_q[7]), .Q(d_ff_187_q[5]), .Qn(d_ff_187_qn));  // open: preset, en, reset
  or or_476 (or_476_out, ~and_96_out, or_477_out);  // OR_Gate
  D_Flip_Flop d_ff_188 (.clk(CLK), .D(d_ff_188_q[7]), .Q(d_ff_188_q[5]), .Qn(d_ff_188_qn));  // open: preset, en, reset
  or or_477 (or_477_out, or_478_out, d_ff_217_q[5]);
  D_Flip_Flop d_ff_189 (.clk(CLK), .D(d_ff_124_q[0]), .Q(d_ff_124_q[2]), .Qn(d_ff_189_qn));  // open: preset, en, reset
  or or_478 (or_478_out, or_479_out, d_ff_218_q[5]);
  D_Flip_Flop d_ff_190 (.clk(CLK), .D(d_ff_125_q[0]), .Q(d_ff_125_q[2]), .Qn(d_ff_190_qn));  // open: preset, en, reset
  or or_479 (or_479_out, or_480_out, d_ff_219_q[5]);
  D_Flip_Flop d_ff_191 (.clk(CLK), .D(d_ff_126_q[0]), .Q(d_ff_126_q[2]), .Qn(d_ff_191_qn));  // open: preset, en, reset
  or or_480 (or_480_out, or_481_out, d_ff_220_q[5]);
  D_Flip_Flop d_ff_192 (.clk(CLK), .D(d_ff_127_q[0]), .Q(d_ff_127_q[2]), .Qn(d_ff_192_qn));  // open: preset, en, reset
  or or_481 (or_481_out, or_482_out, d_ff_221_q[5]);
  D_Flip_Flop d_ff_193 (.clk(CLK), .D(d_ff_128_q[0]), .Q(d_ff_128_q[2]), .Qn(d_ff_193_qn));  // open: preset, en, reset
  or or_482 (or_482_out, or_483_out, d_ff_222_q[5]);
  D_Flip_Flop d_ff_194 (.clk(CLK), .D(d_ff_129_q[0]), .Q(d_ff_129_q[2]), .Qn(d_ff_194_qn));  // open: preset, en, reset
  or or_483 (or_483_out, or_484_out, d_ff_223_q[5]);
  D_Flip_Flop d_ff_195 (.clk(CLK), .D(d_ff_130_q[0]), .Q(d_ff_130_q[2]), .Qn(d_ff_195_qn));  // open: preset, en, reset
  or or_484 (or_484_out, or_485_out, d_ff_224_q[5]);
  D_Flip_Flop d_ff_196 (.clk(CLK), .D(d_ff_131_q[0]), .Q(d_ff_131_q[2]), .Qn(d_ff_196_qn));  // open: preset, en, reset
  or or_485 (or_485_out, or_486_out, d_ff_225_q[5]);
  D_Flip_Flop d_ff_197 (.clk(CLK), .D(d_ff_132_q[0]), .Q(d_ff_132_q[2]), .Qn(d_ff_197_qn));  // open: preset, en, reset
  or or_486 (or_486_out, or_487_out, d_ff_226_q[5]);
  D_Flip_Flop d_ff_198 (.clk(CLK), .D(d_ff_133_q[0]), .Q(d_ff_133_q[2]), .Qn(d_ff_198_qn));  // open: preset, en, reset
  or or_487 (or_487_out, or_488_out, d_ff_227_q[5]);
  D_Flip_Flop d_ff_199 (.clk(CLK), .D(d_ff_134_q[0]), .Q(d_ff_134_q[2]), .Qn(d_ff_199_qn));  // open: preset, en, reset
  or or_488 (or_488_out, or_489_out, d_ff_228_q[5]);
  D_Flip_Flop d_ff_200 (.clk(CLK), .D(d_ff_135_q[0]), .Q(d_ff_135_q[2]), .Qn(d_ff_200_qn));  // open: preset, en, reset
  or or_489 (or_489_out, or_490_out, d_ff_229_q[5]);
  D_Flip_Flop d_ff_201 (.clk(CLK), .D(d_ff_136_q[0]), .Q(d_ff_136_q[2]), .Qn(d_ff_201_qn));  // open: preset, en, reset
  or or_490 (or_490_out, or_491_out, d_ff_230_q[5]);
  D_Flip_Flop d_ff_202 (.clk(CLK), .D(d_ff_137_q[0]), .Q(d_ff_137_q[2]), .Qn(d_ff_202_qn));  // open: preset, en, reset
  or or_491 (or_491_out, or_492_out, d_ff_231_q[5]);
  D_Flip_Flop d_ff_203 (.clk(CLK), .D(d_ff_138_q[0]), .Q(d_ff_138_q[2]), .Qn(d_ff_203_qn));  // open: preset, en, reset
  or or_492 (or_492_out, or_493_out, d_ff_232_q[5]);
  D_Flip_Flop d_ff_204 (.clk(CLK), .D(d_ff_139_q[0]), .Q(d_ff_139_q[2]), .Qn(d_ff_204_qn));  // open: preset, en, reset
  or or_493 (or_493_out, or_494_out, d_ff_233_q[5]);
  D_Flip_Flop d_ff_205 (.clk(CLK), .D(d_ff_140_q), .Q(d_ff_64_q[2]), .Qn(d_ff_205_qn));  // open: preset, en, reset
  or or_494 (or_494_out, or_495_out, d_ff_234_q[5]);
  D_Flip_Flop d_ff_206 (.clk(CLK), .D(d_ff_141_q), .Q(d_ff_65_q[2]), .Qn(d_ff_206_qn));  // open: preset, en, reset
  or or_495 (or_495_out, or_496_out, d_ff_235_q[5]);
  D_Flip_Flop d_ff_207 (.clk(CLK), .D(d_ff_142_q), .Q(d_ff_66_q[2]), .Qn(d_ff_207_qn));  // open: preset, en, reset
  or or_496 (or_496_out, or_497_out, d_ff_236_q[5]);
  D_Flip_Flop d_ff_208 (.clk(CLK), .D(d_ff_143_q), .Q(d_ff_67_q[2]), .Qn(d_ff_208_qn));  // open: preset, en, reset
  or or_497 (or_497_out, or_498_out, d_ff_237_q[5]);
  D_Flip_Flop d_ff_209 (.clk(CLK), .D(d_ff_144_q), .Q(d_ff_68_q[2]), .Qn(d_ff_209_qn));  // open: preset, en, reset
  or or_498 (or_498_out, or_499_out, d_ff_238_q[5]);
  D_Flip_Flop d_ff_210 (.clk(CLK), .D(d_ff_145_q), .Q(d_ff_69_q[2]), .Qn(d_ff_210_qn));  // open: preset, en, reset
  or or_499 (or_499_out, or_500_out, d_ff_239_q[5]);
  D_Flip_Flop d_ff_211 (.clk(CLK), .D(d_ff_146_q), .Q(d_ff_70_q[2]), .Qn(d_ff_211_qn));  // open: preset, en, reset
  or or_500 (or_500_out, or_501_out, d_ff_240_q[5]);
  D_Flip_Flop d_ff_212 (.clk(CLK), .D(d_ff_147_q), .Q(d_ff_71_q[2]), .Qn(d_ff_212_qn));  // open: preset, en, reset
  or or_501 (or_501_out, or_502_out, d_ff_241_q[5]);
  D_Flip_Flop d_ff_213 (.clk(CLK), .D(d_ff_148_q), .Q(d_ff_72_q[2]), .Qn(d_ff_213_qn));  // open: preset, en, reset
  or or_502 (or_502_out, or_503_out, d_ff_242_q[5]);
  D_Flip_Flop d_ff_214 (.clk(CLK), .D(d_ff_149_q), .Q(d_ff_73_q[2]), .Qn(d_ff_214_qn));  // open: preset, en, reset
  or or_503 (or_503_out, or_504_out, d_ff_243_q[5]);
  D_Flip_Flop d_ff_215 (.clk(CLK), .D(d_ff_150_q), .Q(d_ff_74_q[2]), .Qn(d_ff_215_qn));  // open: preset, en, reset
  or or_504 (or_504_out, or_538_out, d_ff_244_q[5]);
  D_Flip_Flop d_ff_216 (.clk(CLK), .D(d_ff_151_q), .Q(d_ff_75_q[2]), .Qn(d_ff_216_qn));  // open: preset, en, reset
  assign or_505_out = command_unit_cmp_instruction_1_ram_instruction;  // OR_Gate or_505, 8 bits wide OR_Gate
  and and_26 (and_26_out[4], and_27_out, and_28_out);
  and and_27 (and_27_out, d_ff_152_qn, d_ff_153_qn, d_ff_76_qn);
  or or_506 (or_506_out, d_ff_153_q[4], d_ff_153_q[5], or_429_out);
  assign or_507_out = {2'b00, d_ff_153_q, d_ff_153_q[4], 3'b000} | or_508_out;  // OR_Gate or_507, 8 bits wide
  and and_28 (and_28_out, and_29_out, and_30_out);
  not not_2 (not_2_out, and_29_out);
  and and_29 (and_29_out, d_ff_154_qn, d_ff_77_qn, d_ff_1_qn);
  assign or_508_out = {2'b00, d_ff_77_q, d_ff_77_q[4], 3'b000} | or_430_out;  // OR_Gate or_508, 8 bits wide
  or or_509 (or_509_out, or_431_out, not_3_out);
  not not_3 (not_3_out, and_31_out);
  and and_30 (and_30_out, and_31_out, and_32_out);
  and and_31 (and_31_out, d_ff_155_qn, d_ff_78_qn, d_ff_2_qn);
  and and_32 (and_32_out, and_1_out, and_2_out);
  and and_33 (and_33_out, and_34_out, and_35_out);
  and and_34 (and_34_out, d_ff_157_qn, d_ff_92_qn, d_ff_16_qn);
  and and_35 (and_35_out, and_36_out, and_37_out);
  and and_36 (and_36_out, d_ff_158_qn, d_ff_93_qn, d_ff_17_qn);
  and and_37 (and_37_out, and_38_out, and_39_out);
  and and_38 (and_38_out, d_ff_159_qn, d_ff_94_qn, d_ff_18_qn);
  and and_39 (and_39_out, and_40_out, and_41_out);
  and and_40 (and_40_out, d_ff_160_qn, d_ff_95_qn, d_ff_19_qn);
  and and_41 (and_41_out, and_42_out, and_43_out);
  and and_42 (and_42_out, d_ff_161_qn, d_ff_96_qn, d_ff_20_qn);
  and and_43 (and_43_out, and_44_out, and_45_out);
  and and_44 (and_44_out, d_ff_162_qn, d_ff_97_qn, d_ff_21_qn);
  and and_45 (and_45_out, and_46_out, and_47_out);
  and and_46 (and_46_out, d_ff_163_qn, d_ff_98_qn, d_ff_22_qn);
  and and_47 (and_47_out, and_48_out, and_49_out);
  and and_48 (and_48_out, d_ff_164_qn, d_ff_99_qn, d_ff_23_qn);
  and and_49 (and_49_out, and_50_out, and_51_out);
  and and_50 (and_50_out, d_ff_165_qn, d_ff_100_qn, d_ff_24_qn);
  and and_51 (and_51_out, and_52_out, and_53_out);
  and and_52 (and_52_out, d_ff_166_qn, d_ff_101_qn, d_ff_25_qn);
  and and_53 (and_53_out, and_54_out, and_55_out);
  and and_54 (and_54_out, d_ff_167_qn, d_ff_102_qn, d_ff_26_qn);
  and and_55 (and_55_out, and_56_out, and_57_out);
  and and_56 (and_56_out, d_ff_168_qn, d_ff_103_qn, d_ff_27_qn);
  and and_57 (and_57_out, and_58_out, and_59_out);
  and and_58 (and_58_out, d_ff_169_qn, d_ff_104_qn, d_ff_28_qn);
  and and_59 (and_59_out, and_60_out, and_61_out);
  and and_60 (and_60_out, d_ff_170_qn, d_ff_105_qn, d_ff_29_qn);
  and and_61 (and_61_out, and_62_out, and_63_out);
  and and_62 (and_62_out, d_ff_171_qn, d_ff_106_qn, d_ff_30_qn);
  and and_63 (and_63_out, and_64_out, and_65_out);
  and and_64 (and_64_out, d_ff_172_qn, d_ff_107_qn, d_ff_31_qn);
  and and_65 (and_65_out, and_66_out, and_67_out);
  and and_66 (and_66_out, d_ff_173_qn, d_ff_108_qn, d_ff_32_qn);
  and and_67 (and_67_out, and_68_out, and_69_out);
  and and_68 (and_68_out, d_ff_174_qn, d_ff_109_qn, d_ff_33_qn);
  and and_69 (and_69_out, and_70_out, and_71_out);
  and and_70 (and_70_out, d_ff_175_qn, d_ff_110_qn, d_ff_34_qn);
  and and_71 (and_71_out, and_72_out, and_73_out);
  and and_72 (and_72_out, d_ff_176_qn, d_ff_111_qn, d_ff_35_qn);
  and and_73 (and_73_out, and_74_out, and_75_out);
  and and_74 (and_74_out, d_ff_177_qn, d_ff_112_qn, d_ff_36_qn);
  and and_75 (and_75_out, and_76_out, and_77_out);
  and and_76 (and_76_out, d_ff_178_qn, d_ff_113_qn, d_ff_37_qn);
  and and_77 (and_77_out, and_78_out, and_79_out);
  and and_78 (and_78_out, d_ff_179_qn, d_ff_114_qn, d_ff_38_qn);
  and and_79 (and_79_out, and_80_out, and_81_out);
  and and_80 (and_80_out, d_ff_180_qn, d_ff_115_qn, d_ff_39_qn);
  and and_81 (and_81_out, and_82_out, and_83_out);
  and and_82 (and_82_out, d_ff_181_qn, d_ff_116_qn, d_ff_40_qn);
  and and_83 (and_83_out, and_84_out, and_85_out);
  and and_84 (and_84_out, d_ff_182_qn, d_ff_117_qn, d_ff_41_qn);
  and and_85 (and_85_out, and_86_out, and_87_out);
  and and_86 (and_86_out, d_ff_183_qn, d_ff_118_qn, d_ff_42_qn);
  and and_87 (and_87_out, and_88_out, and_89_out);
  and and_88 (and_88_out, d_ff_184_qn, d_ff_119_qn, d_ff_43_qn);
  and and_89 (and_89_out, and_90_out, and_91_out);
  and and_90 (and_90_out, d_ff_185_qn, d_ff_120_qn, d_ff_44_qn);
  and and_91 (and_91_out, and_92_out, and_93_out);
  and and_92 (and_92_out, d_ff_186_qn, d_ff_121_qn, d_ff_45_qn);
  and and_93 (and_93_out, and_94_out, and_95_out);
  and and_94 (and_94_out, d_ff_187_qn, d_ff_122_qn, d_ff_46_qn);
  and and_95 (and_95_out, and_96_out, and_125_out);
  and and_96 (and_96_out, d_ff_188_qn, d_ff_123_qn, d_ff_47_qn);
  or or_510 (d_ff_124_q[3], d_ff_48_q, d_ff_124_q[0]);
  D_Flip_Flop d_ff_217 (.clk(CLK), .D(d_ff_124_q[2]), .Q(d_ff_217_q[5]), .Qn(d_ff_217_qn));  // open: preset, en, reset
  and and_97 (and_97_out, d_ff_217_qn, d_ff_189_qn, d_ff_124_qn, d_ff_48_qn);
  or or_511 (d_ff_125_q[3], d_ff_49_q, d_ff_125_q[0]);
  D_Flip_Flop d_ff_218 (.clk(CLK), .D(d_ff_125_q[2]), .Q(d_ff_218_q[5]), .Qn(d_ff_218_qn));  // open: preset, en, reset
  and and_98 (and_98_out, d_ff_218_qn, d_ff_190_qn, d_ff_125_qn, d_ff_49_qn);
  or or_512 (d_ff_126_q[3], d_ff_50_q, d_ff_126_q[0]);
  D_Flip_Flop d_ff_219 (.clk(CLK), .D(d_ff_126_q[2]), .Q(d_ff_219_q[5]), .Qn(d_ff_219_qn));  // open: preset, en, reset
  and and_99 (and_99_out, d_ff_219_qn, d_ff_191_qn, d_ff_126_qn, d_ff_50_qn);
  or or_513 (d_ff_127_q[3], d_ff_51_q, d_ff_127_q[0]);
  D_Flip_Flop d_ff_220 (.clk(CLK), .D(d_ff_127_q[2]), .Q(d_ff_220_q[5]), .Qn(d_ff_220_qn));  // open: preset, en, reset
  and and_100 (and_100_out, d_ff_220_qn, d_ff_192_qn, d_ff_127_qn, d_ff_51_qn);
  or or_514 (d_ff_128_q[3], d_ff_52_q, d_ff_128_q[0]);
  D_Flip_Flop d_ff_221 (.clk(CLK), .D(d_ff_128_q[2]), .Q(d_ff_221_q[5]), .Qn(d_ff_221_qn));  // open: preset, en, reset
  and and_101 (and_101_out, d_ff_221_qn, d_ff_193_qn, d_ff_128_qn, d_ff_52_qn);
  or or_515 (d_ff_129_q[3], d_ff_53_q, d_ff_129_q[0]);
  D_Flip_Flop d_ff_222 (.clk(CLK), .D(d_ff_129_q[2]), .Q(d_ff_222_q[5]), .Qn(d_ff_222_qn));  // open: preset, en, reset
  and and_102 (and_102_out, d_ff_222_qn, d_ff_194_qn, d_ff_129_qn, d_ff_53_qn);
  or or_516 (d_ff_130_q[3], d_ff_54_q, d_ff_130_q[0]);
  D_Flip_Flop d_ff_223 (.clk(CLK), .D(d_ff_130_q[2]), .Q(d_ff_223_q[5]), .Qn(d_ff_223_qn));  // open: preset, en, reset
  and and_103 (and_103_out, d_ff_223_qn, d_ff_195_qn, d_ff_130_qn, d_ff_54_qn);
  or or_517 (d_ff_131_q[3], d_ff_55_q, d_ff_131_q[0]);
  D_Flip_Flop d_ff_224 (.clk(CLK), .D(d_ff_131_q[2]), .Q(d_ff_224_q[5]), .Qn(d_ff_224_qn));  // open: preset, en, reset
  and and_104 (and_104_out, d_ff_224_qn, d_ff_196_qn, d_ff_131_qn, d_ff_55_qn);
  or or_518 (d_ff_132_q[3], d_ff_56_q, d_ff_132_q[0]);
  D_Flip_Flop d_ff_225 (.clk(CLK), .D(d_ff_132_q[2]), .Q(d_ff_225_q[5]), .Qn(d_ff_225_qn));  // open: preset, en, reset
  and and_105 (and_105_out, d_ff_225_qn, d_ff_197_qn, d_ff_132_qn, d_ff_56_qn);
  or or_519 (d_ff_133_q[3], d_ff_57_q, d_ff_133_q[0]);
  D_Flip_Flop d_ff_226 (.clk(CLK), .D(d_ff_133_q[2]), .Q(d_ff_226_q[5]), .Qn(d_ff_226_qn));  // open: preset, en, reset
  and and_106 (and_106_out, d_ff_226_qn, d_ff_198_qn, d_ff_133_qn, d_ff_57_qn);
  or or_520 (d_ff_134_q[3], d_ff_58_q, d_ff_134_q[0]);
  D_Flip_Flop d_ff_227 (.clk(CLK), .D(d_ff_134_q[2]), .Q(d_ff_227_q[5]), .Qn(d_ff_227_qn));  // open: preset, en, reset
  and and_107 (and_107_out, d_ff_227_qn, d_ff_199_qn, d_ff_134_qn, d_ff_58_qn);
  or or_521 (d_ff_135_q[3], d_ff_59_q, d_ff_135_q[0]);
  D_Flip_Flop d_ff_228 (.clk(CLK), .D(d_ff_135_q[2]), .Q(d_ff_228_q[5]), .Qn(d_ff_228_qn));  // open: preset, en, reset
  and and_108 (and_108_out, d_ff_228_qn, d_ff_200_qn, d_ff_135_qn, d_ff_59_qn);
  or or_522 (d_ff_136_q[3], d_ff_60_q, d_ff_136_q[0]);
  D_Flip_Flop d_ff_229 (.clk(CLK), .D(d_ff_136_q[2]), .Q(d_ff_229_q[5]), .Qn(d_ff_229_qn));  // open: preset, en, reset
  and and_109 (and_109_out, d_ff_229_qn, d_ff_201_qn, d_ff_136_qn, d_ff_60_qn);
  or or_523 (d_ff_137_q[3], d_ff_61_q, d_ff_137_q[0]);
  D_Flip_Flop d_ff_230 (.clk(CLK), .D(d_ff_137_q[2]), .Q(d_ff_230_q[5]), .Qn(d_ff_230_qn));  // open: preset, en, reset
  and and_110 (and_110_out, d_ff_230_qn, d_ff_202_qn, d_ff_137_qn, d_ff_61_qn);
  or or_524 (d_ff_138_q[3], d_ff_62_q, d_ff_138_q[0]);
  D_Flip_Flop d_ff_231 (.clk(CLK), .D(d_ff_138_q[2]), .Q(d_ff_231_q[5]), .Qn(d_ff_231_qn));  // open: preset, en, reset
  and and_111 (and_111_out, d_ff_231_qn, d_ff_203_qn, d_ff_138_qn, d_ff_62_qn);
  or or_525 (d_ff_139_q[3], d_ff_63_q, d_ff_139_q[0]);
  D_Flip_Flop d_ff_232 (.clk(CLK), .D(d_ff_139_q[2]), .Q(d_ff_232_q[5]), .Qn(d_ff_232_qn));  // open: preset, en, reset
  and and_112 (and_112_out, d_ff_232_qn, d_ff_204_qn, d_ff_139_qn, d_ff_63_qn);
  or or_526 (d_ff_64_q[3], d_ff_64_q[0], d_ff_140_q);
  D_Flip_Flop d_ff_233 (.clk(CLK), .D(d_ff_64_q[2]), .Q(d_ff_233_q[5]), .Qn(d_ff_233_qn));  // open: preset, en, reset
  and and_113 (and_113_out, d_ff_233_qn, d_ff_205_qn, d_ff_140_qn, d_ff_64_qn);
  or or_527 (d_ff_65_q[3], d_ff_65_q[0], d_ff_141_q);
  D_Flip_Flop d_ff_234 (.clk(CLK), .D(d_ff_65_q[2]), .Q(d_ff_234_q[5]), .Qn(d_ff_234_qn));  // open: preset, en, reset
  and and_114 (and_114_out, d_ff_234_qn, d_ff_206_qn, d_ff_141_qn, d_ff_65_qn);
  or or_528 (d_ff_66_q[3], d_ff_66_q[0], d_ff_142_q);
  D_Flip_Flop d_ff_235 (.clk(CLK), .D(d_ff_66_q[2]), .Q(d_ff_235_q[5]), .Qn(d_ff_235_qn));  // open: preset, en, reset
  and and_115 (and_115_out, d_ff_235_qn, d_ff_207_qn, d_ff_142_qn, d_ff_66_qn);
  or or_529 (d_ff_67_q[3], d_ff_67_q[0], d_ff_143_q);
  D_Flip_Flop d_ff_236 (.clk(CLK), .D(d_ff_67_q[2]), .Q(d_ff_236_q[5]), .Qn(d_ff_236_qn));  // open: preset, en, reset
  and and_116 (and_116_out, d_ff_236_qn, d_ff_208_qn, d_ff_143_qn, d_ff_67_qn);
  or or_530 (d_ff_68_q[3], d_ff_68_q[0], d_ff_144_q);
  D_Flip_Flop d_ff_237 (.clk(CLK), .D(d_ff_68_q[2]), .Q(d_ff_237_q[5]), .Qn(d_ff_237_qn));  // open: preset, en, reset
  and and_117 (and_117_out, d_ff_237_qn, d_ff_209_qn, d_ff_144_qn, d_ff_68_qn);
  or or_531 (d_ff_69_q[3], d_ff_69_q[0], d_ff_145_q);
  D_Flip_Flop d_ff_238 (.clk(CLK), .D(d_ff_69_q[2]), .Q(d_ff_238_q[5]), .Qn(d_ff_238_qn));  // open: preset, en, reset
  and and_118 (and_118_out, d_ff_238_qn, d_ff_210_qn, d_ff_145_qn, d_ff_69_qn);
  or or_532 (d_ff_70_q[3], d_ff_70_q[0], d_ff_146_q);
  D_Flip_Flop d_ff_239 (.clk(CLK), .D(d_ff_70_q[2]), .Q(d_ff_239_q[5]), .Qn(d_ff_239_qn));  // open: preset, en, reset
  and and_119 (and_119_out, d_ff_239_qn, d_ff_211_qn, d_ff_146_qn, d_ff_70_qn);
  or or_533 (d_ff_71_q[3], d_ff_71_q[0], d_ff_147_q);
  D_Flip_Flop d_ff_240 (.clk(CLK), .D(d_ff_71_q[2]), .Q(d_ff_240_q[5]), .Qn(d_ff_240_qn));  // open: preset, en, reset
  and and_120 (and_120_out, d_ff_240_qn, d_ff_212_qn, d_ff_147_qn, d_ff_71_qn);
  or or_534 (d_ff_72_q[3], d_ff_72_q[0], d_ff_148_q);
  D_Flip_Flop d_ff_241 (.clk(CLK), .D(d_ff_72_q[2]), .Q(d_ff_241_q[5]), .Qn(d_ff_241_qn));  // open: preset, en, reset
  and and_121 (and_121_out, d_ff_241_qn, d_ff_213_qn, d_ff_148_qn, d_ff_72_qn);
  or or_535 (d_ff_73_q[3], d_ff_73_q[0], d_ff_149_q);
  D_Flip_Flop d_ff_242 (.clk(CLK), .D(d_ff_73_q[2]), .Q(d_ff_242_q[5]), .Qn(d_ff_242_qn));  // open: preset, en, reset
  and and_122 (and_122_out, d_ff_242_qn, d_ff_214_qn, d_ff_149_qn, d_ff_73_qn);
  or or_536 (d_ff_74_q[3], d_ff_74_q[0], d_ff_150_q);
  D_Flip_Flop d_ff_243 (.clk(CLK), .D(d_ff_74_q[2]), .Q(d_ff_243_q[5]), .Qn(d_ff_243_qn));  // open: preset, en, reset
  and and_123 (and_123_out, d_ff_243_qn, d_ff_215_qn, d_ff_150_qn, d_ff_74_qn);
  or or_537 (d_ff_75_q[3], d_ff_75_q[0], d_ff_151_q);
  D_Flip_Flop d_ff_244 (.clk(CLK), .D(d_ff_75_q[2]), .Q(d_ff_244_q[5]), .Qn(d_ff_244_qn));  // open: preset, en, reset
  and and_124 (and_124_out, d_ff_244_qn, d_ff_216_qn, d_ff_151_qn, d_ff_75_qn);
  buf or_538 (or_538_out, command_unit_cmp_instruction_1_ram_enable);  // OR_Gate
  and mov_ax_value16 (mov_ax_value16_out, and_154_out[0], ~and_154_out[1], ~and_154_out[2], ~and_154_out[3], ~and_154_out[4], ~and_154_out[5], ~and_154_out[6], ~and_154_out[7], ~and_154_out[8], ~and_154_out[9], ~and_154_out[10], ~and_154_out[11], ~and_154_out[12], ~and_154_out[13], ~and_154_out[14], ~and_154_out[15]);  // AND_Gate
  and mov_bx_value16 (mov_bx_value16_out, ~and_154_out[0], and_154_out[1], ~and_154_out[2], ~and_154_out[3], ~and_154_out[4], ~and_154_out[5], ~and_154_out[6], ~and_154_out[7], ~and_154_out[8], ~and_154_out[9], ~and_154_out[10], ~and_154_out[11], ~and_154_out[12], ~and_154_out[13], ~and_154_out[14], ~and_154_out[15]);  // AND_Gate
  and mov_cx_value16 (mov_cx_value16_out, and_154_out[0], and_154_out[1], ~and_154_out[2], ~and_154_out[3], ~and_154_out[4], ~and_154_out[5], ~and_154_out[6], ~and_154_out[7], ~and_154_out[8], ~and_154_out[9], ~and_154_out[10], ~and_154_out[11], ~and_154_out[12], ~and_154_out[13], ~and_154_out[14], ~and_154_out[15]);  // AND_Gate
  and mov_dx_value16 (mov_dx_value16_out, ~and_154_out[0], ~and_154_out[1], and_154_out[2], ~and_154_out[3], ~and_154_out[4], ~and_154_out[5], ~and_154_out[6], ~and_154_out[7], ~and_154_out[8], ~and_154_out[9], ~and_154_out[10], ~and_154_out[11], ~and_154_out[12], ~and_154_out[13], ~and_154_out[14], ~and_154_out[15]);  // AND_Gate
  and mov_ax_bx (mov_ax_bx_out, and_154_out[0], ~and_154_out[1], and_154_out[2], ~and_154_out[3], ~and_154_out[4], ~and_154_out[5], ~and_154_out[6], ~and_154_out[7], ~and_154_out[8], ~and_154_out[9], ~and_154_out[10], ~and_154_out[11], ~and_154_out[12], ~and_154_out[13], ~and_154_out[14], ~and_154_out[15]);  // AND_Gate
  and mov_ax_cx (mov_ax_cx_out, ~and_154_out[0], and_154_out[1], and_154_out[2], ~and_154_out[3], ~and_154_out[4], ~and_154_out[5], ~and_154_out[6], ~and_154_out[7], ~and_154_out[8], ~and_154_out[9], ~and_154_out[10], ~and_154_out[11], ~and_154_out[12], ~and_154_out[13], ~and_154_out[14], ~and_154_out[15]);  // AND_Gate
  and mov_ax_dx (mov_ax_dx_out, and_154_out[0], and_154_out[1], and_154_out[2], ~and_154_out[3], ~and_154_out[4], ~and_154_out[5], ~and_154_out[6], ~and_154_out[7], ~and_154_out[8], ~and_154_out[9], ~and_154_out[10], ~and_154_out[11], ~and_154_out[12], ~and_154_out[13], ~and_154_out[14], ~and_154_out[15]);  // AND_Gate
  and mov_bx_ax (mov_bx_ax_out, ~and_154_out[0], ~and_154_out[1], ~and_154_out[2], and_154_out[3], ~and_154_out[4], ~and_154_out[5], ~and_154_out[6], ~and_154_out[7], ~and_154_out[8], ~and_154_out[9], ~and_154_out[10], ~and_154_out[11], ~and_154_out[12], ~and_154_out[13], ~and_154_out[14], ~and_154_out[15]);  // AND_Gate
  and mov_bx_cx (mov_bx_cx_out, and_154_out[0], ~and_154_out[1], ~and_154_out[2], and_154_out[3], ~and_154_out[4], ~and_154_out[5], ~and_154_out[6], ~and_154_out[7], ~and_154_out[8], ~and_154_out[9], ~and_154_out[10], ~and_154_out[11], ~and_154_out[12], ~and_154_out[13], ~and_154_out[14], ~and_154_out[15]);  // AND_Gate
  and mov_bx_dx (mov_bx_dx_out, ~and_154_out[0], and_154_out[1], ~and_154_out[2], and_154_out[3], ~and_154_out[4], ~and_154_out[5], ~and_154_out[6], ~and_154_out[7], ~and_154_out[8], ~and_154_out[9], ~and_154_out[10], ~and_154_out[11], ~and_154_out[12], ~and_154_out[13], ~and_154_out[14], ~and_154_out[15]);  // AND_Gate
  and mov_cx_ax (mov_cx_ax_out, and_154_out[0], and_154_out[1], ~and_154_out[2], and_154_out[3], ~and_154_out[4], ~and_154_out[5], ~and_154_out[6], ~and_154_out[7], ~and_154_out[8], ~and_154_out[9], ~and_154_out[10], ~and_154_out[11], ~and_154_out[12], ~and_154_out[13], ~and_154_out[14], ~and_154_out[15]);  // AND_Gate
  and mov_cx_bx (mov_cx_bx_out, ~and_154_out[0], ~and_154_out[1], and_154_out[2], and_154_out[3], ~and_154_out[4], ~and_154_out[5], ~and_154_out[6], ~and_154_out[7], ~and_154_out[8], ~and_154_out[9], ~and_154_out[10], ~and_154_out[11], ~and_154_out[12], ~and_154_out[13], ~and_154_out[14], ~and_154_out[15]);  // AND_Gate
  and mov_cx_dx (mov_cx_dx_out, and_154_out[0], ~and_154_out[1], and_154_out[2], and_154_out[3], ~and_154_out[4], ~and_154_out[5], ~and_154_out[6], ~and_154_out[7], ~and_154_out[8], ~and_154_out[9], ~and_154_out[10], ~and_154_out[11], ~and_154_out[12], ~and_154_out[13], ~and_154_out[14], ~and_154_out[15]);  // AND_Gate
  and mov_dx_ax (mov_dx_ax_out, ~and_154_out[0], and_154_out[1], and_154_out[2], and_154_out[3], ~and_154_out[4], ~and_154_out[5], ~and_154_out[6], ~and_154_out[7], ~and_154_out[8], ~and_154_out[9], ~and_154_out[10], ~and_154_out[11], ~and_154_out[12], ~and_154_out[13], ~and_154_out[14], ~and_154_out[15]);  // AND_Gate
  and mov_dx_bx (mov_dx_bx_out, and_154_out[0], and_154_out[1], and_154_out[2], and_154_out[3], ~and_154_out[4], ~and_154_out[5], ~and_154_out[6], ~and_154_out[7], ~and_154_out[8], ~and_154_out[9], ~and_154_out[10], ~and_154_out[11], ~and_154_out[12], ~and_154_out[13], ~and_154_out[14], ~and_154_out[15]);  // AND_Gate
  and mov_dx_cx (mov_dx_cx_out, ~and_154_out[0], ~and_154_out[1], ~and_154_out[2], ~and_154_out[3], and_154_out[4], ~and_154_out[5], ~and_154_out[6], ~and_154_out[7], ~and_154_out[8], ~and_154_out[9], ~and_154_out[10], ~and_154_out[11], ~and_154_out[12], ~and_154_out[13], ~and_154_out[14], ~and_154_out[15]);  // AND_Gate
  and mov_ax__ax (mov_ax__ax_out, and_154_out[0], ~and_154_out[1], ~and_154_out[2], ~and_154_out[3], and_154_out[4], ~and_154_out[5], ~and_154_out[6], ~and_154_out[7], ~and_154_out[8], ~and_154_out[9], ~and_154_out[10], ~and_154_out[11], ~and_154_out[12], ~and_154_out[13], ~and_154_out[14], ~and_154_out[15]);  // AND_Gate
  and mov_ax__bx (mov_ax__bx_out, ~and_154_out[0], and_154_out[1], ~and_154_out[2], ~and_154_out[3], and_154_out[4], ~and_154_out[5], ~and_154_out[6], ~and_154_out[7], ~and_154_out[8], ~and_154_out[9], ~and_154_out[10], ~and_154_out[11], ~and_154_out[12], ~and_154_out[13], ~and_154_out[14], ~and_154_out[15]);  // AND_Gate
  and mov_ax__cx (mov_ax__cx_out, and_154_out[0], and_154_out[1], ~and_154_out[2], ~and_154_out[3], and_154_out[4], ~and_154_out[5], ~and_154_out[6], ~and_154_out[7], ~and_154_out[8], ~and_154_out[9], ~and_154_out[10], ~and_154_out[11], ~and_154_out[12], ~and_154_out[13], ~and_154_out[14], ~and_154_out[15]);  // AND_Gate
  and mov_ax__dx (mov_ax__dx_out, ~and_154_out[0], ~and_154_out[1], and_154_out[2], ~and_154_out[3], and_154_out[4], ~and_154_out[5], ~and_154_out[6], ~and_154_out[7], ~and_154_out[8], ~and_154_out[9], ~and_154_out[10], ~and_154_out[11], ~and_154_out[12], ~and_154_out[13], ~and_154_out[14], ~and_154_out[15]);  // AND_Gate
  and mov_bx__ax (mov_bx__ax_out, and_154_out[0], ~and_154_out[1], and_154_out[2], ~and_154_out[3], and_154_out[4], ~and_154_out[5], ~and_154_out[6], ~and_154_out[7], ~and_154_out[8], ~and_154_out[9], ~and_154_out[10], ~and_154_out[11], ~and_154_out[12], ~and_154_out[13], ~and_154_out[14], ~and_154_out[15]);  // AND_Gate
  and mov_bx__bx (mov_bx__bx_out, ~and_154_out[0], and_154_out[1], ~and_154_out[2], and_154_out[3], and_154_out[4], ~and_154_out[5], ~and_154_out[6], ~and_154_out[7], ~and_154_out[8], ~and_154_out[9], ~and_154_out[10], ~and_154_out[11], ~and_154_out[12], ~and_154_out[13], ~and_154_out[14], ~and_154_out[15]);  // AND_Gate
  and mov_bx__cx (mov_bx__cx_out, and_154_out[0], and_154_out[1], ~and_154_out[2], and_154_out[3], and_154_out[4], ~and_154_out[5], ~and_154_out[6], ~and_154_out[7], ~and_154_out[8], ~and_154_out[9], ~and_154_out[10], ~and_154_out[11], ~and_154_out[12], ~and_154_out[13], ~and_154_out[14], ~and_154_out[15]);  // AND_Gate
  and mov_bx__dx (mov_bx__dx_out, ~and_154_out[0], ~and_154_out[1], ~and_154_out[2], and_154_out[3], and_154_out[4], ~and_154_out[5], ~and_154_out[6], ~and_154_out[7], ~and_154_out[8], ~and_154_out[9], ~and_154_out[10], ~and_154_out[11], ~and_154_out[12], ~and_154_out[13], ~and_154_out[14], ~and_154_out[15]);  // AND_Gate
  and mov_cx__ax (mov_cx__ax_out, and_154_out[0], ~and_154_out[1], ~and_154_out[2], and_154_out[3], and_154_out[4], ~and_154_out[5], ~and_154_out[6], ~and_154_out[7], ~and_154_out[8], ~and_154_out[9], ~and_154_out[10], ~and_154_out[11], ~and_154_out[12], ~and_154_out[13], ~and_154_out[14], ~and_154_out[15]);  // AND_Gate
  and mov_cx__bx (mov_cx__bx_out, ~and_154_out[0], and_154_out[1], ~and_154_out[2], and_154_out[3], and_154_out[4], ~and_154_out[5], ~and_154_out[6], ~and_154_out[7], ~and_154_out[8], ~and_154_out[9], ~and_154_out[10], ~and_154_out[11], ~and_154_out[12], ~and_154_out[13], ~and_154_out[14], ~and_154_out[15]);  // AND_Gate
  and mov_cx__cx (mov_cx__cx_out, and_154_out[0], and_154_out[1], ~and_154_out[2], and_154_out[3], and_154_out[4], ~and_154_out[5], ~and_154_out[6], ~and_154_out[7], ~and_154_out[8], ~and_154_out[9], ~and_154_out[10], ~and_154_out[11], ~and_154_out[12], ~and_154_out[13], ~and_154_out[14], ~and_154_out[15]);  // AND_Gate
  and mov_cx__dx (mov_cx__dx_out, ~and_154_out[0], ~and_154_out[1], and_154_out[2], and_154_out[3], and_154_out[4], ~and_154_out[5], ~and_154_out[6], ~and_154_out[7], ~and_154_out[8], ~and_154_out[9], ~and_154_out[10], ~and_154_out[11], ~and_154_out[12], ~and_154_out[13], ~and_154_out[14], ~and_154_out[15]);  // AND_Gate
  and mov_dx__ax (mov_dx__ax_out, and_154_out[0], ~and_154_out[1], and_154_out[2], and_154_out[3], and_154_out[4], ~and_154_out[5], ~and_154_out[6], ~and_154_out[7], ~and_154_out[8], ~and_154_out[9], ~and_154_out[10], ~and_154_out[11], ~and_154_out[12], ~and_154_out[13], ~and_154_out[14], ~and_154_out[15]);  // AND_Gate
  and mov_dx__bx (mov_dx__bx_out, ~and_154_out[0], and_154_out[1], and_154_out[2], and_154_out[3], and_154_out[4], ~and_154_out[5], ~and_154_out[6], ~and_154_out[7], ~and_154_out[8], ~and_154_out[9], ~and_154_out[10], ~and_154_out[11], ~and_154_out[12], ~and_154_out[13], ~and_154_out[14], ~and_154_out[15]);  // AND_Gate
  and mov_dx__cx (mov_dx__cx_out, and_154_out[0], and_154_out[1], and_154_out[2], and_154_out[3], and_154_out[4], ~and_154_out[5], ~and_154_out[6], ~and_154_out[7], ~and_154_out[8], ~and_154_out[9], ~and_154_out[10], ~and_154_out[11], ~and_154_out[12], ~and_154_out[13], ~and_154_out[14], ~and_154_out[15]);  // AND_Gate
  and mov_dx__dx (mov_dx__dx_out, ~and_154_out[0], ~and_154_out[1], ~and_154_out[2], ~and_154_out[3], ~and_154_out[4], and_154_out[5], ~and_154_out[6], ~and_154_out[7], ~and_154_out[8], ~and_154_out[9], ~and_154_out[10], ~and_154_out[11], ~and_154_out[12], ~and_154_out[13], ~and_154_out[14], ~and_154_out[15]);  // AND_Gate
  and mov__ax__ax (mov__ax__ax_out, and_154_out[0], ~and_154_out[1], ~and_154_out[2], ~and_154_out[3], ~and_154_out[4], and_154_out[5], ~and_154_out[6], ~and_154_out[7], ~and_154_out[8], ~and_154_out[9], ~and_154_out[10], ~and_154_out[11], ~and_154_out[12], ~and_154_out[13], ~and_154_out[14], ~and_154_out[15]);  // AND_Gate
  and mov__ax__bx (mov__ax__bx_out, ~and_154_out[0], and_154_out[1], ~and_154_out[2], ~and_154_out[3], ~and_154_out[4], and_154_out[5], ~and_154_out[6], ~and_154_out[7], ~and_154_out[8], ~and_154_out[9], ~and_154_out[10], ~and_154_out[11], ~and_154_out[12], ~and_154_out[13], ~and_154_out[14], ~and_154_out[15]);  // AND_Gate
  and mov__ax__cx (mov__ax__cx_out, and_154_out[0], and_154_out[1], ~and_154_out[2], ~and_154_out[3], ~and_154_out[4], and_154_out[5], ~and_154_out[6], ~and_154_out[7], ~and_154_out[8], ~and_154_out[9], ~and_154_out[10], ~and_154_out[11], ~and_154_out[12], ~and_154_out[13], ~and_154_out[14], ~and_154_out[15]);  // AND_Gate
  and mov__ax__dx (mov__ax__dx_out, ~and_154_out[0], ~and_154_out[1], and_154_out[2], ~and_154_out[3], ~and_154_out[4], and_154_out[5], ~and_154_out[6], ~and_154_out[7], ~and_154_out[8], ~and_154_out[9], ~and_154_out[10], ~and_154_out[11], ~and_154_out[12], ~and_154_out[13], ~and_154_out[14], ~and_154_out[15]);  // AND_Gate
  and mov__bx__ax (mov__bx__ax_out, and_154_out[0], ~and_154_out[1], and_154_out[2], ~and_154_out[3], ~and_154_out[4], and_154_out[5], ~and_154_out[6], ~and_154_out[7], ~and_154_out[8], ~and_154_out[9], ~and_154_out[10], ~and_154_out[11], ~and_154_out[12], ~and_154_out[13], ~and_154_out[14], ~and_154_out[15]);  // AND_Gate
  and mov__bx__bx (mov__bx__bx_out, ~and_154_out[0], and_154_out[1], and_154_out[2], ~and_154_out[3], ~and_154_out[4], and_154_out[5], ~and_154_out[6], ~and_154_out[7], ~and_154_out[8], ~and_154_out[9], ~and_154_out[10], ~and_154_out[11], ~and_154_out[12], ~and_154_out[13], ~and_154_out[14], ~and_154_out[15]);  // AND_Gate
  and mov__bx__cx (mov__bx__cx_out, and_154_out[0], and_154_out[1], and_154_out[2], ~and_154_out[3], ~and_154_out[4], and_154_out[5], ~and_154_out[6], ~and_154_out[7], ~and_154_out[8], ~and_154_out[9], ~and_154_out[10], ~and_154_out[11], ~and_154_out[12], ~and_154_out[13], ~and_154_out[14], ~and_154_out[15]);  // AND_Gate
  and mov__bx__dx (mov__bx__dx_out, ~and_154_out[0], ~and_154_out[1], ~and_154_out[2], and_154_out[3], ~and_154_out[4], and_154_out[5], ~and_154_out[6], ~and_154_out[7], ~and_154_out[8], ~and_154_out[9], ~and_154_out[10], ~and_154_out[11], ~and_154_out[12], ~and_154_out[13], ~and_154_out[14], ~and_154_out[15]);  // AND_Gate
  and mov__cx__ax (mov__cx__ax_out, and_154_out[0], ~and_154_out[1], ~and_154_out[2], and_154_out[3], ~and_154_out[4], and_154_out[5], ~and_154_out[6], ~and_154_out[7], ~and_154_out[8], ~and_154_out[9], ~and_154_out[10], ~and_154_out[11], ~and_154_out[12], ~and_154_out[13], ~and_154_out[14], ~and_154_out[15]);  // AND_Gate
  and mov__cx__bx (mov__cx__bx_out, ~and_154_out[0], and_154_out[1], ~and_154_out[2], and_154_out[3], ~and_154_out[4], and_154_out[5], ~and_154_out[6], ~and_154_out[7], ~and_154_out[8], ~and_154_out[9], ~and_154_out[10], ~and_154_out[11], ~and_154_out[12], ~and_154_out[13], ~and_154_out[14], ~and_154_out[15]);  // AND_Gate
  and mov__cx__cx (mov__cx__cx_out, and_154_out[0], and_154_out[1], ~and_154_out[2], and_154_out[3], ~and_154_out[4], and_154_out[5], ~and_154_out[6], ~and_154_out[7], ~and_154_out[8], ~and_154_out[9], ~and_154_out[10], ~and_154_out[11], ~and_154_out[12], ~and_154_out[13], ~and_154_out[14], ~and_154_out[15]);  // AND_Gate
  and mov__cx__dx (mov__cx__dx_out, ~and_154_out[0], ~and_154_out[1], and_154_out[2], and_154_out[3], ~and_154_out[4], and_154_out[5], ~and_154_out[6], ~and_154_out[7], ~and_154_out[8], ~and_154_out[9], ~and_154_out[10], ~and_154_out[11], ~and_154_out[12], ~and_154_out[13], ~and_154_out[14], ~and_154_out[15]);  // AND_Gate
  and mov__dx__ax (mov__dx__ax_out, and_154_out[0], ~and_154_out[1], and_154_out[2], and_154_out[3], ~and_154_out[4], and_154_out[5], ~and_154_out[6], ~and_154_out[7], ~and_154_out[8], ~and_154_out[9], ~and_154_out[10], ~and_154_out[11], ~and_154_out[12], ~and_154_out[13], ~and_154_out[14], ~and_154_out[15]);  // AND_Gate
  and mov__dx__bx (mov__dx__bx_out, ~and_154_out[0], and_154_out[1], and_154_out[2], and_154_out[3], ~and_154_out[4], and_154_out[5], ~and_154_out[6], ~and_154_out[7], ~and_154_out[8], ~and_154_out[9], ~and_154_out[10], ~and_154_out[11], ~and_154_out[12], ~and_154_out[13], ~and_154_out[14], ~and_154_out[15]);  // AND_Gate
  and mov__dx__cx (mov__dx__cx_out, and_154_out[0], and_154_out[1], and_154_out[2], and_154_out[3], ~and_154_out[4], and_154_out[5], ~and_154_out[6], ~and_154_out[7], ~and_154_out[8], ~and_154_out[9], ~and_154_out[10], ~and_154_out[11], ~and_154_out[12], ~and_154_out[13], ~and_154_out[14], ~and_154_out[15]);  // AND_Gate
  and mov__dx__dx (mov__dx__dx_out, ~and_154_out[0], ~and_154_out[1], ~and_154_out[2], ~and_154_out[3], and_154_out[4], and_154_out[5], ~and_154_out[6], ~and_154_out[7], ~and_154_out[8], ~and_154_out[9], ~and_154_out[10], ~and_154_out[11], ~and_154_out[12], ~and_154_out[13], ~and_154_out[14], ~and_154_out[15]);  // AND_Gate
  and and_125 (and_125_out, and_97_out, and_126_out);
  and add_ax_ax (add_ax_ax_out, and_154_out[0], ~and_154_out[1], ~and_154_out[2], ~and_154_out[3], and_154_out[4], and_154_out[5], ~and_154_out[6], ~and_154_out[7], ~and_154_out[8], ~and_154_out[9], ~and_154_out[10], ~and_154_out[11], ~and_154_out[12], ~and_154_out[13], ~and_154_out[14], ~and_154_out[15]);  // AND_Gate
  assign or_539_out = {d_ff_125_q[3:2], 1'b0, d_ff_125_q[0]} | or_540_out;  // OR_Gate or_539, 4 bits wide
  and and_126 (and_126_out, and_98_out, and_127_out);
  and add_ax_bx (add_ax_bx_out, ~and_154_out[0], and_154_out[1], ~and_154_out[2], ~and_154_out[3], and_154_out[4], and_154_out[5], ~and_154_out[6], ~and_154_out[7], ~and_154_out[8], ~and_154_out[9], ~and_154_out[10], ~and_154_out[11], ~and_154_out[12], ~and_154_out[13], ~and_154_out[14], ~and_154_out[15]);  // AND_Gate
  assign or_540_out = {d_ff_126_q[3:2], 1'b0, d_ff_126_q[0]} | or_541_out;  // OR_Gate or_540, 4 bits wide
  and and_127 (and_127_out, and_99_out, and_128_out);
  and add_ax_cx (add_ax_cx_out, and_154_out[0], and_154_out[1], ~and_154_out[2], ~and_154_out[3], and_154_out[4], and_154_out[5], ~and_154_out[6], ~and_154_out[7], ~and_154_out[8], ~and_154_out[9], ~and_154_out[10], ~and_154_out[11], ~and_154_out[12], ~and_154_out[13], ~and_154_out[14], ~and_154_out[15]);  // AND_Gate
  assign or_541_out = {d_ff_127_q[3:2], 1'b0, d_ff_127_q[0]} | or_542_out;  // OR_Gate or_541, 4 bits wide
  and and_128 (and_128_out, and_100_out, and_129_out);
  and add_ax_dx (add_ax_dx_out, ~and_154_out[0], ~and_154_out[1], and_154_out[2], ~and_154_out[3], and_154_out[4], and_154_out[5], ~and_154_out[6], ~and_154_out[7], ~and_154_out[8], ~and_154_out[9], ~and_154_out[10], ~and_154_out[11], ~and_154_out[12], ~and_154_out[13], ~and_154_out[14], ~and_154_out[15]);  // AND_Gate
  assign or_542_out = {d_ff_128_q[3:2], 1'b0, d_ff_128_q[0]} | or_543_out;  // OR_Gate or_542, 4 bits wide
  and and_129 (and_129_out, and_101_out, and_130_out);
  and add_bx_ax (add_bx_ax_out, and_154_out[0], ~and_154_out[1], and_154_out[2], ~and_154_out[3], and_154_out[4], and_154_out[5], ~and_154_out[6], ~and_154_out[7], ~and_154_out[8], ~and_154_out[9], ~and_154_out[10], ~and_154_out[11], ~and_154_out[12], ~and_154_out[13], ~and_154_out[14], ~and_154_out[15]);  // AND_Gate
  assign or_543_out = {d_ff_129_q[3:2], 1'b0, d_ff_129_q[0]} | or_544_out;  // OR_Gate or_543, 4 bits wide
  and and_130 (and_130_out, and_102_out, and_131_out);
  and add_bx_bx (add_bx_bx_out, ~and_154_out[0], and_154_out[1], and_154_out[2], ~and_154_out[3], and_154_out[4], and_154_out[5], ~and_154_out[6], ~and_154_out[7], ~and_154_out[8], ~and_154_out[9], ~and_154_out[10], ~and_154_out[11], ~and_154_out[12], ~and_154_out[13], ~and_154_out[14], ~and_154_out[15]);  // AND_Gate
  assign or_544_out = {d_ff_130_q[3:2], 1'b0, d_ff_130_q[0]} | or_545_out;  // OR_Gate or_544, 4 bits wide
  and and_131 (and_131_out, and_103_out, and_132_out);
  and add_bx_cx (add_bx_cx_out, and_154_out[0], and_154_out[1], and_154_out[2], ~and_154_out[3], and_154_out[4], and_154_out[5], ~and_154_out[6], ~and_154_out[7], ~and_154_out[8], ~and_154_out[9], ~and_154_out[10], ~and_154_out[11], ~and_154_out[12], ~and_154_out[13], ~and_154_out[14], ~and_154_out[15]);  // AND_Gate
  assign or_545_out = {d_ff_131_q[3:2], 1'b0, d_ff_131_q[0]} | or_546_out;  // OR_Gate or_545, 4 bits wide
  and and_132 (and_132_out, and_104_out, and_133_out);
  and add_bx_dx (add_bx_dx_out, ~and_154_out[0], ~and_154_out[1], ~and_154_out[2], and_154_out[3], and_154_out[4], and_154_out[5], ~and_154_out[6], ~and_154_out[7], ~and_154_out[8], ~and_154_out[9], ~and_154_out[10], ~and_154_out[11], ~and_154_out[12], ~and_154_out[13], ~and_154_out[14], ~and_154_out[15]);  // AND_Gate
  assign or_546_out = {d_ff_132_q[3:2], 1'b0, d_ff_132_q[0]} | or_547_out;  // OR_Gate or_546, 4 bits wide
  and and_133 (and_133_out, and_105_out, and_134_out);
  and add_cx_ax (add_cx_ax_out, and_154_out[0], ~and_154_out[1], ~and_154_out[2], and_154_out[3], and_154_out[4], and_154_out[5], ~and_154_out[6], ~and_154_out[7], ~and_154_out[8], ~and_154_out[9], ~and_154_out[10], ~and_154_out[11], ~and_154_out[12], ~and_154_out[13], ~and_154_out[14], ~and_154_out[15]);  // AND_Gate
  assign or_547_out = {d_ff_133_q[3:2], 1'b0, d_ff_133_q[0]} | or_548_out;  // OR_Gate or_547, 4 bits wide
  and and_134 (and_134_out, and_106_out, and_135_out);
  and add_cx_bx (add_cx_bx_out, ~and_154_out[0], and_154_out[1], ~and_154_out[2], and_154_out[3], and_154_out[4], and_154_out[5], ~and_154_out[6], ~and_154_out[7], ~and_154_out[8], ~and_154_out[9], ~and_154_out[10], ~and_154_out[11], ~and_154_out[12], ~and_154_out[13], ~and_154_out[14], ~and_154_out[15]);  // AND_Gate
  assign or_548_out = {d_ff_134_q[3:2], 1'b0, d_ff_134_q[0]} | or_549_out;  // OR_Gate or_548, 4 bits wide
  and and_135 (and_135_out, and_107_out, and_136_out);
  and add_cx_cx (add_cx_cx_out, and_154_out[0], and_154_out[1], ~and_154_out[2], and_154_out[3], and_154_out[4], and_154_out[5], ~and_154_out[6], ~and_154_out[7], ~and_154_out[8], ~and_154_out[9], ~and_154_out[10], ~and_154_out[11], ~and_154_out[12], ~and_154_out[13], ~and_154_out[14], ~and_154_out[15]);  // AND_Gate
  assign or_549_out = {d_ff_135_q[3:2], 1'b0, d_ff_135_q[0]} | or_550_out;  // OR_Gate or_549, 4 bits wide
  and and_136 (and_136_out, and_108_out, and_137_out);
  and add_cx_dx (add_cx_dx_out, ~and_154_out[0], ~and_154_out[1], and_154_out[2], and_154_out[3], and_154_out[4], and_154_out[5], ~and_154_out[6], ~and_154_out[7], ~and_154_out[8], ~and_154_out[9], ~and_154_out[10], ~and_154_out[11], ~and_154_out[12], ~and_154_out[13], ~and_154_out[14], ~and_154_out[15]);  // AND_Gate
  assign or_550_out = {d_ff_136_q[3:2], 1'b0, d_ff_136_q[0]} | or_551_out;  // OR_Gate or_550, 4 bits wide
  and and_137 (and_137_out, and_109_out, and_138_out);
  and add_dx_ax (add_dx_ax_out, and_154_out[0], ~and_154_out[1], and_154_out[2], and_154_out[3], and_154_out[4], and_154_out[5], ~and_154_out[6], ~and_154_out[7], ~and_154_out[8], ~and_154_out[9], ~and_154_out[10], ~and_154_out[11], ~and_154_out[12], ~and_154_out[13], ~and_154_out[14], ~and_154_out[15]);  // AND_Gate
  assign or_551_out = {d_ff_137_q[3:2], 1'b0, d_ff_137_q[0]} | or_552_out;  // OR_Gate or_551, 4 bits wide
  and and_138 (and_138_out, and_110_out, and_139_out);
  and add_dx_bx (add_dx_bx_out, ~and_154_out[0], and_154_out[1], and_154_out[2], and_154_out[3], and_154_out[4], and_154_out[5], ~and_154_out[6], ~and_154_out[7], ~and_154_out[8], ~and_154_out[9], ~and_154_out[10], ~and_154_out[11], ~and_154_out[12], ~and_154_out[13], ~and_154_out[14], ~and_154_out[15]);  // AND_Gate
  assign or_552_out = {d_ff_138_q[3:2], 1'b0, d_ff_138_q[0]} | or_553_out;  // OR_Gate or_552, 4 bits wide
  and and_139 (and_139_out, and_111_out, and_140_out);
  and add_dx_cx (add_dx_cx_out, and_154_out[0], and_154_out[1], and_154_out[2], and_154_out[3], and_154_out[4], and_154_out[5], ~and_154_out[6], ~and_154_out[7], ~and_154_out[8], ~and_154_out[9], ~and_154_out[10], ~and_154_out[11], ~and_154_out[12], ~and_154_out[13], ~and_154_out[14], ~and_154_out[15]);  // AND_Gate
  assign or_553_out = {d_ff_139_q[3:2], 1'b0, d_ff_139_q[0]} | or_554_out;  // OR_Gate or_553, 4 bits wide
  and and_140 (and_140_out, and_112_out, and_141_out);
  and add_dx_dx (add_dx_dx_out, ~and_154_out[0], ~and_154_out[1], ~and_154_out[2], ~and_154_out[3], ~and_154_out[4], ~and_154_out[5], and_154_out[6], ~and_154_out[7], ~and_154_out[8], ~and_154_out[9], ~and_154_out[10], ~and_154_out[11], ~and_154_out[12], ~and_154_out[13], ~and_154_out[14], ~and_154_out[15]);  // AND_Gate
  assign or_554_out = {d_ff_64_q[3:2], d_ff_64_q[2], d_ff_64_q[0]} | or_555_out;  // OR_Gate or_554, 4 bits wide
  and and_141 (and_141_out, and_113_out, and_142_out);
  and sub_ax_bx (sub_ax_bx_out, and_154_out[0], ~and_154_out[1], ~and_154_out[2], ~and_154_out[3], ~and_154_out[4], ~and_154_out[5], and_154_out[6], ~and_154_out[7], ~and_154_out[8], ~and_154_out[9], ~and_154_out[10], ~and_154_out[11], ~and_154_out[12], ~and_154_out[13], ~and_154_out[14], ~and_154_out[15]);  // AND_Gate
  assign or_555_out = {d_ff_65_q[3:2], d_ff_65_q[2], d_ff_65_q[0]} | or_556_out;  // OR_Gate or_555, 4 bits wide
  and and_142 (and_142_out, and_114_out, and_143_out);
  and sub_ax_cx (sub_ax_cx_out, ~and_154_out[0], and_154_out[1], ~and_154_out[2], ~and_154_out[3], ~and_154_out[4], ~and_154_out[5], and_154_out[6], ~and_154_out[7], ~and_154_out[8], ~and_154_out[9], ~and_154_out[10], ~and_154_out[11], ~and_154_out[12], ~and_154_out[13], ~and_154_out[14], ~and_154_out[15]);  // AND_Gate
  assign or_556_out = {d_ff_66_q[3:2], d_ff_66_q[2], d_ff_66_q[0]} | or_557_out;  // OR_Gate or_556, 4 bits wide
  and and_143 (and_143_out, and_115_out, and_144_out);
  and sub_ax_dx (sub_ax_dx_out, and_154_out[0], and_154_out[1], ~and_154_out[2], ~and_154_out[3], ~and_154_out[4], ~and_154_out[5], and_154_out[6], ~and_154_out[7], ~and_154_out[8], ~and_154_out[9], ~and_154_out[10], ~and_154_out[11], ~and_154_out[12], ~and_154_out[13], ~and_154_out[14], ~and_154_out[15]);  // AND_Gate
  assign or_557_out = {d_ff_67_q[3:2], d_ff_67_q[2], d_ff_67_q[0]} | or_558_out;  // OR_Gate or_557, 4 bits wide
  and and_144 (and_144_out, and_116_out, and_145_out);
  and sub_bx_ax (sub_bx_ax_out, ~and_154_out[0], ~and_154_out[1], and_154_out[2], ~and_154_out[3], ~and_154_out[4], ~and_154_out[5], and_154_out[6], ~and_154_out[7], ~and_154_out[8], ~and_154_out[9], ~and_154_out[10], ~and_154_out[11], ~and_154_out[12], ~and_154_out[13], ~and_154_out[14], ~and_154_out[15]);  // AND_Gate
  assign or_558_out = {d_ff_68_q[3:2], d_ff_68_q[2], d_ff_68_q[0]} | or_559_out;  // OR_Gate or_558, 4 bits wide
  and and_145 (and_145_out, and_117_out, and_146_out);
  and sub_bx_cx (sub_bx_cx_out, and_154_out[0], ~and_154_out[1], and_154_out[2], ~and_154_out[3], ~and_154_out[4], ~and_154_out[5], and_154_out[6], ~and_154_out[7], ~and_154_out[8], ~and_154_out[9], ~and_154_out[10], ~and_154_out[11], ~and_154_out[12], ~and_154_out[13], ~and_154_out[14], ~and_154_out[15]);  // AND_Gate
  assign or_559_out = {d_ff_69_q[3:2], d_ff_69_q[2], d_ff_69_q[0]} | or_560_out;  // OR_Gate or_559, 4 bits wide
  and and_146 (and_146_out, and_118_out, and_147_out);
  and sub_bx_dx (sub_bx_dx_out, ~and_154_out[0], and_154_out[1], and_154_out[2], ~and_154_out[3], ~and_154_out[4], ~and_154_out[5], and_154_out[6], ~and_154_out[7], ~and_154_out[8], ~and_154_out[9], ~and_154_out[10], ~and_154_out[11], ~and_154_out[12], ~and_154_out[13], ~and_154_out[14], ~and_154_out[15]);  // AND_Gate
  assign or_560_out = {d_ff_70_q[3:2], d_ff_70_q[2], d_ff_70_q[0]} | or_561_out;  // OR_Gate or_560, 4 bits wide
  and and_147 (and_147_out, and_119_out, and_148_out);
  and sub_cx_ax (sub_cx_ax_out, and_154_out[0], and_154_out[1], and_154_out[2], ~and_154_out[3], ~and_154_out[4], ~and_154_out[5], and_154_out[6], ~and_154_out[7], ~and_154_out[8], ~and_154_out[9], ~and_154_out[10], ~and_154_out[11], ~and_154_out[12], ~and_154_out[13], ~and_154_out[14], ~and_154_out[15]);  // AND_Gate
  assign or_561_out = {d_ff_71_q[3:2], d_ff_71_q[2], d_ff_71_q[0]} | or_562_out;  // OR_Gate or_561, 4 bits wide
  and and_148 (and_148_out, and_120_out, and_149_out);
  and sub_cx_bx (sub_cx_bx_out, ~and_154_out[0], ~and_154_out[1], ~and_154_out[2], and_154_out[3], ~and_154_out[4], ~and_154_out[5], and_154_out[6], ~and_154_out[7], ~and_154_out[8], ~and_154_out[9], ~and_154_out[10], ~and_154_out[11], ~and_154_out[12], ~and_154_out[13], ~and_154_out[14], ~and_154_out[15]);  // AND_Gate
  assign or_562_out = {d_ff_72_q[3:2], d_ff_72_q[2], d_ff_72_q[0]} | or_563_out;  // OR_Gate or_562, 4 bits wide
  and and_149 (and_149_out, and_121_out, and_150_out);
  and sub_cx_dx (sub_cx_dx_out, and_154_out[0], ~and_154_out[1], ~and_154_out[2], and_154_out[3], ~and_154_out[4], ~and_154_out[5], and_154_out[6], ~and_154_out[7], ~and_154_out[8], ~and_154_out[9], ~and_154_out[10], ~and_154_out[11], ~and_154_out[12], ~and_154_out[13], ~and_154_out[14], ~and_154_out[15]);  // AND_Gate
  assign or_563_out = {d_ff_73_q[3:2], d_ff_73_q[2], d_ff_73_q[0]} | or_564_out;  // OR_Gate or_563, 4 bits wide
  and and_150 (and_150_out, and_122_out, and_151_out);
  and sub_dx_ax (sub_dx_ax_out, ~and_154_out[0], and_154_out[1], ~and_154_out[2], and_154_out[3], ~and_154_out[4], ~and_154_out[5], and_154_out[6], ~and_154_out[7], ~and_154_out[8], ~and_154_out[9], ~and_154_out[10], ~and_154_out[11], ~and_154_out[12], ~and_154_out[13], ~and_154_out[14], ~and_154_out[15]);  // AND_Gate
  assign or_564_out = {d_ff_74_q[3:2], d_ff_74_q[2], d_ff_74_q[0]} | or_565_out;  // OR_Gate or_564, 4 bits wide
  and and_151 (and_151_out, and_123_out, and_152_out);
  and sub_dx_bx (sub_dx_bx_out, and_154_out[0], and_154_out[1], ~and_154_out[2], and_154_out[3], ~and_154_out[4], ~and_154_out[5], and_154_out[6], ~and_154_out[7], ~and_154_out[8], ~and_154_out[9], ~and_154_out[10], ~and_154_out[11], ~and_154_out[12], ~and_154_out[13], ~and_154_out[14], ~and_154_out[15]);  // AND_Gate
  assign or_565_out = {d_ff_75_q[3:2], d_ff_75_q[2], d_ff_75_q[0]};  // OR_Gate or_565, 4 bits wide OR_Gate
  and and_152 (and_152_out, and_124_out, and_153_out);
  and sub_dx_cx (sub_dx_cx_out, ~and_154_out[0], ~and_154_out[1], and_154_out[2], and_154_out[3], ~and_154_out[4], ~and_154_out[5], and_154_out[6], ~and_154_out[7], ~and_154_out[8], ~and_154_out[9], ~and_154_out[10], ~and_154_out[11], ~and_154_out[12], ~and_154_out[13], ~and_154_out[14], ~and_154_out[15]);  // AND_Gate
  buf and_153 (and_153_out, command_unit_cmp_instruction_1_running_instruction);  // AND_Gate
  and cmp_ax_bx (cmp_ax_bx_out, and_154_out[0], ~and_154_out[1], and_154_out[2], and_154_out[3], ~and_154_out[4], ~and_154_out[5], and_154_out[6], ~and_154_out[7], ~and_154_out[8], ~and_154_out[9], ~and_154_out[10], ~and_154_out[11], ~and_154_out[12], ~and_154_out[13], ~and_154_out[14], ~and_154_out[15]);  // AND_Gate
  // AND_Gate cmp_ax_cx has open pins: in0=and_154_out[0], in1=and_154_out[1], in2=and_154_out[2], in3=and_154_out[3], in4=and_154_out[4], in5=and_154_out[5], in6=and_154_out[6], in7=and_154_out[7], in8=and_154_out[8], in9=and_154_out[9], in10=and_154_out[10], in11=and_154_out[11], in12=and_154_out[12], in13=and_154_out[13], in14=and_154_out[14], in15=and_154_out[15], out=open
  // AND_Gate cmp_ax_dx has open pins: in0=and_154_out[0], in1=and_154_out[1], in2=and_154_out[2], in3=and_154_out[3], in4=and_154_out[4], in5=and_154_out[5], in6=and_154_out[6], in7=and_154_out[7], in8=and_154_out[8], in9=and_154_out[9], in10=and_154_out[10], in11=and_154_out[11], in12=and_154_out[12], in13=and_154_out[13], in14=and_154_out[14], in15=and_154_out[15], out=open
  // AND_Gate cmp_bx_ax has open pins: in0=and_154_out[0], in1=and_154_out[1], in2=and_154_out[2], in3=and_154_out[3], in4=and_154_out[4], in5=and_154_out[5], in6=and_154_out[6], in7=and_154_out[7], in8=and_154_out[8], in9=and_154_out[9], in10=and_154_out[10], in11=and_154_out[11], in12=and_154_out[12], in13=and_154_out[13], in14=and_154_out[14], in15=and_154_out[15], out=open
  // AND_Gate cmp_bx_cx has open pins: in0=and_154_out[0], in1=and_154_out[1], in2=and_154_out[2], in3=and_154_out[3], in4=and_154_out[4], in5=and_154_out[5], in6=and_154_out[6], in7=and_154_out[7], in8=and_154_out[8], in9=and_154_out[9], in10=and_154_out[10], in11=and_154_out[11], in12=and_154_out[12], in13=and_154_out[13], in14=and_154_out[14], in15=and_154_out[15], out=open
  // AND_Gate cmp_bx_dx has open pins: in0=and_154_out[0], in1=and_154_out[1], in2=and_154_out[2], in3=and_154_out[3], in4=and_154_out[4], in5=and_154_out[5], in6=and_154_out[6], in7=and_154_out[7], in8=and_154_out[8], in9=and_154_out[9], in10=and_154_out[10], in11=and_154_out[11], in12=and_154_out[12], in13=and_154_out[13], in14=and_154_out[14], in15=and_154_out[15], out=open
  // AND_Gate cmp_cx_ax has open pins: in0=and_154_out[0], in1=and_154_out[1], in2=and_154_out[2], in3=and_154_out[3], in4=and_154_out[4], in5=and_154_out[5], in6=and_154_out[6], in7=and_154_out[7], in8=and_154_out[8], in9=and_154_out[9], in10=and_154_out[10], in11=and_154_out[11], in12=and_154_out[12], in13=and_154_out[13], in14=and_154_out[14], in15=and_154_out[15], out=open
  // AND_Gate cmp_cx_bx has open pins: in0=and_154_out[0], in1=and_154_out[1], in2=and_154_out[2], in3=and_154_out[3], in4=and_154_out[4], in5=and_154_out[5], in6=and_154_out[6], in7=and_154_out[7], in8=and_154_out[8], in9=and_154_out[9], in10=and_154_out[10], in11=and_154_out[11], in12=and_154_out[12], in13=and_154_out[13], in14=and_154_out[14], in15=and_154_out[15], out=open
  // AND_Gate cmp_cx_dx has open pins: in0=and_154_out[0], in1=and_154_out[1], in2=and_154_out[2], in3=and_154_out[3], in4=and_154_out[4], in5=and_154_out[5], in6=and_154_out[6], in7=and_154_out[7], in8=and_154_out[8], in9=and_154_out[9], in10=and_154_out[10], in11=and_154_out[11], in12=and_154_out[12], in13=and_154_out[13], in14=and_154_out[14], in15=and_154_out[15], out=open
  // AND_Gate cmp_dx_ax has open pins: in0=and_154_out[0], in1=and_154_out[1], in2=and_154_out[2], in3=and_154_out[3], in4=and_154_out[4], in5=and_154_out[5], in6=and_154_out[6], in7=and_154_out[7], in8=and_154_out[8], in9=and_154_out[9], in10=and_154_out[10], in11=and_154_out[11], in12=and_154_out[12], in13=and_154_out[13], in14=and_154_out[14], in15=and_154_out[15], out=open
  // AND_Gate cmp_dx_bx has open pins: in0=and_154_out[0], in1=and_154_out[1], in2=and_154_out[2], in3=and_154_out[3], in4=and_154_out[4], in5=and_154_out[5], in6=and_154_out[6], in7=and_154_out[7], in8=and_154_out[8], in9=and_154_out[9], in10=and_154_out[10], in11=and_154_out[11], in12=and_154_out[12], in13=and_154_out[13], in14=and_154_out[14], in15=and_154_out[15], out=open
  // AND_Gate cmp_dx_cx has open pins: in0=and_154_out[0], in1=and_154_out[1], in2=and_154_out[2], in3=and_154_out[3], in4=and_154_out[4], in5=and_154_out[5], in6=and_154_out[6], in7=and_154_out[7], in8=and_154_out[8], in9=and_154_out[9], in10=and_154_out[10], in11=and_154_out[11], in12=and_154_out[12], in13=and_154_out[13], in14=and_154_out[14], in15=and_154_out[15], out=open
  assign Math_Unit_Instruction = {d_ff_124_q[3:2], 1'b0, d_ff_124_q[0]} | or_539_out;  // OR_Gate or_566, 4 bits wide
  or or_567 (Math_Unit_Enable, or_324_out, or_568_out);
  or or_568 (or_568_out, d_ff_125_q[3], d_ff_125_q[2], or_569_out);
  or or_569 (or_569_out, d_ff_126_q[3], d_ff_126_q[2], or_570_out);
  or or_570 (or_570_out, d_ff_127_q[3], d_ff_127_q[2], or_571_out);
  or or_571 (or_571_out, d_ff_128_q[3], d_ff_128_q[2], or_572_out);
  or or_572 (or_572_out, or_330_out, or_573_out);
  or or_573 (or_573_out, d_ff_130_q[3], d_ff_130_q[2], or_574_out);
  or or_574 (or_574_out, d_ff_131_q[3], d_ff_131_q[2], or_575_out);
  or or_575 (or_575_out, d_ff_132_q[3], d_ff_132_q[2], or_576_out);
  or or_576 (or_576_out, d_ff_133_q[3], d_ff_133_q[2], or_577_out);
  or or_577 (or_577_out, or_336_out, or_578_out);
  or or_578 (or_578_out, d_ff_135_q[3], d_ff_135_q[2], or_579_out);
  or or_579 (or_579_out, d_ff_136_q[3], d_ff_136_q[2], or_580_out);
  or or_580 (or_580_out, d_ff_137_q[3], d_ff_137_q[2], or_581_out);
  or or_581 (or_581_out, d_ff_138_q[3], d_ff_138_q[2], or_582_out);
  or or_582 (or_582_out, or_342_out, or_583_out);
  or or_583 (or_583_out, d_ff_64_q[3], d_ff_64_q[2], or_584_out);
  or or_584 (or_584_out, d_ff_65_q[3], d_ff_65_q[2], or_585_out);
  or or_585 (or_585_out, d_ff_66_q[3], d_ff_66_q[2], or_586_out);
  or or_586 (or_586_out, d_ff_67_q[3], d_ff_67_q[2], or_587_out);
  or or_587 (or_587_out, d_ff_68_q[3], d_ff_68_q[2], or_588_out);
  or or_588 (or_588_out, d_ff_69_q[3], d_ff_69_q[2], or_589_out);
  or or_589 (or_589_out, d_ff_70_q[3], d_ff_70_q[2], or_590_out);
  or or_590 (or_590_out, d_ff_71_q[3], d_ff_71_q[2], or_591_out);
  or or_591 (or_591_out, d_ff_72_q[3], d_ff_72_q[2], or_592_out);
  or or_592 (or_592_out, d_ff_73_q[3], d_ff_73_q[2], or_593_out);
  or or_593 (or_593_out, d_ff_74_q[3], d_ff_74_q[2], or_594_out);
  or or_594 (or_594_out, d_ff_75_q[3], d_ff_75_q[2]);
  assign and_154_out = {16{and_26_out[4]}} & Data_In;  // AND_Gate and_154, 16 bits wide
  or or_595 (RAM0_Instruction_Enable, and_26_out[4], or_506_out);
  assign RAM0_Instruction = {3'b000, {2{and_26_out[4]}}, 3'b000} | or_507_out;  // OR_Gate or_596, 8 bits wide
endmodule

module BUS_Math_Unit (
  input  [15:0] BUS_IN,
  input  [3:0] Instruction,
  input  Enable,
  input  CLK,
  output [15:0] BUS_OUT
);

  wire and_1_out, and_2_out;
  wire [15:0] adder_1_out, register_1_q, register_2_q, subtractor_1_out;

  Register_part #(.width(16)) register_1 (.D(BUS_IN), .en(and_1_out), .Q(register_1_q), .clk(CLK));  // open: clr
  and and_1 (and_1_out, ~Instruction[0], Instruction[3], Enable);  // AND_Gate
  Register_part #(.width(16)) register_2 (.D(BUS_IN), .en(and_2_out), .Q(register_2_q), .clk(CLK));  // open: clr
  and and_2 (and_2_out, Instruction[0], Instruction[3], Enable);
  Adder #(.width(16)) adder_1 (.a(register_1_q), .b(register_2_q), .out(adder_1_out));  // open: cin, cout
  Subtractor #(.width(16)) subtractor_1 (
    .a(register_1_q), .b(register_2_q), .out(subtractor_1_out));  // open: bin, bout
  Multiplexer #(.width(16)) multiplexer_1 (
    .in0(adder_1_out), .in1(subtractor_1_out), .out(BUS_OUT), .sel(Instruction[1]), .en(Instruction[2]));
endmodule

module BUS_Comparator (
  input  [15:0] Data_In,
  input  CLK,
  input  Enable,
  input  Instruction,
  output [1:0] Comparison_Line
);

  wire and_1_out, and_2_out, Equal_out, Greater_out, Less_out, subtractor_1_bout, subtractor_2_bout;
  wire [15:0] register_1_q, register_2_q, subtractor_1_out, subtractor_2_out;

  or or_1 (Comparison_Line[0], Equal_out, Less_out);
  or or_2 (Comparison_Line[1], Equal_out, Greater_out);
  Register_part #(.width(16)) register_1 (.D(Data_In), .en(and_1_out), .Q(register_1_q), .clk(CLK));  // open: clr
  and and_1 (and_1_out, ~Instruction, Enable);  // AND_Gate
  Register_part #(.width(16)) register_2 (.D(Data_In), .en(and_2_out), .Q(register_2_q), .clk(CLK));  // open: clr
  and and_2 (and_2_out, Instruction, Enable);
  and Equal (Equal_out, ~subtractor_1_bout, ~subtractor_2_bout);  // AND_Gate
  and Greater (Greater_out, ~subtractor_1_bout, subtractor_2_bout);  // AND_Gate
  and Less (Less_out, subtractor_1_bout, subtractor_2_bout);
  Subtractor #(.width(16)) subtractor_1 (
    .a(register_1_q), .b(register_2_q), .out(subtractor_1_out), .bout(subtractor_1_bout));  // open: bin
  // Probe on subtractor_1_out
  // Probe on subtractor_2_out
  Subtractor #(.width(16)) subtractor_2 (
    .a({16{1'b0}}), .b(subtractor_1_out), .out(subtractor_2_out), .bout(subtractor_2_bout));  // open: bin
endmodule

module Command_Unit_CMP_Instruction (
  input  CLK,
  input  Enable,
  output Running_Instruction,
  output Comparison_Enable,
  output Comparison_Instruction,
  output Base_Register_Enable,
  output [2:0] Base_Register_Instruction,
  output Other_Register_Enable,
  output [2:0] Other_Register_Instruction,
  output RAM_Enable,
  output [7:0] RAM_Instruction
);

  wire d_ff_1_qn, d_ff_2_qn, d_ff_3_qn;

  D_Flip_Flop d_ff_1 (.clk(CLK), .D(Enable), .Q(Base_Register_Enable), .Qn(d_ff_1_qn));  // open: preset, en, reset
  D_Flip_Flop d_ff_2 (
    .clk(CLK), .D(Base_Register_Enable), .Q(Comparison_Instruction), .Qn(d_ff_2_qn));  // open: preset, en, reset
  D_Flip_Flop d_ff_3 (
    .clk(CLK), .D(Comparison_Instruction), .Q(RAM_Enable), .Qn(d_ff_3_qn));  // open: preset, en, reset
  and and_1 (Running_Instruction, d_ff_3_qn, d_ff_2_qn, d_ff_1_qn);
  or or_1 (Comparison_Enable, Base_Register_Enable, Comparison_Instruction);

  assign Base_Register_Instruction = {{2{Base_Register_Enable}}, 1'b0};
  assign Other_Register_Enable = Comparison_Instruction;
  assign Other_Register_Instruction = {{2{Comparison_Instruction}}, 1'b0};
  assign RAM_Instruction = {2'b00, RAM_Enable, {5{1'b0}}};
endmodule

module Command_Unit_mov_reg_value16 (
  input  CLK,
  input  Enable,
  output Instruction_Running,
  output RAM_Enable,
  output Register_Enable,
  output [7:0] RAM_Instruction,
  output [2:0] Register_Instruction
);

  wire d_ff_1_q, d_ff_1_qn, d_ff_2_qn, d_ff_3_q, d_ff_3_qn;

  D_Flip_Flop d_ff_1 (.clk(CLK), .D(Enable), .Q(d_ff_1_q), .Qn(d_ff_1_qn));  // open: preset, en, reset
  D_Flip_Flop d_ff_2 (.clk(CLK), .D(d_ff_1_q), .Q(RAM_Instruction[4]), .Qn(d_ff_2_qn));  // open: preset, en, reset
  D_Flip_Flop d_ff_3 (.clk(CLK), .D(RAM_Instruction[4]), .Q(d_ff_3_q), .Qn(d_ff_3_qn));  // open: preset, en, reset
  or or_1 (RAM_Instruction[5], d_ff_3_q, d_ff_1_q);
  and and_1 (Instruction_Running, d_ff_3_qn, d_ff_2_qn, d_ff_1_qn);
  or or_2 (RAM_Enable, d_ff_3_q, d_ff_1_q);

  assign {RAM_Instruction[7:6], RAM_Instruction[3:0]} = {2'b00, RAM_Instruction[4], 3'b000};
  assign Register_Enable = RAM_Instruction[4];
  assign Register_Instruction = 3'b000;
endmodule

module Command_Unit_mov_reg_reg (
  input  CLK,
  input  Enable,
  output Instruction_Running,
  output RAM_Enable,
  output Destination_Enable,
  output [7:0] RAM_Instruction,
  output [2:0] Destination_Instruction,
  output Source_Enable,
  output [2:0] Source_Instruction
);

  wire d_ff_1_qn, d_ff_2_qn;

  D_Flip_Flop d_ff_1 (.clk(CLK), .D(Enable), .Q(Destination_Enable), .Qn(d_ff_1_qn));  // open: preset, en, reset
  D_Flip_Flop d_ff_2 (.clk(CLK), .D(Destination_Enable), .Q(RAM_Enable), .Qn(d_ff_2_qn));  // open: preset, en, reset
  and and_1 (Instruction_Running, d_ff_2_qn, d_ff_1_qn);

  assign Destination_Instruction = 3'b000;
  assign RAM_Instruction = {2'b00, RAM_Enable, {5{1'b0}}};
  assign Source_Enable = Destination_Enable;
  assign Source_Instruction = {{2{Destination_Enable}}, 1'b0};
endmodule

module Command_Unit_mov_reg__reg (
  input  CLK,
  input  Enable,
  output Instruction_Running,
  output RAM_Enable,
  output Destination_Enable,
  output [7:0] RAM_Instruction,
  output [2:0] Destination_Instruction,
  output Source_Enable,
  output [2:0] Source_Instruction
);

  wire d_ff_1_qn, d_ff_2_qn, d_ff_3_qn;

  D_Flip_Flop d_ff_1 (.clk(CLK), .D(Enable), .Q(RAM_Instruction[6]), .Qn(d_ff_1_qn));  // open: preset, en, reset
  D_Flip_Flop d_ff_2 (
    .clk(CLK), .D(RAM_Instruction[6]), .Q(Destination_Enable), .Qn(d_ff_2_qn));  // open: preset, en, reset
  D_Flip_Flop d_ff_3 (
    .clk(CLK), .D(Destination_Enable), .Q(RAM_Instruction[5]), .Qn(d_ff_3_qn));  // open: preset, en, reset
  and and_1 (Instruction_Running, d_ff_3_qn, d_ff_2_qn, d_ff_1_qn);
  or or_1 (RAM_Enable, RAM_Instruction[5], Destination_Enable, RAM_Instruction[6]);

  assign Destination_Instruction = 3'b000;
  assign {RAM_Instruction[7], RAM_Instruction[4:0]} = {{3{Destination_Enable}}, 3'b000};
  assign Source_Enable = RAM_Instruction[6];
  assign Source_Instruction = {{2{RAM_Instruction[6]}}, 1'b0};
endmodule

module Command_Unit_mov__reg__reg (
  input  CLK,
  input  Enable,
  output Instruction_Running,
  output RAM_Enable,
  output Destination_Enable,
  output [7:0] RAM_Instruction,
  output [2:0] Destination_Instruction,
  output Source_Enable,
  output [2:0] Source_Instruction
);

  wire d_ff_1_qn, d_ff_2_qn, d_ff_3_qn;

  D_Flip_Flop d_ff_1 (.clk(CLK), .D(Enable), .Q(Destination_Enable), .Qn(d_ff_1_qn));  // open: preset, en, reset
  D_Flip_Flop d_ff_2 (
    .clk(CLK), .D(Destination_Enable), .Q(RAM_Instruction[7]), .Qn(d_ff_2_qn));  // open: preset, en, reset
  D_Flip_Flop d_ff_3 (
    .clk(CLK), .D(RAM_Instruction[7]), .Q(RAM_Instruction[5]), .Qn(d_ff_3_qn));  // open: preset, en, reset
  and and_1 (Instruction_Running, d_ff_3_qn, d_ff_2_qn, d_ff_1_qn);
  or or_1 (RAM_Enable, RAM_Instruction[5], RAM_Instruction[7], Destination_Enable);

  assign Destination_Instruction = {{2{Destination_Enable}}, 1'b0};
  assign {RAM_Instruction[6], RAM_Instruction[4:0]} = {Destination_Enable, 2'b00, RAM_Instruction[7], 2'b00};
  assign Source_Enable = RAM_Instruction[7];
  assign Source_Instruction = {{2{RAM_Instruction[7]}}, 1'b0};
endmodule

module Command_Unit_add_reg_reg (
  input  CLK,
  input  Enable,
  output Instruction_Running,
  output RAM_Enable,
  output Destination_Enable,
  output [7:0] RAM_Instruction,
  output [2:0] Destination_Instruction,
  output Source_Enable,
  output [2:0] Source_Instruction,
  output Math_Enable,
  output [3:0] Math_Instruction
);

  wire d_ff_1_qn, d_ff_2_qn, d_ff_3_qn, d_ff_4_qn;

  D_Flip_Flop d_ff_1 (
    .clk(CLK), .D(Enable), .Q(Destination_Instruction[2]), .Qn(d_ff_1_qn));  // open: preset, en, reset
  or or_1 (Destination_Enable, Math_Instruction[2], Destination_Instruction[2]);
  D_Flip_Flop d_ff_2 (
    .clk(CLK), .D(Destination_Instruction[2]), .Q(Math_Instruction[0]), .Qn(d_ff_2_qn));  // open: preset, en, reset
  D_Flip_Flop d_ff_3 (
    .clk(CLK), .D(Math_Instruction[0]), .Q(Math_Instruction[2]), .Qn(d_ff_3_qn));  // open: preset, en, reset
  D_Flip_Flop d_ff_4 (.clk(CLK), .D(Math_Instruction[2]), .Q(RAM_Enable), .Qn(d_ff_4_qn));  // open: preset, en, reset
  or or_2 (Math_Instruction[3], Math_Instruction[0], Destination_Instruction[2]);
  and and_1 (Instruction_Running, d_ff_4_qn, d_ff_3_qn, d_ff_2_qn, d_ff_1_qn);
  or or_3 (Math_Enable, Destination_Instruction[2], Math_Instruction[0], Math_Instruction[2]);

  assign Destination_Instruction[1:0] = {Destination_Instruction[2], 1'b0};
  assign Math_Instruction[1] = 1'b0;
  assign RAM_Instruction = {2'b00, RAM_Enable, {5{1'b0}}};
  assign Source_Enable = Math_Instruction[0];
  assign Source_Instruction = {{2{Math_Instruction[0]}}, 1'b0};
endmodule

module Command_Unit_sub_reg_reg (
  input  CLK,
  input  Enable,
  output Instruction_Running,
  output RAM_Enable,
  output Destination_Enable,
  output [7:0] RAM_Instruction,
  output [2:0] Destination_Instruction,
  output Source_Enable,
  output [2:0] Source_Instruction,
  output Math_Enable,
  output [3:0] Math_Instruction
);

  wire d_ff_1_qn, d_ff_2_qn, d_ff_3_qn, d_ff_4_qn;

  D_Flip_Flop d_ff_1 (
    .clk(CLK), .D(Enable), .Q(Destination_Instruction[2]), .Qn(d_ff_1_qn));  // open: preset, en, reset
  or or_1 (Destination_Enable, Math_Instruction[2], Destination_Instruction[2]);
  D_Flip_Flop d_ff_2 (
    .clk(CLK), .D(Destination_Instruction[2]), .Q(Math_Instruction[0]), .Qn(d_ff_2_qn));  // open: preset, en, reset
  D_Flip_Flop d_ff_3 (
    .clk(CLK), .D(Math_Instruction[0]), .Q(Math_Instruction[2]), .Qn(d_ff_3_qn));  // open: preset, en, reset
  D_Flip_Flop d_ff_4 (.clk(CLK), .D(Math_Instruction[2]), .Q(RAM_Enable), .Qn(d_ff_4_qn));  // open: preset, en, reset
  or or_2 (Math_Instruction[3], Math_Instruction[0], Destination_Instruction[2]);
  and and_1 (Instruction_Running, d_ff_4_qn, d_ff_3_qn, d_ff_2_qn, d_ff_1_qn);
  or or_3 (Math_Enable, Destination_Instruction[2], Math_Instruction[0], Math_Instruction[2]);

  assign Destination_Instruction[1:0] = {Destination_Instruction[2], 1'b0};
  assign Math_Instruction[1] = Math_Instruction[2];
  assign RAM_Instruction = {2'b00, RAM_Enable, {5{1'b0}}};
  assign Source_Enable = Math_Instruction[0];
  assign Source_Instruction = {{2{Math_Instruction[0]}}, 1'b0};
endmodule

module Command_Unit_cmp_reg_reg (
  input  CLK,
  input  Enable,
  output Instruction_Running,
  output RAM_Enable,
  output Destination_Enable,
  output [7:0] RAM_Instruction,
  output [2:0] Destination_Instruction,
  output Source_Enable,
  output [2:0] Source_Instruction,
  output Compare_Enable,
  output Compare_Instruction
);

  wire d_ff_1_qn, d_ff_2_qn, d_ff_3_qn;

  D_Flip_Flop d_ff_1 (.clk(CLK), .D(Enable), .Q(Destination_Enable), .Qn(d_ff_1_qn));  // open: preset, en, reset
  D_Flip_Flop d_ff_2 (
    .clk(CLK), .D(Destination_Enable), .Q(Compare_Instruction), .Qn(d_ff_2_qn));  // open: preset, en, reset
  D_Flip_Flop d_ff_3 (.clk(CLK), .D(Compare_Instruction), .Q(RAM_Enable), .Qn(d_ff_3_qn));  // open: preset, en, reset
  and and_1 (Instruction_Running, d_ff_3_qn, d_ff_2_qn, d_ff_1_qn);
  or or_1 (Compare_Enable, Compare_Instruction, Destination_Enable);

  assign Destination_Instruction = {{2{Destination_Enable}}, 1'b0};
  assign RAM_Instruction = {2'b00, RAM_Enable, {5{1'b0}}};
  assign Source_Enable = Compare_Instruction;
  assign Source_Instruction = {{2{Compare_Instruction}}, 1'b0};
endmodule

module BUS_Command_Unit_V4 (
  input  CLK,
  input  [15:0] Data_In,
  output ax_enable_instruction,
  output [2:0] ax_instruction,
  output bx_enable_instruction,
  output [2:0] bx_instruction,
  output cx_enable_instruction,
  output [2:0] cx_instruction,
  output RAM0_Instruction_Enable,
  output [7:0] RAM0_Instruction,
  output dx_enable_instruction,
  output [2:0] dx_instruction
);

  wire and_1_out, and_2_out, and_3_out, command_unit_mov_reg_value16_1_instruction_running,
       command_unit_mov_reg_value16_1_ram_enable, command_unit_mov_reg_value16_1_register_enable,
       command_unit_mov_reg_value16_2_instruction_running, command_unit_mov_reg_value16_2_ram_enable,
       command_unit_mov_reg_value16_2_register_enable, command_unit_mov_reg_value16_3_instruction_running,
       command_unit_mov_reg_value16_3_ram_enable, command_unit_mov_reg_value16_3_register_enable,
       command_unit_mov_reg_value16_4_instruction_running, command_unit_mov_reg_value16_4_ram_enable,
       command_unit_mov_reg_value16_4_register_enable, mov_ax_value16_out, mov_bx_value16_out,
       mov_cx_value16_out, mov_dx_value16_out, or_2_out, or_13_out, or_15_out, or_16_out, or_17_out,
       or_19_out, or_21_out, or_23_out, undriven, undriven_2;
  wire [2:0] command_unit_mov_reg_value16_1_register_instruction,
       command_unit_mov_reg_value16_2_register_instruction,
       command_unit_mov_reg_value16_3_register_instruction,
       command_unit_mov_reg_value16_4_register_instruction, or_1_out, or_3_out, or_12_out, or_14_out;
  wire [7:0] command_unit_mov_reg_value16_1_ram_instruction, command_unit_mov_reg_value16_2_ram_instruction,
       command_unit_mov_reg_value16_3_ram_instruction, command_unit_mov_reg_value16_4_ram_instruction,
       or_18_out, or_20_out, or_22_out, or_24_out, undriven_3;
  wire [15:0] and_5_out;
  wire [15:15] and_4_out;

  // OR_Gate or_1 has open pins: out=or_1_out
  // OR_Gate or_2 has open pins: out=or_2_out
  // OR_Gate or_3 has open pins: out=or_3_out
  or or_4 (ax_enable_instruction, command_unit_mov_reg_value16_4_register_enable, or_16_out);
  assign ax_instruction = command_unit_mov_reg_value16_4_register_instruction | or_14_out;  // OR_Gate or_5, 3 bits wide
  or or_6 (bx_enable_instruction, command_unit_mov_reg_value16_1_register_enable, or_15_out);
  assign bx_instruction = command_unit_mov_reg_value16_1_register_instruction | or_12_out;  // OR_Gate or_7, 3 bits wide
  or or_8 (cx_enable_instruction, command_unit_mov_reg_value16_2_register_enable, or_13_out);
  assign cx_instruction = command_unit_mov_reg_value16_2_register_instruction | or_3_out;  // OR_Gate or_9, 3 bits wide
  or or_10 (dx_enable_instruction, command_unit_mov_reg_value16_3_register_enable, or_2_out);
  assign dx_instruction = command_unit_mov_reg_value16_3_register_instruction | or_1_out;  // OR_Gate or_11, 3 bits wide
  // OR_Gate or_12 has open pins: out=or_12_out
  // OR_Gate or_13 has open pins: out=or_13_out
  // OR_Gate or_14 has open pins: out=or_14_out
  // OR_Gate or_15 has open pins: out=or_15_out
  // OR_Gate or_16 has open pins: out=or_16_out
  Command_Unit_mov_reg_value16 command_unit_mov_reg_value16_1 (
    .CLK(CLK), .Enable(mov_bx_value16_out), .Register_Enable(command_unit_mov_reg_value16_1_register_enable),
    .Register_Instruction(command_unit_mov_reg_value16_1_register_instruction),
    .Instruction_Running(command_unit_mov_reg_value16_1_instruction_running),
    .RAM_Enable(command_unit_mov_reg_value16_1_ram_enable),
    .RAM_Instruction(command_unit_mov_reg_value16_1_ram_instruction));
  Command_Unit_mov_reg_value16 command_unit_mov_reg_value16_2 (
    .CLK(CLK), .Enable(mov_cx_value16_out), .Register_Enable(command_unit_mov_reg_value16_2_register_enable),
    .Register_Instruction(command_unit_mov_reg_value16_2_register_instruction),
    .Instruction_Running(command_unit_mov_reg_value16_2_instruction_running),
    .RAM_Enable(command_unit_mov_reg_value16_2_ram_enable),
    .RAM_Instruction(command_unit_mov_reg_value16_2_ram_instruction));
  Command_Unit_mov_reg_value16 command_unit_mov_reg_value16_3 (
    .CLK(CLK), .Enable(mov_dx_value16_out), .Register_Enable(command_unit_mov_reg_value16_3_register_enable),
    .Register_Instruction(command_unit_mov_reg_value16_3_register_instruction),
    .Instruction_Running(command_unit_mov_reg_value16_3_instruction_running),
    .RAM_Enable(command_unit_mov_reg_value16_3_ram_enable),
    .RAM_Instruction(command_unit_mov_reg_value16_3_ram_instruction));
  Command_Unit_mov_reg_value16 command_unit_mov_reg_value16_4 (
    .CLK(CLK), .Enable(mov_ax_value16_out), .Register_Enable(command_unit_mov_reg_value16_4_register_enable),
    .Register_Instruction(command_unit_mov_reg_value16_4_register_instruction),
    .Instruction_Running(command_unit_mov_reg_value16_4_instruction_running),
    .RAM_Enable(command_unit_mov_reg_value16_4_ram_enable),
    .RAM_Instruction(command_unit_mov_reg_value16_4_ram_instruction));
  and and_1 (and_1_out, command_unit_mov_reg_value16_1_instruction_running, and_2_out);
  and and_2 (and_2_out, command_unit_mov_reg_value16_2_instruction_running, and_3_out);
  and and_3 (and_3_out, command_unit_mov_reg_value16_3_instruction_running, undriven);
  and and_4 (and_4_out[15], command_unit_mov_reg_value16_4_instruction_running, and_1_out);
  and mov_ax_value16 (mov_ax_value16_out, and_5_out[0], ~and_5_out[1], ~and_5_out[2], ~and_5_out[3], ~and_5_out[4], ~and_5_out[5], ~and_5_out[6], ~and_5_out[7], ~and_5_out[8], ~and_5_out[9], ~and_5_out[10], ~and_5_out[11], ~and_5_out[12], ~and_5_out[13], ~and_5_out[14], ~and_5_out[15]);  // AND_Gate
  and mov_bx_value16 (mov_bx_value16_out, ~and_5_out[0], and_5_out[1], ~and_5_out[2], ~and_5_out[3], ~and_5_out[4], ~and_5_out[5], ~and_5_out[6], ~and_5_out[7], ~and_5_out[8], ~and_5_out[9], ~and_5_out[10], ~and_5_out[11], ~and_5_out[12], ~and_5_out[13], ~and_5_out[14], ~and_5_out[15]);  // AND_Gate
  or or_17 (or_17_out, command_unit_mov_reg_value16_1_ram_enable, or_19_out);
  assign or_18_out = command_unit_mov_reg_value16_1_ram_instruction | or_20_out;  // OR_Gate or_18, 8 bits wide
  and mov_cx_value16 (mov_cx_value16_out, and_5_out[0], and_5_out[1], ~and_5_out[2], ~and_5_out[3], ~and_5_out[4], ~and_5_out[5], ~and_5_out[6], ~and_5_out[7], ~and_5_out[8], ~and_5_out[9], ~and_5_out[10], ~and_5_out[11], ~and_5_out[12], ~and_5_out[13], ~and_5_out[14], ~and_5_out[15]);  // AND_Gate
  or or_19 (or_19_out, command_unit_mov_reg_value16_2_ram_enable, or_21_out);
  assign or_20_out = command_unit_mov_reg_value16_2_ram_instruction | or_22_out;  // OR_Gate or_20, 8 bits wide
  and mov_dx_value16 (mov_dx_value16_out, ~and_5_out[0], ~and_5_out[1], and_5_out[2], ~and_5_out[3], ~and_5_out[4], ~and_5_out[5], ~and_5_out[6], ~and_5_out[7], ~and_5_out[8], ~and_5_out[9], ~and_5_out[10], ~and_5_out[11], ~and_5_out[12], ~and_5_out[13], ~and_5_out[14], ~and_5_out[15]);  // AND_Gate
  or or_21 (or_21_out, command_unit_mov_reg_value16_3_ram_enable, undriven_2);
  assign or_22_out = command_unit_mov_reg_value16_3_ram_instruction | undriven_3;  // OR_Gate or_22, 8 bits wide
  or or_23 (or_23_out, command_unit_mov_reg_value16_4_ram_enable, or_17_out);
  assign or_24_out = command_unit_mov_reg_value16_4_ram_instruction | or_18_out;  // OR_Gate or_24, 8 bits wide
  assign and_5_out = {16{and_4_out[15]}} & Data_In;  // AND_Gate and_5, 16 bits wide
  or or_25 (RAM0_Instruction_Enable, and_4_out[15], or_23_out);
  assign RAM0_Instruction = {3'b000, {2{and_4_out[15]}}, 3'b000} | or_24_out;  // OR_Gate or_26, 8 bits wide
endmodule
